// Logisim project Abacus2_OldDesign.circ as structural Verilog
module circClk (
  input  clkMode,
  input  clkPulse,
  input  clkHlt,
  output clkClk,
  output clkInv
);

  wire and_1_out, and_2_out, clkAuto_out, or_1_out;

  Clock clkAuto (.out(clkAuto_out));
  and and_1 (and_1_out, clkAuto_out, clkMode);
  and and_2 (and_2_out, ~clkMode, clkPulse);  // AND_Gate
  or or_1 (or_1_out, and_1_out, and_2_out);
  and and_3 (clkClk, or_1_out, ~clkHlt);  // AND_Gate
  not not_1 (clkInv, clkClk);
endmodule

module circPC (
  input  pcRst,
  input  pcLoad,
  input  pcCE,
  input  pcClk,
  input  [7:0] pcIn,
  input  pcOE,
  input  [10:0] pcSeg,
  output pcTC,
  output [18:0] pcOut
);

  wire [18:0] counter_1_q;

  Counter #(.width(19), .max('h7ffff)) counter_1 (
    .clr(pcRst), .load(pcLoad), .up(1'b1), .count(pcCE), .clk(pcClk), .D({pcSeg, pcIn}), .carry(pcTC),
    .Q(counter_1_q));
  assign pcOut = pcOE ? counter_1_q : 19'bz;  // Controlled_Buffer controlled_buffer_1
endmodule

module circRegs (
  input  [7:0] regsIn,
  input  regsHold,
  input  regsClk,
  input  [7:0] regsOut,
  input  regsRst,
  input  regsWE,
  input  regsOE
);

  wire [2:0] regsHolder_q;

  Register #(.width(3)) regsHolder (.D(regsIn[2:0]), .en(regsHold), .clk(regsClk), .Q(regsHolder_q), .clr(regsRst));
  subRegs subregs_1 (
    .regsClk(regsClk), .regsRst(regsRst), .regsSelLH(regsHolder_q[0]), .regsSelPair(regsHolder_q[2:1]),
    .regsIn(regsIn), .regsWE(regsWE), .regsOE(regsOE), .regsOut(regsOut));
endmodule

module subRegs (
  input  regsClk,
  input  regsRst,
  input  regsSelLH,
  input  [1:0] regsSelPair,
  input  [7:0] regsIn,
  input  regsWE,
  input  regsOE,
  output [7:0] regsOut
);

  wire demultiplexer_1_out0, demultiplexer_1_out1, demultiplexer_1_out2, demultiplexer_1_out3,
       demultiplexer_2_out0, demultiplexer_2_out1, demultiplexer_2_out2, demultiplexer_2_out3;

  Demultiplexer #(.select(2), .enable("false")) demultiplexer_1 (
    .out0(demultiplexer_1_out0), .out1(demultiplexer_1_out1), .out2(demultiplexer_1_out2),
    .out3(demultiplexer_1_out3), .in(regsWE), .sel(regsSelPair));
  Demultiplexer #(.select(2), .enable("false")) demultiplexer_2 (
    .out0(demultiplexer_2_out0), .out1(demultiplexer_2_out1), .out2(demultiplexer_2_out2),
    .out3(demultiplexer_2_out3), .in(regsOE), .sel(regsSelPair));
  subReg regsA (
    .regIn(regsIn), .regWE(demultiplexer_1_out0), .regOE(demultiplexer_2_out0), .regClk(regsClk),
    .regSel(regsSelLH), .regRst(regsRst), .regOut(regsOut));
  subReg regsB (
    .regIn(regsIn), .regWE(demultiplexer_1_out1), .regOE(demultiplexer_2_out1), .regClk(regsClk),
    .regSel(regsSelLH), .regRst(regsRst), .regOut(regsOut));
  subReg regsC (
    .regIn(regsIn), .regWE(demultiplexer_1_out2), .regOE(demultiplexer_2_out2), .regClk(regsClk),
    .regSel(regsSelLH), .regRst(regsRst), .regOut(regsOut));
  subReg regsD (
    .regIn(regsIn), .regWE(demultiplexer_1_out3), .regOE(demultiplexer_2_out3), .regClk(regsClk),
    .regSel(regsSelLH), .regRst(regsRst), .regOut(regsOut));
endmodule

module subReg (
  input  [7:0] regIn,
  input  regWE,
  input  regOE,
  input  regClk,
  input  regSel,
  input  regRst,
  output [7:0] regOut
);

  wire demultiplexer_1_out0, demultiplexer_1_out1;
  wire [7:0] regHigh_q, regLow_q;

  Demultiplexer #(.enable("false")) demultiplexer_1 (
    .out0(demultiplexer_1_out0), .out1(demultiplexer_1_out1), .in(regWE), .sel(regSel));
  Register regLow (.D(regIn), .en(demultiplexer_1_out0), .clk(regClk), .Q(regLow_q), .clr(regRst));
  Register regHigh (.D(regIn), .en(demultiplexer_1_out1), .clk(regClk), .Q(regHigh_q), .clr(regRst));
  Multiplexer #(.width(8)) multiplexer_1 (.in0(regLow_q), .in1(regHigh_q), .out(regOut), .sel(regSel), .en(regOE));
endmodule

module circALU (
  input  [7:0] aluInAcc,
  input  [7:0] aluInTwo,
  input  aluInCF,
  input  [3:0] aluSel,
  input  aluOE,
  output [7:0] AluOut,
  output aluPF,
  output aluCF,
  output aluZF,
  output aluSF,
  output aluOF
);

  wire comparator_1_eq;
  wire [3:0] bitadder_1_out;
  wire [7:0] subalu_1_aluadd, subalu_1_aluand, subalu_1_alunot, subalu_1_aluor, subalu_1_alurol,
       subalu_1_alushl, subalu_1_alusub, subalu_1_aluxor;

  subALU subalu_1 (
    .aluAnd(subalu_1_aluand), .aluAdd(subalu_1_aluadd), .aluShl(subalu_1_alushl), .aluInCF(aluInCF),
    .aluInAcc(aluInAcc), .aluInTwo(aluInTwo), .aluSel(aluSel), .aluRol(subalu_1_alurol),
    .aluNot(subalu_1_alunot), .aluOr(subalu_1_aluor), .aluSub(subalu_1_alusub), .aluXor(subalu_1_aluxor),
    .aluCF(aluCF));
  Multiplexer #(.select(4), .width(8)) multiplexer_1 (
    .in0(subalu_1_aluadd), .in1(subalu_1_aluadd), .in2(subalu_1_aluadd), .in3(subalu_1_alusub),
    .in4(subalu_1_alusub), .in5(subalu_1_alusub), .in6(subalu_1_alushl), .in7(subalu_1_alurol),
    .in8(subalu_1_alunot), .in9(subalu_1_aluand), .in10(subalu_1_aluor), .in11(subalu_1_aluxor),
    .in12({8{1'b0}}), .in13({8{1'b0}}), .in14({8{1'b0}}), .in15({8{1'b0}}), .out(AluOut), .sel(aluSel),
    .en(aluOE));
  BitAdder bitadder_1 (.in0(AluOut), .out(bitadder_1_out));
  BitFinder #(.\type ("low0")) bitfinder_1 (.in(AluOut), .found(aluZF));  // open: index
  Comparator #(.width(1), .mode("unsigned")) comparator_1 (
    .a(AluOut[7]), .b(aluInAcc[7]), .eq(comparator_1_eq));  // open: gt, lt
  not not_1 (aluPF, bitadder_1_out[0]);
  not not_2 (aluOF, comparator_1_eq);

  assign aluSF = AluOut[7];
endmodule

module subALU (
  input  [7:0] aluInAcc,
  input  [7:0] aluInTwo,
  input  aluInCF,
  input  [3:0] aluSel,
  output [7:0] aluShl,
  output [7:0] aluRol,
  output [7:0] aluAdd,
  output [7:0] aluNot,
  output [7:0] aluAnd,
  output [7:0] aluOr,
  output [7:0] aluSub,
  output [7:0] aluXor,
  output aluCF
);

  wire adder_1_cout, aluCryEn, aluTwoEn, and_1_out, and_2_out, subtractor_1_bout;
  wire [7:0] multiplexer_1_out, multiplexer_2_out;

  ROM #(.addrWidth(3), .dataWidth(2)) ALUSelROM (.addr(aluSel[2:0]), .data({aluTwoEn, aluCryEn}));
  and and_1 (and_1_out, aluInCF, aluCryEn);
  Adder adder_1 (.a(aluInAcc), .b(multiplexer_1_out), .out(aluAdd), .cin(and_1_out), .cout(adder_1_cout));
  Multiplexer #(.width(8), .enable("false")) multiplexer_1 (
    .in0(aluInTwo), .in1({8{1'b0}}), .out(multiplexer_1_out), .sel(aluTwoEn));
  and and_2 (and_2_out, aluInCF, aluCryEn);
  Subtractor subtractor_1 (
    .a(aluInAcc), .b(multiplexer_2_out), .out(aluSub), .bin(and_2_out), .bout(subtractor_1_bout));
  Multiplexer #(.width(8), .enable("false")) multiplexer_2 (
    .in0(aluInTwo), .in1({8{1'b0}}), .out(multiplexer_2_out), .sel(aluTwoEn));
  or or_1 (aluCF, subtractor_1_bout, adder_1_cout);
  Shifter shifter_1 (.in(aluInAcc), .\dist (3'b001), .out(aluShl));
  Shifter #(.shift("rl")) shifter_2 (.in(aluInAcc), .\dist (3'b001), .out(aluRol));
  Negator negator_1 (.in(aluInAcc), .out(aluNot));
  assign aluAnd = aluInAcc & aluInTwo;  // AND_Gate and_3, 8 bits wide
  assign aluOr = aluInAcc | aluInTwo;  // OR_Gate or_2, 8 bits wide
  assign aluXor = aluInAcc ^ aluInTwo;  // XOR_Gate xor_1, 8 bits wide

  // Notes on the sheet:
  //   contents of ALUSelROM (hex, n*v repeats v):
  //   3 1 0 3 1 0 1
endmodule

module circFlags (
  input  flagsInCF,
  input  flagsWE,
  input  flagsInPF,
  input  flagsClk,
  input  flagsInZF,
  input  flagsInSF,
  input  flagsInOF,
  input  flagsTglIF,
  input  flagsTglDF,
  input  flagsRst,
  output flagsCF,
  output flagsPF,
  output flagsZF,
  output flagsSF,
  output flagsOF,
  output flagsIF,
  output flagsDF
);

  Register #(.width(5)) register_1 (
    .D({flagsInOF, flagsInSF, flagsInZF, flagsInPF, flagsInCF}), .en(flagsWE), .clk(flagsClk),
    .Q({flagsOF, flagsSF, flagsZF, flagsPF, flagsCF}), .clr(flagsRst));
  T_Flip_Flop t_ff_1 (.T(flagsTglIF), .clk(flagsClk), .Q(flagsIF), .reset(flagsRst));  // open: Qn, preset
  T_Flip_Flop t_ff_2 (.T(flagsTglDF), .clk(flagsClk), .Q(flagsDF), .reset(flagsRst));  // open: Qn, preset
endmodule

module circStack (
  input  stackRst,
  input  stackDown,
  input  stackCE,
  input  stackClk,
  input  stackWE,
  input  stackOE,
  input  [7:0] stackIn,
  output stackTC,
  output [7:0] stackOut
);

  wire not_1_out;
  wire [11:0] stackCounter_q;

  Counter #(.width(12), .max('hfff)) stackCounter (
    .clr(stackRst), .load(1'b0), .up(not_1_out), .count(stackCE), .clk(stackClk), .carry(stackTC),
    .Q(stackCounter_q));  // open: D
  not not_1 (not_1_out, stackDown);
  RAM #(.addrWidth(12), .databus("bibus")) stackMemory (
    .addr(stackCounter_q), .we(stackWE), .oe(stackOE), .clk(stackClk), .din(stackIn), .dout(stackOut));
endmodule

module circOut (
  input  [7:0] outIn,
  input  outWE,
  input  outClk,
  input  outLoad,
  input  outCE,
  input  outRst,
  output [31:0] outOut
);

  wire demultiplexer_1_out0, demultiplexer_1_out1, demultiplexer_1_out2, demultiplexer_1_out3;
  wire [1:0] outCounter_q;

  Counter #(.width(2), .max('h3)) outCounter (
    .clr(outRst), .load(outLoad), .up(1'b1), .count(outCE), .clk(outClk), .D(outIn[1:0]), .Q(outCounter_q));  // open: carry
  Demultiplexer #(.select(2), .enable("false")) demultiplexer_1 (
    .out0(demultiplexer_1_out0), .out1(demultiplexer_1_out1), .out2(demultiplexer_1_out2),
    .out3(demultiplexer_1_out3), .in(outWE), .sel(outCounter_q));
  Register out0 (.D(outIn), .en(demultiplexer_1_out0), .clk(outClk), .Q(outOut[7:0]), .clr(outRst));
  Register out1 (.D(outIn), .en(demultiplexer_1_out1), .clk(outClk), .Q(outOut[15:8]), .clr(outRst));
  Register out2 (.D(outIn), .en(demultiplexer_1_out2), .clk(outClk), .Q(outOut[23:16]), .clr(outRst));
  Register out3 (.D(outIn), .en(demultiplexer_1_out3), .clk(outClk), .Q(outOut[31:24]), .clr(outRst));
endmodule

module circDsp (
  input  [7:0] dspIn,
  input  dspWE,
  input  dspRst,
  input  dspLoad,
  input  dspCE,
  input  dspClk,
  output [7:0] out_7,
  output [7:0] out_8,
  output [7:0] out_9,
  output [7:0] out_10,
  output [7:0] out_11,
  output [7:0] out_12,
  output [7:0] out_13,
  output [7:0] out_14,
  output [7:0] out_15,
  output [7:0] out_16,
  output [7:0] out_17,
  output [7:0] out_18,
  output [7:0] out_19,
  output [7:0] out_20,
  output [7:0] out_21,
  output [7:0] out_22,
  output [7:0] out_23,
  output [7:0] out_24,
  output [7:0] out_25,
  output [7:0] out_26,
  output [7:0] out_27,
  output [7:0] out_28,
  output [7:0] out_29,
  output [7:0] out_30,
  output [7:0] out_31,
  output [7:0] out_32,
  output [7:0] out_33,
  output [7:0] out_34,
  output [7:0] out_35,
  output [7:0] out_36,
  output [7:0] out_37,
  output [7:0] out_38,
  output [7:0] out_39,
  output [7:0] out_40,
  output [7:0] out_41,
  output [7:0] out_42,
  output [7:0] out_43,
  output [7:0] out_44,
  output [7:0] out_45,
  output [7:0] out_46,
  output [7:0] out_47,
  output [7:0] out_48,
  output [7:0] out_49,
  output [7:0] out_50,
  output [7:0] out_51,
  output [7:0] out_52,
  output [7:0] out_53,
  output [7:0] out_54,
  output [7:0] out_55,
  output [7:0] out_56,
  output [7:0] out_57,
  output [7:0] out_58,
  output [7:0] out_59,
  output [7:0] out_60,
  output [7:0] out_61,
  output [7:0] out_62,
  output [7:0] out_63,
  output [7:0] out_64,
  output [7:0] out_65,
  output [7:0] out_66,
  output [7:0] out_67,
  output [7:0] out_68,
  output [7:0] out_69,
  output [7:0] out_70
);

  wire [5:0] dspCounter_q;

  Counter #(.width(6), .max('h3f)) dspCounter (
    .clr(dspRst), .load(dspLoad), .up(1'b1), .count(dspCE), .clk(dspClk), .D(dspIn[5:0]), .Q(dspCounter_q));  // open: carry
  subDspRAM64 subdspram64_1 (
    .dspRAM64In(dspIn), .dspRAM64Sel(dspCounter_q), .dspRAM64WE(dspWE), .dspRAM64Clk(dspClk),
    .dspRAM64Rst(dspRst), .dspRAM64Out0(out_7), .dspRAM64Out1(out_8), .dspRAM64Out2(out_9),
    .dspRAM64Out3(out_10), .dspRAM64Out4(out_11), .dspRAM64Out5(out_12), .dspRAM64Out6(out_13),
    .dspRAM64Out7(out_14), .dspRAM64Out8(out_15), .dspRAM64Out9(out_16), .dspRAM64Out10(out_17),
    .dspRAM64Out11(out_18), .dspRAM64Out12(out_19), .dspRAM64Out13(out_20), .dspRAM64Out14(out_21),
    .dspRAM64Out15(out_22), .dspRAM64Out16(out_23), .dspRAM64Out17(out_24), .dspRAM64Out18(out_25),
    .dspRAM64Out19(out_26), .dspRAM64Out20(out_27), .dspRAM64Out21(out_28), .dspRAM64Out22(out_29),
    .dspRAM64Out23(out_30), .dspRAM64Out24(out_31), .dspRAM64Out25(out_32), .dspRAM64Out26(out_33),
    .dspRAM64Out27(out_34), .dspRAM64Out28(out_35), .dspRAM64Out29(out_36), .dspRAM64Out30(out_37),
    .dspRAM64Out31(out_38), .dspRAM64Out32(out_39), .dspRAM64Out33(out_40), .dspRAM64Out34(out_41),
    .dspRAM64Out35(out_42), .dspRAM64Out36(out_43), .dspRAM64Out37(out_44), .dspRAM64Out38(out_45),
    .dspRAM64Out39(out_46), .dspRAM64Out40(out_47), .dspRAM64Out41(out_48), .dspRAM64Out42(out_49),
    .dspRAM64Out43(out_50), .dspRAM64Out44(out_51), .dspRAM64Out45(out_52), .dspRAM64Out46(out_53),
    .dspRAM64Out47(out_54), .dspRAM64Out48(out_55), .dspRAM64Out49(out_56), .dspRAM64Out50(out_57),
    .dspRAM64Out51(out_58), .dspRAM64Out52(out_59), .dspRAM64Out53(out_60), .dspRAM64Out54(out_61),
    .dspRAM64Out55(out_62), .dspRAM64Out56(out_63), .dspRAM64Out57(out_64), .dspRAM64Out58(out_65),
    .dspRAM64Out59(out_66), .dspRAM64Out60(out_67), .dspRAM64Out61(out_68), .dspRAM64Out62(out_69),
    .dspRAM64Out63(out_70));
endmodule

module subDspRAM8 (
  input  [7:0] dspRAM8In,
  input  dspRAM8WE,
  input  [2:0] dspRAM8Sel,
  input  dspRAM8Clk,
  input  dspRAM8Rst,
  output [7:0] dspRAM8Out0,
  output [7:0] dspRAM8Out1,
  output [7:0] dspRAM8Out2,
  output [7:0] dspRAM8Out3,
  output [7:0] dspRAM8Out4,
  output [7:0] dspRAM8Out5,
  output [7:0] dspRAM8Out6,
  output [7:0] dspRAM8Out7
);

  wire demultiplexer_1_out0, demultiplexer_1_out1, demultiplexer_1_out2, demultiplexer_1_out3,
       demultiplexer_1_out4, demultiplexer_1_out5, demultiplexer_1_out6, demultiplexer_1_out7;

  Demultiplexer #(.select(3), .enable("false")) demultiplexer_1 (
    .out0(demultiplexer_1_out0), .out1(demultiplexer_1_out1), .out2(demultiplexer_1_out2),
    .out3(demultiplexer_1_out3), .out4(demultiplexer_1_out4), .out5(demultiplexer_1_out5),
    .out6(demultiplexer_1_out6), .out7(demultiplexer_1_out7), .in(dspRAM8WE), .sel(dspRAM8Sel));
  Register register_1 (.D(dspRAM8In), .en(demultiplexer_1_out0), .clk(dspRAM8Clk), .Q(dspRAM8Out0), .clr(dspRAM8Rst));
  Register register_2 (.D(dspRAM8In), .en(demultiplexer_1_out1), .clk(dspRAM8Clk), .Q(dspRAM8Out1), .clr(dspRAM8Rst));
  Register register_3 (.D(dspRAM8In), .en(demultiplexer_1_out2), .clk(dspRAM8Clk), .Q(dspRAM8Out2), .clr(dspRAM8Rst));
  Register register_4 (.D(dspRAM8In), .en(demultiplexer_1_out3), .clk(dspRAM8Clk), .Q(dspRAM8Out3), .clr(dspRAM8Rst));
  Register register_5 (.D(dspRAM8In), .en(demultiplexer_1_out4), .clk(dspRAM8Clk), .Q(dspRAM8Out4), .clr(dspRAM8Rst));
  Register register_6 (.D(dspRAM8In), .en(demultiplexer_1_out5), .clk(dspRAM8Clk), .Q(dspRAM8Out5), .clr(dspRAM8Rst));
  Register register_7 (.D(dspRAM8In), .en(demultiplexer_1_out6), .clk(dspRAM8Clk), .Q(dspRAM8Out6), .clr(dspRAM8Rst));
  Register register_8 (.D(dspRAM8In), .en(demultiplexer_1_out7), .clk(dspRAM8Clk), .Q(dspRAM8Out7), .clr(dspRAM8Rst));
endmodule

module subDspRAM64 (
  input  [7:0] dspRAM64In,
  input  [5:0] dspRAM64Sel,
  input  dspRAM64WE,
  input  dspRAM64Clk,
  input  dspRAM64Rst,
  output [7:0] dspRAM64Out0,
  output [7:0] dspRAM64Out1,
  output [7:0] dspRAM64Out2,
  output [7:0] dspRAM64Out3,
  output [7:0] dspRAM64Out4,
  output [7:0] dspRAM64Out5,
  output [7:0] dspRAM64Out6,
  output [7:0] dspRAM64Out7,
  output [7:0] dspRAM64Out8,
  output [7:0] dspRAM64Out9,
  output [7:0] dspRAM64Out10,
  output [7:0] dspRAM64Out11,
  output [7:0] dspRAM64Out12,
  output [7:0] dspRAM64Out13,
  output [7:0] dspRAM64Out14,
  output [7:0] dspRAM64Out15,
  output [7:0] dspRAM64Out16,
  output [7:0] dspRAM64Out17,
  output [7:0] dspRAM64Out18,
  output [7:0] dspRAM64Out19,
  output [7:0] dspRAM64Out20,
  output [7:0] dspRAM64Out21,
  output [7:0] dspRAM64Out22,
  output [7:0] dspRAM64Out23,
  output [7:0] dspRAM64Out24,
  output [7:0] dspRAM64Out25,
  output [7:0] dspRAM64Out26,
  output [7:0] dspRAM64Out27,
  output [7:0] dspRAM64Out28,
  output [7:0] dspRAM64Out29,
  output [7:0] dspRAM64Out30,
  output [7:0] dspRAM64Out31,
  output [7:0] dspRAM64Out32,
  output [7:0] dspRAM64Out33,
  output [7:0] dspRAM64Out34,
  output [7:0] dspRAM64Out35,
  output [7:0] dspRAM64Out36,
  output [7:0] dspRAM64Out37,
  output [7:0] dspRAM64Out38,
  output [7:0] dspRAM64Out39,
  output [7:0] dspRAM64Out40,
  output [7:0] dspRAM64Out41,
  output [7:0] dspRAM64Out42,
  output [7:0] dspRAM64Out43,
  output [7:0] dspRAM64Out44,
  output [7:0] dspRAM64Out45,
  output [7:0] dspRAM64Out46,
  output [7:0] dspRAM64Out47,
  output [7:0] dspRAM64Out48,
  output [7:0] dspRAM64Out49,
  output [7:0] dspRAM64Out50,
  output [7:0] dspRAM64Out51,
  output [7:0] dspRAM64Out52,
  output [7:0] dspRAM64Out53,
  output [7:0] dspRAM64Out54,
  output [7:0] dspRAM64Out55,
  output [7:0] dspRAM64Out56,
  output [7:0] dspRAM64Out57,
  output [7:0] dspRAM64Out58,
  output [7:0] dspRAM64Out59,
  output [7:0] dspRAM64Out60,
  output [7:0] dspRAM64Out61,
  output [7:0] dspRAM64Out62,
  output [7:0] dspRAM64Out63
);

  wire demultiplexer_1_out0, demultiplexer_1_out1, demultiplexer_1_out2, demultiplexer_1_out3,
       demultiplexer_1_out4, demultiplexer_1_out5, demultiplexer_1_out6, demultiplexer_1_out7;

  Demultiplexer #(.select(3), .enable("false")) demultiplexer_1 (
    .out0(demultiplexer_1_out0), .out1(demultiplexer_1_out1), .out2(demultiplexer_1_out2),
    .out3(demultiplexer_1_out3), .out4(demultiplexer_1_out4), .out5(demultiplexer_1_out5),
    .out6(demultiplexer_1_out6), .out7(demultiplexer_1_out7), .in(dspRAM64WE), .sel(dspRAM64Sel[5:3]));
  subDspRAM8 subdspram8_1 (
    .dspRAM8In(dspRAM64In), .dspRAM8WE(demultiplexer_1_out0), .dspRAM8Sel(dspRAM64Sel[2:0]),
    .dspRAM8Clk(dspRAM64Clk), .dspRAM8Rst(dspRAM64Rst), .dspRAM8Out0(dspRAM64Out0),
    .dspRAM8Out1(dspRAM64Out1), .dspRAM8Out2(dspRAM64Out2), .dspRAM8Out3(dspRAM64Out3),
    .dspRAM8Out4(dspRAM64Out4), .dspRAM8Out5(dspRAM64Out5), .dspRAM8Out6(dspRAM64Out6),
    .dspRAM8Out7(dspRAM64Out7));
  subDspRAM8 subdspram8_2 (
    .dspRAM8In(dspRAM64In), .dspRAM8WE(demultiplexer_1_out1), .dspRAM8Sel(dspRAM64Sel[2:0]),
    .dspRAM8Clk(dspRAM64Clk), .dspRAM8Rst(dspRAM64Rst), .dspRAM8Out0(dspRAM64Out8),
    .dspRAM8Out1(dspRAM64Out9), .dspRAM8Out2(dspRAM64Out10), .dspRAM8Out3(dspRAM64Out11),
    .dspRAM8Out4(dspRAM64Out12), .dspRAM8Out5(dspRAM64Out13), .dspRAM8Out6(dspRAM64Out14),
    .dspRAM8Out7(dspRAM64Out15));
  subDspRAM8 subdspram8_3 (
    .dspRAM8In(dspRAM64In), .dspRAM8WE(demultiplexer_1_out2), .dspRAM8Sel(dspRAM64Sel[2:0]),
    .dspRAM8Clk(dspRAM64Clk), .dspRAM8Rst(dspRAM64Rst), .dspRAM8Out0(dspRAM64Out16),
    .dspRAM8Out1(dspRAM64Out17), .dspRAM8Out2(dspRAM64Out18), .dspRAM8Out3(dspRAM64Out19),
    .dspRAM8Out4(dspRAM64Out20), .dspRAM8Out5(dspRAM64Out21), .dspRAM8Out6(dspRAM64Out22),
    .dspRAM8Out7(dspRAM64Out23));
  subDspRAM8 subdspram8_4 (
    .dspRAM8In(dspRAM64In), .dspRAM8WE(demultiplexer_1_out3), .dspRAM8Sel(dspRAM64Sel[2:0]),
    .dspRAM8Clk(dspRAM64Clk), .dspRAM8Rst(dspRAM64Rst), .dspRAM8Out0(dspRAM64Out24),
    .dspRAM8Out1(dspRAM64Out25), .dspRAM8Out2(dspRAM64Out26), .dspRAM8Out3(dspRAM64Out27),
    .dspRAM8Out4(dspRAM64Out28), .dspRAM8Out5(dspRAM64Out29), .dspRAM8Out6(dspRAM64Out30),
    .dspRAM8Out7(dspRAM64Out31));
  subDspRAM8 subdspram8_5 (
    .dspRAM8In(dspRAM64In), .dspRAM8WE(demultiplexer_1_out4), .dspRAM8Sel(dspRAM64Sel[2:0]),
    .dspRAM8Clk(dspRAM64Clk), .dspRAM8Rst(dspRAM64Rst), .dspRAM8Out0(dspRAM64Out32),
    .dspRAM8Out1(dspRAM64Out33), .dspRAM8Out2(dspRAM64Out34), .dspRAM8Out3(dspRAM64Out35),
    .dspRAM8Out4(dspRAM64Out36), .dspRAM8Out5(dspRAM64Out37), .dspRAM8Out6(dspRAM64Out38),
    .dspRAM8Out7(dspRAM64Out39));
  subDspRAM8 subdspram8_6 (
    .dspRAM8In(dspRAM64In), .dspRAM8WE(demultiplexer_1_out5), .dspRAM8Sel(dspRAM64Sel[2:0]),
    .dspRAM8Clk(dspRAM64Clk), .dspRAM8Rst(dspRAM64Rst), .dspRAM8Out0(dspRAM64Out40),
    .dspRAM8Out1(dspRAM64Out41), .dspRAM8Out2(dspRAM64Out42), .dspRAM8Out3(dspRAM64Out43),
    .dspRAM8Out4(dspRAM64Out44), .dspRAM8Out5(dspRAM64Out45), .dspRAM8Out6(dspRAM64Out46),
    .dspRAM8Out7(dspRAM64Out47));
  subDspRAM8 subdspram8_7 (
    .dspRAM8In(dspRAM64In), .dspRAM8WE(demultiplexer_1_out6), .dspRAM8Sel(dspRAM64Sel[2:0]),
    .dspRAM8Clk(dspRAM64Clk), .dspRAM8Rst(dspRAM64Rst), .dspRAM8Out0(dspRAM64Out48),
    .dspRAM8Out1(dspRAM64Out49), .dspRAM8Out2(dspRAM64Out50), .dspRAM8Out3(dspRAM64Out51),
    .dspRAM8Out4(dspRAM64Out52), .dspRAM8Out5(dspRAM64Out53), .dspRAM8Out6(dspRAM64Out54),
    .dspRAM8Out7(dspRAM64Out55));
  subDspRAM8 subdspram8_8 (
    .dspRAM8In(dspRAM64In), .dspRAM8WE(demultiplexer_1_out7), .dspRAM8Sel(dspRAM64Sel[2:0]),
    .dspRAM8Clk(dspRAM64Clk), .dspRAM8Rst(dspRAM64Rst), .dspRAM8Out0(dspRAM64Out56),
    .dspRAM8Out1(dspRAM64Out57), .dspRAM8Out2(dspRAM64Out58), .dspRAM8Out3(dspRAM64Out59),
    .dspRAM8Out4(dspRAM64Out60), .dspRAM8Out5(dspRAM64Out61), .dspRAM8Out6(dspRAM64Out62),
    .dspRAM8Out7(dspRAM64Out63));
endmodule

module circTrm (
);

  TTY tty_1 ();  // open: data, clk, we, clr
  Keyboard keyboard_1 ();  // open: clk, re, clr, avail, data
endmodule

module testDsp (
  input  [7:0] in_1,
  input  in_2,
  input  in_3,
  input  in_4,
  input  in_5
);

  wire clock_1_out;
  wire [7:0] circdsp_1_out_7, circdsp_1_out_8, circdsp_1_out_9, circdsp_1_out_10, circdsp_1_out_11,
       circdsp_1_out_12, circdsp_1_out_13, circdsp_1_out_14, circdsp_1_out_15, circdsp_1_out_16,
       circdsp_1_out_17, circdsp_1_out_18, circdsp_1_out_19, circdsp_1_out_20, circdsp_1_out_21,
       circdsp_1_out_22, circdsp_1_out_23, circdsp_1_out_24, circdsp_1_out_25, circdsp_1_out_26,
       circdsp_1_out_27, circdsp_1_out_28, circdsp_1_out_29, circdsp_1_out_30, circdsp_1_out_31,
       circdsp_1_out_32, circdsp_1_out_33, circdsp_1_out_34, circdsp_1_out_35, circdsp_1_out_36,
       circdsp_1_out_37, circdsp_1_out_38, circdsp_1_out_39, circdsp_1_out_40, circdsp_1_out_41,
       circdsp_1_out_42, circdsp_1_out_43, circdsp_1_out_44, circdsp_1_out_45, circdsp_1_out_46,
       circdsp_1_out_47, circdsp_1_out_48, circdsp_1_out_49, circdsp_1_out_50, circdsp_1_out_51,
       circdsp_1_out_52, circdsp_1_out_53, circdsp_1_out_54, circdsp_1_out_55, circdsp_1_out_56,
       circdsp_1_out_57, circdsp_1_out_58, circdsp_1_out_59, circdsp_1_out_60, circdsp_1_out_61,
       circdsp_1_out_62, circdsp_1_out_63, circdsp_1_out_64, circdsp_1_out_65, circdsp_1_out_66,
       circdsp_1_out_67, circdsp_1_out_68, circdsp_1_out_69, circdsp_1_out_70;

  Clock clock_1 (.out(clock_1_out));
  DotMatrix #(.inputtype("row"), .matrixcols(8), .matrixrows(32), .dotshape("circle")) dotmatrix_1 (
    .row0(circdsp_1_out_7), .row1(circdsp_1_out_8), .row2(circdsp_1_out_9), .row3(circdsp_1_out_10),
    .row4(circdsp_1_out_11), .row5(circdsp_1_out_12), .row6(circdsp_1_out_13), .row7(circdsp_1_out_14),
    .row8(circdsp_1_out_15), .row9(circdsp_1_out_16), .row10(circdsp_1_out_17), .row11(circdsp_1_out_18),
    .row12(circdsp_1_out_19), .row13(circdsp_1_out_20), .row14(circdsp_1_out_21), .row15(circdsp_1_out_22),
    .row16(circdsp_1_out_23), .row17(circdsp_1_out_24), .row18(circdsp_1_out_25), .row19(circdsp_1_out_26),
    .row20(circdsp_1_out_27), .row21(circdsp_1_out_28), .row22(circdsp_1_out_29), .row23(circdsp_1_out_30),
    .row24(circdsp_1_out_31), .row25(circdsp_1_out_32), .row26(circdsp_1_out_33), .row27(circdsp_1_out_34),
    .row28(circdsp_1_out_35), .row29(circdsp_1_out_36), .row30(circdsp_1_out_37), .row31(circdsp_1_out_38));
  circDsp circdsp_1 (
    .out_47(circdsp_1_out_47), .out_45(circdsp_1_out_45), .out_43(circdsp_1_out_43),
    .out_41(circdsp_1_out_41), .out_39(circdsp_1_out_39), .out_37(circdsp_1_out_37),
    .out_35(circdsp_1_out_35), .out_33(circdsp_1_out_33), .out_31(circdsp_1_out_31),
    .out_29(circdsp_1_out_29), .out_27(circdsp_1_out_27), .out_25(circdsp_1_out_25),
    .out_23(circdsp_1_out_23), .out_21(circdsp_1_out_21), .out_19(circdsp_1_out_19),
    .out_17(circdsp_1_out_17), .out_15(circdsp_1_out_15), .out_13(circdsp_1_out_13),
    .out_11(circdsp_1_out_11), .out_9(circdsp_1_out_9), .out_7(circdsp_1_out_7), .dspCE(in_5), .dspRst(in_3),
    .dspIn(in_1), .dspWE(in_2), .dspLoad(in_4), .dspClk(clock_1_out), .out_8(circdsp_1_out_8),
    .out_10(circdsp_1_out_10), .out_12(circdsp_1_out_12), .out_14(circdsp_1_out_14),
    .out_16(circdsp_1_out_16), .out_18(circdsp_1_out_18), .out_20(circdsp_1_out_20),
    .out_22(circdsp_1_out_22), .out_24(circdsp_1_out_24), .out_26(circdsp_1_out_26),
    .out_28(circdsp_1_out_28), .out_30(circdsp_1_out_30), .out_32(circdsp_1_out_32),
    .out_34(circdsp_1_out_34), .out_36(circdsp_1_out_36), .out_38(circdsp_1_out_38),
    .out_40(circdsp_1_out_40), .out_42(circdsp_1_out_42), .out_44(circdsp_1_out_44),
    .out_46(circdsp_1_out_46), .out_48(circdsp_1_out_48), .out_49(circdsp_1_out_49),
    .out_50(circdsp_1_out_50), .out_51(circdsp_1_out_51), .out_52(circdsp_1_out_52),
    .out_53(circdsp_1_out_53), .out_54(circdsp_1_out_54), .out_55(circdsp_1_out_55),
    .out_56(circdsp_1_out_56), .out_57(circdsp_1_out_57), .out_58(circdsp_1_out_58),
    .out_59(circdsp_1_out_59), .out_60(circdsp_1_out_60), .out_61(circdsp_1_out_61),
    .out_62(circdsp_1_out_62), .out_63(circdsp_1_out_63), .out_64(circdsp_1_out_64),
    .out_65(circdsp_1_out_65), .out_66(circdsp_1_out_66), .out_67(circdsp_1_out_67),
    .out_68(circdsp_1_out_68), .out_69(circdsp_1_out_69), .out_70(circdsp_1_out_70));
  DotMatrix #(.inputtype("row"), .matrixcols(8), .matrixrows(32), .dotshape("circle")) dotmatrix_2 (
    .row0(circdsp_1_out_39), .row1(circdsp_1_out_40), .row2(circdsp_1_out_41), .row3(circdsp_1_out_42),
    .row4(circdsp_1_out_43), .row5(circdsp_1_out_44), .row6(circdsp_1_out_45), .row7(circdsp_1_out_46),
    .row8(circdsp_1_out_47), .row9(circdsp_1_out_48), .row10(circdsp_1_out_49), .row11(circdsp_1_out_50),
    .row12(circdsp_1_out_51), .row13(circdsp_1_out_52), .row14(circdsp_1_out_53), .row15(circdsp_1_out_54),
    .row16(circdsp_1_out_55), .row17(circdsp_1_out_56), .row18(circdsp_1_out_57), .row19(circdsp_1_out_58),
    .row20(circdsp_1_out_59), .row21(circdsp_1_out_60), .row22(circdsp_1_out_61), .row23(circdsp_1_out_62),
    .row24(circdsp_1_out_63), .row25(circdsp_1_out_64), .row26(circdsp_1_out_65), .row27(circdsp_1_out_66),
    .row28(circdsp_1_out_67), .row29(circdsp_1_out_68), .row30(circdsp_1_out_69), .row31(circdsp_1_out_70));
endmodule
