// Logisim project Abacus_2.circ as structural Verilog: 9 circuits, main circuit main
module main (
);

  Clock clock_1 ();  // open: out
  alu alu_1 ();  // open: CLEAR, CLK, IE, OE, A, B, CN, M, S, EVEN, ODD, SIZE, E, ZF, SF, CO, OV, PF
endmodule

module regs (
  input  [15:0] D,
  input  SIZE,
  input  WE,
  input  [2:0] SEL,
  input  CLK,
  input  CLR,
  output [15:0] Q
);

  wire and_1_out, and_2_out, and_3_out, and_4_out, decoder_1_out0, decoder_1_out1, decoder_1_out2,
       decoder_1_out3, decoder_2_out0, decoder_2_out1, decoder_2_out2, decoder_2_out3, decoder_3_out0,
       decoder_3_out1, decoder_3_out2, decoder_3_out3, not_1_out, xor_1_out;

  and and_1 (and_1_out, SIZE, SEL[0]);
  not not_1 (not_1_out, SEL[0]);
  and and_2 (and_2_out, WE, not_1_out);
  Decoder #(.select(2)) decoder_1 (
    .out0(decoder_1_out0), .out1(decoder_1_out1), .out2(decoder_1_out2), .out3(decoder_1_out3),
    .sel(SEL[2:1]), .en(and_2_out));
  xor xor_1 (xor_1_out, SIZE, SEL[0]);
  and and_3 (and_3_out, WE, xor_1_out);
  Decoder #(.select(2)) decoder_2 (
    .out0(decoder_2_out0), .out1(decoder_2_out1), .out2(decoder_2_out2), .out3(decoder_2_out3),
    .sel(SEL[2:1]), .en(and_3_out));
  and and_4 (and_4_out, and_1_out, WE);
  Decoder #(.select(2)) decoder_3 (
    .out0(decoder_3_out0), .out1(decoder_3_out1), .out2(decoder_3_out2), .out3(decoder_3_out3),
    .sel(SEL[2:1]), .en(and_4_out));
  Register AH (.D(D[15:8]), .en(decoder_2_out0), .clk(CLK), .Q(Q[15:8]), .clr(CLR));
  Register BH (.D(D[15:8]), .en(decoder_2_out1), .clk(CLK), .Q(Q[15:8]), .clr(CLR));
  Register CH (.D(D[15:8]), .en(decoder_2_out2), .clk(CLK), .Q(Q[15:8]), .clr(CLR));
  Register DH (.D(D[15:8]), .en(decoder_2_out3), .clk(CLK), .Q(Q[15:8]), .clr(CLR));
  Register #(.width(16)) EX (.D(D), .en(decoder_3_out0), .clk(CLK), .Q(Q), .clr(CLR));
  Register #(.width(16)) FX (.D(D), .en(decoder_3_out1), .clk(CLK), .Q(Q), .clr(CLR));
  Register #(.width(16)) SP (.D(D), .en(decoder_3_out2), .clk(CLK), .Q(Q), .clr(CLR));
  Register #(.width(16)) BP (.D(D), .en(decoder_3_out3), .clk(CLK), .Q(Q), .clr(CLR));
  Register AL (.D(D[7:0]), .en(decoder_1_out0), .clk(CLK), .Q(Q[7:0]), .clr(CLR));
  Register BL (.D(D[7:0]), .en(decoder_1_out1), .clk(CLK), .Q(Q[7:0]), .clr(CLR));
  Register CL (.D(D[7:0]), .en(decoder_1_out2), .clk(CLK), .Q(Q[7:0]), .clr(CLR));
  Register DL (.D(D[7:0]), .en(decoder_1_out3), .clk(CLK), .Q(Q[7:0]), .clr(CLR));

  // Notes on the sheet:
  //   REDO THIS, NEEDS OUTPUT ENABLE.
  //   OUTPUT TO 2 BUSSES AT ONCE.
endmodule

module regs_flags (
);

  Register FLAGS ();  // open: D, en, clk, Q, clr
endmodule

module alu (
  input  CLEAR,
  input  CLK,
  input  IE,
  input  OE,
  input  [15:0] A,
  input  [15:0] B,
  input  CN,
  input  M,
  input  [3:0] S,
  input  EVEN,
  input  ODD,
  input  SIZE,
  output [15:0] E,
  output ZF,
  output SF,
  output CO,
  output OV,
  output PF
);

  wire alu_core_1_co8, alu_core_1_co16, alu_core_1_ov8, alu_core_1_ov16, alu_parity_1_s_e8,
       alu_parity_1_s_e16;
  wire [7:0] RS_q;
  wire [7:6] undriven;
  wire [15:0] alu_core_1_f, RA_q, RB_q, RE_q;

  Register #(.width(16)) RA (.D(A), .en(IE), .clk(CLK), .Q(RA_q), .clr(CLEAR));
  Register #(.width(16)) RB (.D(B), .en(IE), .clk(CLK), .Q(RB_q), .clr(CLEAR));
  Register RS (.D({undriven, CN, M, S}), .en(IE), .clk(CLK), .Q(RS_q), .clr(CLEAR));
  alu_core alu_core_1 (
    .A(RA_q), .B(RB_q), .CN(RS_q[5]), .S(RS_q[3:0]), .M(RS_q[4]), .F(alu_core_1_f), .CO8(alu_core_1_co8),
    .OV8(alu_core_1_ov8), .OV16(alu_core_1_ov16), .CO16(alu_core_1_co16));
  Register #(.width(16)) RE (.D(alu_core_1_f), .en(IE), .clk(CLK), .Q(RE_q), .clr(CLEAR));
  alu_parity alu_parity_1 (
    .EVEN(EVEN), .ODD(ODD), .DATA(alu_core_1_f), .S_E8(alu_parity_1_s_e8), .S_E16(alu_parity_1_s_e16));  // open: S_O8, S_O16
  alu_flags alu_flags_1 (
    .IN_SIZE(SIZE), .IN_DATA(alu_core_1_f), .IN_C8(alu_core_1_co8), .IN_C16(alu_core_1_co16),
    .IN_O8(alu_core_1_ov8), .IN_O16(alu_core_1_ov16), .IN_P8(alu_parity_1_s_e8), .IN_P16(alu_parity_1_s_e16),
    .ZF(ZF), .SF(SF), .CO(CO), .OV(OV), .PF(PF));
  assign E = OE ? RE_q : 16'bz;  // Controlled_Buffer controlled_buffer_1
endmodule

module alu_core (
  input  [15:0] A,
  input  [15:0] B,
  input  CN,
  input  [3:0] S,
  input  M,
  output [15:0] F,
  output CO8,
  output OV8,
  output OV16,
  output CO16
);

  wire l_74181_e6f12ee4_1_g, l_74181_e6f12ee4_1_p, l_74181_e6f12ee4_2_g, l_74181_e6f12ee4_2_p,
       l_74181_e6f12ee4_3_g, l_74181_e6f12ee4_3_p, l_74181_e6f12ee4_4_g, l_74181_e6f12ee4_4_p,
       l_74182_4f460642_1_cn_x_c4f77548, l_74182_4f460642_1_cn_y_925745ef, l_74182_4f460642_1_cn_z_5d92889f;

  L_74181_e6f12ee4 l_74181_e6f12ee4_1 (
    .A0(A[0]), .M(M), .Cn(CN), .B3(B[3]), .A3(A[3]), .B2(B[2]), .A2(A[2]), .S3(S[3]), .S2(S[2]), .S1(S[1]),
    .S0(S[0]), .B1(B[1]), .A1(A[1]), .B0(B[0]), .G(l_74181_e6f12ee4_1_g), .F0(F[0]),
    .P(l_74181_e6f12ee4_1_p), .F3(F[3]), .F2(F[2]), .F1(F[1]));  // open: Cn_4_cb6af43f, A_B_66665e43
  L_74181_e6f12ee4 l_74181_e6f12ee4_2 (
    .A0(A[4]), .M(M), .Cn(l_74182_4f460642_1_cn_x_c4f77548), .B3(B[7]), .A3(A[7]), .B2(B[6]), .A2(A[6]),
    .S3(S[3]), .S2(S[2]), .S1(S[1]), .S0(S[0]), .B1(B[5]), .A1(A[5]), .B0(B[4]), .G(l_74181_e6f12ee4_2_g),
    .F0(F[4]), .Cn_4_cb6af43f(CO8), .P(l_74181_e6f12ee4_2_p), .F3(F[7]), .F2(F[6]), .F1(F[5]));  // open: A_B_66665e43
  L_74182_4f460642 l_74182_4f460642_1 (
    .Cn(CN), .iG1(l_74181_e6f12ee4_2_g), .iP1(l_74181_e6f12ee4_2_p), .iG2(l_74181_e6f12ee4_3_g),
    .iP2(l_74181_e6f12ee4_3_p), .iG0(l_74181_e6f12ee4_1_g), .iG3(l_74181_e6f12ee4_4_g),
    .iP3(l_74181_e6f12ee4_4_p), .iP0(l_74181_e6f12ee4_1_p), .Cn_x_c4f77548(l_74182_4f460642_1_cn_x_c4f77548),
    .Cn_y_925745ef(l_74182_4f460642_1_cn_y_925745ef), .Cn_z_5d92889f(l_74182_4f460642_1_cn_z_5d92889f));  // open: iG, iP
  L_74181_e6f12ee4 l_74181_e6f12ee4_3 (
    .A0(A[8]), .M(M), .Cn(l_74182_4f460642_1_cn_y_925745ef), .B3(B[11]), .A3(A[11]), .B2(B[10]), .A2(A[10]),
    .S3(S[3]), .S2(S[2]), .S1(S[1]), .S0(S[0]), .B1(B[9]), .A1(A[9]), .B0(B[8]), .G(l_74181_e6f12ee4_3_g),
    .F0(F[8]), .P(l_74181_e6f12ee4_3_p), .F3(F[11]), .F2(F[10]), .F1(F[9]));  // open: Cn_4_cb6af43f, A_B_66665e43
  L_74181_e6f12ee4 l_74181_e6f12ee4_4 (
    .A0(A[12]), .M(M), .Cn(l_74182_4f460642_1_cn_z_5d92889f), .B3(B[15]), .A3(A[15]), .B2(B[14]), .A2(A[14]),
    .S3(S[3]), .S2(S[2]), .S1(S[1]), .S0(S[0]), .B1(B[13]), .A1(A[13]), .B0(B[12]), .G(l_74181_e6f12ee4_4_g),
    .F0(F[12]), .Cn_4_cb6af43f(CO16), .P(l_74181_e6f12ee4_4_p), .F3(F[15]), .F2(F[14]), .F1(F[13]));  // open: A_B_66665e43
  xor xor_1 (OV8, CO8, l_74182_4f460642_1_cn_x_c4f77548);
  xor xor_2 (OV16, l_74182_4f460642_1_cn_z_5d92889f, CO16);

  // Notes on the sheet:
  //   0–3
  //   4–7
  //   8–11
  //   12–15
endmodule

module alu_flags (
  input  IN_SIZE,
  input  [15:0] IN_DATA,
  input  IN_C8,
  input  IN_C16,
  input  IN_O8,
  input  IN_O16,
  input  IN_P8,
  input  IN_P16,
  output ZF,
  output SF,
  output CO,
  output OV,
  output PF
);

  wire and_1_out, and_2_out, and_3_out, not_1_out;

  and and_1 (and_1_out, IN_DATA[15], IN_DATA[14], IN_DATA[13], IN_DATA[12], IN_DATA[11], IN_DATA[10], IN_DATA[9], IN_DATA[8]);
  and and_2 (and_2_out, IN_DATA[7], IN_DATA[6], IN_DATA[5], IN_DATA[4], IN_DATA[3], IN_DATA[2], IN_DATA[1], IN_DATA[0]);
  and and_3 (and_3_out, and_2_out, and_1_out);
  not not_1 (not_1_out, IN_SIZE);
  assign ZF = not_1_out ? and_2_out : 1'bz;  // Controlled_Buffer controlled_buffer_1
  assign SF = not_1_out ? IN_DATA[7] : 1'bz;  // Controlled_Buffer controlled_buffer_2
  assign CO = not_1_out ? IN_C8 : 1'bz;  // Controlled_Buffer controlled_buffer_3
  assign OV = not_1_out ? IN_O8 : 1'bz;  // Controlled_Buffer controlled_buffer_4
  assign PF = not_1_out ? IN_P8 : 1'bz;  // Controlled_Buffer controlled_buffer_5
  assign ZF = IN_SIZE ? and_3_out : 1'bz;  // Controlled_Buffer controlled_buffer_6
  assign SF = IN_SIZE ? IN_DATA[15] : 1'bz;  // Controlled_Buffer controlled_buffer_7
  assign CO = IN_SIZE ? IN_C16 : 1'bz;  // Controlled_Buffer controlled_buffer_8
  assign OV = IN_SIZE ? IN_O16 : 1'bz;  // Controlled_Buffer controlled_buffer_9
  assign PF = IN_SIZE ? IN_P16 : 1'bz;  // Controlled_Buffer controlled_buffer_10
endmodule

module alu_parity (
  input  EVEN,
  input  ODD,
  input  [15:0] DATA,
  output S_E8,
  output S_O8,
  output S_E16,
  output S_O16
);

  alu_47180 alu_47180_1 (.DATA(DATA[7:0]), .EVEN(EVEN), .ODD(ODD), .SUM_E(S_E8), .SUM_O(S_O8));
  alu_47180 alu_47180_2 (.DATA(DATA[15:8]), .EVEN(S_E8), .ODD(S_O8), .SUM_E(S_E16), .SUM_O(S_O16));
endmodule

module alu_47180 (
  input  [7:0] DATA,
  input  EVEN,
  input  ODD,
  output SUM_E,
  output SUM_O
);

  wire [3:0] bitadder_1_out;

  BitAdder bitadder_1 (.in0(DATA), .out(bitadder_1_out));
  // PlaRom #(.Contents("1 1 2 2 1 2 1 2 1 2 2 1 0 2 2 0 1 1 1 0 0 1 0 1 1 0*3 1 1"), .Select("high"), .\and (6), .outputs(2)) P_CHK: pin names not known; wires that end beside it: {bitadder_1_out[0], EVEN, ODD}, {SUM_O, SUM_E}
endmodule

module nb_regs (
);

  Register BANK_0 ();  // open: D, en, clk, Q, clr
  Register BANK_1 ();  // open: D, en, clk, Q, clr
  Register BANK_2 ();  // open: D, en, clk, Q, clr
  Register BANK_3 ();  // open: D, en, clk, Q, clr
  Register BANK_4 ();  // open: D, en, clk, Q, clr
  Register BANK_5 ();  // open: D, en, clk, Q, clr
  Register BANK_6 ();  // open: D, en, clk, Q, clr
  Register BANK_7 ();  // open: D, en, clk, Q, clr
  Register BANK_8 ();  // open: D, en, clk, Q, clr
  Register BANK_9 ();  // open: D, en, clk, Q, clr
  Register BANK_A ();  // open: D, en, clk, Q, clr
  Register BANK_B ();  // open: D, en, clk, Q, clr
  Register BANK_C ();  // open: D, en, clk, Q, clr
  Register BANK_D ();  // open: D, en, clk, Q, clr
  Register BANK_E ();  // open: D, en, clk, Q, clr
  Register BANK_F ();  // open: D, en, clk, Q, clr
endmodule
