// Logisim project 74-Series IC.circ as structural Verilog: 18 circuits, main circuit 7400
module _7400 (
  input  VCC,
  input  GND,
  input  A1,
  input  B1,
  input  A2,
  input  B2,
  input  A3,
  input  B3,
  input  A4,
  input  B4,
  output Y1,
  output Y2,
  output Y3,
  output Y4
);

  wire nand_1_out, nand_2_out, nand_3_out, nand_4_out, not_1_out, PWR;

  not not_1 (not_1_out, GND);
  and and_1 (PWR, VCC, not_1_out);
  nand nand_1 (nand_1_out, A1, B1);
  assign Y1 = PWR ? nand_1_out : 1'bz;  // Controlled_Buffer controlled_buffer_1
  assign Y2 = PWR ? nand_2_out : 1'bz;  // Controlled_Buffer controlled_buffer_2
  nand nand_2 (nand_2_out, A2, B2);
  assign Y3 = PWR ? nand_3_out : 1'bz;  // Controlled_Buffer controlled_buffer_3
  nand nand_3 (nand_3_out, A3, B3);
  assign Y4 = PWR ? nand_4_out : 1'bz;  // Controlled_Buffer controlled_buffer_4
  nand nand_4 (nand_4_out, A4, B4);
endmodule

module _7402 (
  input  VCC,
  input  GND,
  input  A1,
  input  B1,
  input  A2,
  input  B2,
  input  A3,
  input  B3,
  input  A4,
  input  B4,
  output Y1,
  output Y2,
  output Y3,
  output Y4
);

  wire nor_1_out, nor_2_out, nor_3_out, nor_4_out, not_1_out, PWR;

  not not_1 (not_1_out, GND);
  and and_1 (PWR, VCC, not_1_out);
  nor nor_1 (nor_1_out, A1, B1);
  assign Y1 = PWR ? nor_1_out : 1'bz;  // Controlled_Buffer controlled_buffer_1
  assign Y2 = PWR ? nor_2_out : 1'bz;  // Controlled_Buffer controlled_buffer_2
  nor nor_2 (nor_2_out, A2, B2);
  assign Y3 = PWR ? nor_3_out : 1'bz;  // Controlled_Buffer controlled_buffer_3
  nor nor_3 (nor_3_out, A3, B3);
  assign Y4 = PWR ? nor_4_out : 1'bz;  // Controlled_Buffer controlled_buffer_4
  nor nor_4 (nor_4_out, A4, B4);
endmodule

module _7404 (
  input  VCC,
  input  GND,
  input  A1,
  input  A2,
  input  A3,
  input  A4,
  input  A5,
  input  A6,
  output Y1,
  output Y2,
  output Y3,
  output Y4,
  output Y5,
  output Y6
);

  wire not_1_out, not_2_out, not_3_out, not_4_out, not_5_out, not_6_out, not_7_out, PWR;

  not not_1 (not_1_out, GND);
  and and_1 (PWR, VCC, not_1_out);
  assign Y1 = PWR ? not_2_out : 1'bz;  // Controlled_Buffer controlled_buffer_1
  not not_2 (not_2_out, A1);
  assign Y2 = PWR ? not_3_out : 1'bz;  // Controlled_Buffer controlled_buffer_2
  not not_3 (not_3_out, A2);
  assign Y3 = PWR ? not_4_out : 1'bz;  // Controlled_Buffer controlled_buffer_3
  not not_4 (not_4_out, A3);
  not not_5 (not_5_out, A4);
  assign Y4 = PWR ? not_5_out : 1'bz;  // Controlled_Buffer controlled_buffer_4
  not not_6 (not_6_out, A5);
  assign Y5 = PWR ? not_6_out : 1'bz;  // Controlled_Buffer controlled_buffer_5
  assign Y6 = PWR ? not_7_out : 1'bz;  // Controlled_Buffer controlled_buffer_6
  not not_7 (not_7_out, A6);
endmodule

module _7408 (
  input  VCC,
  input  GND,
  input  A1,
  input  B1,
  input  A2,
  input  B2,
  input  A3,
  input  B3,
  input  A4,
  input  B4,
  output Y1,
  output Y2,
  output Y3,
  output Y4
);

  wire and_2_out, and_3_out, and_4_out, and_5_out, not_1_out, PWR;

  not not_1 (not_1_out, GND);
  and and_1 (PWR, VCC, not_1_out);
  and and_2 (and_2_out, A1, B1);
  assign Y1 = PWR ? and_2_out : 1'bz;  // Controlled_Buffer controlled_buffer_1
  and and_3 (and_3_out, A2, B2);
  assign Y2 = PWR ? and_3_out : 1'bz;  // Controlled_Buffer controlled_buffer_2
  and and_4 (and_4_out, A3, B3);
  assign Y3 = PWR ? and_4_out : 1'bz;  // Controlled_Buffer controlled_buffer_3
  and and_5 (and_5_out, A4, B4);
  assign Y4 = PWR ? and_5_out : 1'bz;  // Controlled_Buffer controlled_buffer_4
endmodule

module _7432 (
  input  VCC,
  input  GND,
  input  A1,
  input  B1,
  input  A2,
  input  B2,
  input  A3,
  input  B3,
  input  A4,
  input  B4,
  output Y1,
  output Y2,
  output Y3,
  output Y4
);

  wire not_1_out, or_1_out, or_2_out, or_3_out, or_4_out, PWR;

  not not_1 (not_1_out, GND);
  and and_1 (PWR, VCC, not_1_out);
  or or_1 (or_1_out, A1, B1);
  assign Y1 = PWR ? or_1_out : 1'bz;  // Controlled_Buffer controlled_buffer_1
  or or_2 (or_2_out, A2, B2);
  assign Y2 = PWR ? or_2_out : 1'bz;  // Controlled_Buffer controlled_buffer_2
  assign Y3 = PWR ? or_3_out : 1'bz;  // Controlled_Buffer controlled_buffer_3
  or or_3 (or_3_out, A3, B3);
  assign Y4 = PWR ? or_4_out : 1'bz;  // Controlled_Buffer controlled_buffer_4
  or or_4 (or_4_out, A4, B4);
endmodule

module _7476 (
  input  VCC,
  input  GND,
  input  J1,
  input  CLK1,
  input  K1,
  input  nPRE1,
  input  nCLR1,
  input  J2,
  input  CLK2,
  input  K2,
  input  nPRE2,
  input  nCLR2,
  output Q1,
  output nQ1,
  output Q2,
  output nQ2
);

  wire j_k_ff_1_q, j_k_ff_1_qn, j_k_ff_2_q, j_k_ff_2_qn, not_1_out, not_2_out, not_3_out, not_4_out,
       not_5_out, PWR;

  not not_1 (not_1_out, GND);
  and and_1 (PWR, VCC, not_1_out);
  not not_2 (not_2_out, nPRE1);
  not not_3 (not_3_out, nPRE2);
  assign Q1 = PWR ? j_k_ff_1_q : 1'bz;  // Controlled_Buffer controlled_buffer_1
  J_K_Flip_Flop j_k_ff_1 (
    .J(J1), .clk(CLK1), .K(K1), .Q(j_k_ff_1_q), .Qn(j_k_ff_1_qn), .preset(not_2_out), .en(PWR),
    .reset(not_4_out));
  not not_4 (not_4_out, nCLR1);
  J_K_Flip_Flop j_k_ff_2 (
    .J(J2), .clk(CLK2), .K(K2), .Q(j_k_ff_2_q), .Qn(j_k_ff_2_qn), .preset(not_3_out), .en(PWR),
    .reset(not_5_out));
  assign Q2 = PWR ? j_k_ff_2_q : 1'bz;  // Controlled_Buffer controlled_buffer_2
  assign nQ2 = PWR ? j_k_ff_2_qn : 1'bz;  // Controlled_Buffer controlled_buffer_3
  not not_5 (not_5_out, nCLR2);
  assign nQ1 = PWR ? j_k_ff_1_qn : 1'bz;  // Controlled_Buffer controlled_buffer_4
endmodule

module _7486 (
  input  VCC,
  input  GND,
  input  A1,
  input  B1,
  input  A2,
  input  B2,
  input  A3,
  input  B3,
  input  A4,
  input  B4,
  output Y1,
  output Y2,
  output Y3,
  output Y4
);

  wire not_1_out, PWR, xor_1_out, xor_2_out, xor_3_out, xor_4_out;

  not not_1 (not_1_out, GND);
  and and_1 (PWR, VCC, not_1_out);
  assign Y1 = PWR ? xor_1_out : 1'bz;  // Controlled_Buffer controlled_buffer_1
  xor xor_1 (xor_1_out, A1, B1);
  xor xor_2 (xor_2_out, A2, B2);
  assign Y2 = PWR ? xor_2_out : 1'bz;  // Controlled_Buffer controlled_buffer_2
  xor xor_3 (xor_3_out, A3, B3);
  assign Y3 = PWR ? xor_3_out : 1'bz;  // Controlled_Buffer controlled_buffer_3
  xor xor_4 (xor_4_out, A4, B4);
  assign Y4 = PWR ? xor_4_out : 1'bz;  // Controlled_Buffer controlled_buffer_4
endmodule

module _74107 (
  input  VCC,
  input  GND,
  input  J1,
  input  CLK1,
  input  K1,
  input  nCLR1,
  input  J2,
  input  CLK2,
  input  K2,
  input  nCLR2,
  output Q1,
  output nQ1,
  output Q2,
  output nQ2
);

  wire j_k_ff_1_q, j_k_ff_1_qn, j_k_ff_2_q, j_k_ff_2_qn, not_1_out, not_2_out, not_3_out, PWR;

  not not_1 (not_1_out, GND);
  and and_1 (PWR, VCC, not_1_out);
  J_K_Flip_Flop j_k_ff_1 (
    .J(J1), .clk(CLK1), .K(K1), .Q(j_k_ff_1_q), .Qn(j_k_ff_1_qn), .preset(1'b0), .en(PWR), .reset(not_2_out));
  assign Q1 = PWR ? j_k_ff_1_q : 1'bz;  // Controlled_Buffer controlled_buffer_1
  not not_2 (not_2_out, nCLR1);
  assign Q2 = PWR ? j_k_ff_2_q : 1'bz;  // Controlled_Buffer controlled_buffer_2
  J_K_Flip_Flop j_k_ff_2 (
    .J(J2), .clk(CLK2), .K(K2), .Q(j_k_ff_2_q), .Qn(j_k_ff_2_qn), .preset(1'b0), .en(PWR), .reset(not_3_out));
  assign nQ2 = PWR ? j_k_ff_2_qn : 1'bz;  // Controlled_Buffer controlled_buffer_3
  not not_3 (not_3_out, nCLR2);
  assign nQ1 = PWR ? j_k_ff_1_qn : 1'bz;  // Controlled_Buffer controlled_buffer_4
endmodule

module _74138 (
  input  VCC,
  input  GND,
  input  nE1,
  input  nE2,
  input  E3,
  input  A0,
  input  A1,
  input  A2,
  output nO0,
  output nO1,
  output nO2,
  output nO3,
  output nO4,
  output nO5,
  output nO6,
  output nO7
);

  wire and_2_out, controlled_buffer_1_out, demultiplexer_1_out0, demultiplexer_1_out1, demultiplexer_1_out2,
       demultiplexer_1_out3, demultiplexer_1_out4, demultiplexer_1_out5, demultiplexer_1_out6,
       demultiplexer_1_out7, nor_1_out, not_1_out, not_2_out, not_3_out, not_4_out, not_5_out, not_6_out,
       not_7_out, not_8_out, not_9_out, PWR;

  and and_1 (PWR, VCC, not_1_out);
  not not_1 (not_1_out, GND);
  nor nor_1 (nor_1_out, nE1, nE2);
  assign controlled_buffer_1_out = PWR ? and_2_out : 1'bz;  // Controlled_Buffer controlled_buffer_1
  and and_2 (and_2_out, nor_1_out, E3);
  Demultiplexer #(.select(3)) demultiplexer_1 (
    .out0(demultiplexer_1_out0), .out1(demultiplexer_1_out1), .out2(demultiplexer_1_out2),
    .out3(demultiplexer_1_out3), .out4(demultiplexer_1_out4), .out5(demultiplexer_1_out5),
    .out6(demultiplexer_1_out6), .out7(demultiplexer_1_out7), .in(controlled_buffer_1_out), .sel({A2, A1, A0}));  // open: en
  not not_2 (not_2_out, demultiplexer_1_out0);
  not not_3 (not_3_out, demultiplexer_1_out1);
  not not_4 (not_4_out, demultiplexer_1_out2);
  not not_5 (not_5_out, demultiplexer_1_out3);
  not not_6 (not_6_out, demultiplexer_1_out4);
  not not_7 (not_7_out, demultiplexer_1_out5);
  not not_8 (not_8_out, demultiplexer_1_out6);
  not not_9 (not_9_out, demultiplexer_1_out7);
  assign nO0 = PWR ? not_2_out : 1'bz;  // Controlled_Buffer controlled_buffer_2
  assign nO1 = PWR ? not_3_out : 1'bz;  // Controlled_Buffer controlled_buffer_3
  assign nO2 = PWR ? not_4_out : 1'bz;  // Controlled_Buffer controlled_buffer_4
  assign nO3 = PWR ? not_5_out : 1'bz;  // Controlled_Buffer controlled_buffer_5
  assign nO4 = PWR ? not_6_out : 1'bz;  // Controlled_Buffer controlled_buffer_6
  assign nO5 = PWR ? not_7_out : 1'bz;  // Controlled_Buffer controlled_buffer_7
  assign nO6 = PWR ? not_8_out : 1'bz;  // Controlled_Buffer controlled_buffer_8
  assign nO7 = PWR ? not_9_out : 1'bz;  // Controlled_Buffer controlled_buffer_9
endmodule

module _74139 (
  input  VCC,
  input  GND,
  input  nG1,
  input  A1,
  input  B1,
  input  nG2,
  input  A2,
  input  B2,
  output _1Y0,
  output _1Y1,
  output _1Y2,
  output _1Y3,
  output _2Y0,
  output _2Y1,
  output _2Y2,
  output _2Y3
);

  wire controlled_buffer_1_out, controlled_buffer_2_out, demultiplexer_1_out0, demultiplexer_1_out1,
       demultiplexer_1_out2, demultiplexer_1_out3, demultiplexer_2_out0, demultiplexer_2_out1,
       demultiplexer_2_out2, demultiplexer_2_out3, not_1_out, not_2_out, not_3_out, not_4_out, not_5_out,
       not_6_out, not_7_out, not_8_out, not_9_out, not_10_out, not_11_out, PWR;

  and and_1 (PWR, VCC, not_1_out);
  not not_1 (not_1_out, GND);
  not not_2 (not_2_out, nG1);
  not not_3 (not_3_out, nG2);
  assign controlled_buffer_1_out = PWR ? not_2_out : 1'bz;  // Controlled_Buffer controlled_buffer_1
  assign controlled_buffer_2_out = PWR ? not_3_out : 1'bz;  // Controlled_Buffer controlled_buffer_2
  Demultiplexer #(.select(2)) demultiplexer_1 (
    .out0(demultiplexer_1_out0), .out1(demultiplexer_1_out1), .out2(demultiplexer_1_out2),
    .out3(demultiplexer_1_out3), .in(controlled_buffer_1_out), .sel({B1, A1}));  // open: en
  Demultiplexer #(.select(2)) demultiplexer_2 (
    .out0(demultiplexer_2_out0), .out1(demultiplexer_2_out1), .out2(demultiplexer_2_out2),
    .out3(demultiplexer_2_out3), .in(controlled_buffer_2_out), .sel({B2, A2}));  // open: en
  not not_4 (not_4_out, demultiplexer_1_out0);
  assign _1Y0 = PWR ? not_4_out : 1'bz;  // Controlled_Buffer controlled_buffer_3
  assign _1Y1 = PWR ? not_5_out : 1'bz;  // Controlled_Buffer controlled_buffer_4
  not not_5 (not_5_out, demultiplexer_1_out1);
  not not_6 (not_6_out, demultiplexer_1_out2);
  assign _1Y2 = PWR ? not_6_out : 1'bz;  // Controlled_Buffer controlled_buffer_5
  assign _1Y3 = PWR ? not_7_out : 1'bz;  // Controlled_Buffer controlled_buffer_6
  not not_7 (not_7_out, demultiplexer_1_out3);
  not not_8 (not_8_out, demultiplexer_2_out0);
  assign _2Y0 = PWR ? not_8_out : 1'bz;  // Controlled_Buffer controlled_buffer_7
  not not_9 (not_9_out, demultiplexer_2_out1);
  assign _2Y1 = PWR ? not_9_out : 1'bz;  // Controlled_Buffer controlled_buffer_8
  assign _2Y2 = PWR ? not_10_out : 1'bz;  // Controlled_Buffer controlled_buffer_9
  not not_10 (not_10_out, demultiplexer_2_out2);
  assign _2Y3 = PWR ? not_11_out : 1'bz;  // Controlled_Buffer controlled_buffer_10
  not not_11 (not_11_out, demultiplexer_2_out3);
endmodule

module _74157 (
  input  VCC,
  input  STR,
  input  GND,
  input  SEL,
  input  A1,
  input  B1,
  input  A2,
  input  B2,
  input  A3,
  input  B3,
  input  A4,
  input  B4,
  output Y1,
  output Y2,
  output Y3,
  output Y4
);

  wire bitselector_1_out, bitselector_2_out, bitselector_3_out, bitselector_4_out, not_1_out, PWR, STROBE;
  wire [1:0] controlled_buffer_1_out, controlled_buffer_2_out, controlled_buffer_3_out,
       controlled_buffer_4_out;

  not not_1 (not_1_out, GND);
  and and_1 (PWR, VCC, not_1_out);
  not not_2 (STROBE, STR);
  assign controlled_buffer_1_out = STROBE ? {B1, A1} : 2'bz;  // Controlled_Buffer controlled_buffer_1
  assign controlled_buffer_2_out = STROBE ? {B2, A2} : 2'bz;  // Controlled_Buffer controlled_buffer_2
  assign controlled_buffer_3_out = STROBE ? {B3, A3} : 2'bz;  // Controlled_Buffer controlled_buffer_3
  assign controlled_buffer_4_out = STROBE ? {B4, A4} : 2'bz;  // Controlled_Buffer controlled_buffer_4
  BitSelector #(.width(2)) bitselector_1 (.in(controlled_buffer_1_out), .out(bitselector_1_out), .sel(SEL));
  BitSelector #(.width(2)) bitselector_2 (.in(controlled_buffer_2_out), .out(bitselector_2_out), .sel(SEL));
  BitSelector #(.width(2)) bitselector_3 (.in(controlled_buffer_3_out), .out(bitselector_3_out), .sel(SEL));
  BitSelector #(.width(2)) bitselector_4 (.in(controlled_buffer_4_out), .out(bitselector_4_out), .sel(SEL));
  assign Y1 = PWR ? bitselector_1_out : 1'bz;  // Controlled_Buffer controlled_buffer_5
  assign Y2 = PWR ? bitselector_2_out : 1'bz;  // Controlled_Buffer controlled_buffer_6
  assign Y3 = PWR ? bitselector_3_out : 1'bz;  // Controlled_Buffer controlled_buffer_7
  assign Y4 = PWR ? bitselector_4_out : 1'bz;  // Controlled_Buffer controlled_buffer_8
endmodule

module _74161 (
  input  VCC,
  input  GND,
  input  nLOAD,
  input  P0,
  input  P1,
  input  P2,
  input  P3,
  input  ENT,
  input  ENP,
  input  CLR,
  input  CLK,
  output Q0,
  output Q1,
  output Q2,
  output RCO,
  output Q3
);

  wire and_2_out, controlled_buffer_1_out, controlled_buffer_3_out, controlled_buffer_4_out,
       controlled_buffer_5_out, counter_1_carry, not_1_out, not_2_out, PWR;
  wire [3:0] controlled_buffer_2_out, counter_1_q;

  not not_1 (not_1_out, GND);
  and and_1 (PWR, VCC, not_1_out);
  not not_2 (not_2_out, nLOAD);
  assign controlled_buffer_1_out = PWR ? not_2_out : 1'bz;  // Controlled_Buffer controlled_buffer_1
  assign controlled_buffer_2_out = PWR ? {P3, P2, P1, P0} : 4'bz;  // Controlled_Buffer controlled_buffer_2
  assign controlled_buffer_3_out = PWR ? ENP : 1'bz;  // Controlled_Buffer controlled_buffer_3
  Counter #(.width(4), .max('hf)) counter_1 (
    .load(controlled_buffer_1_out), .D(controlled_buffer_2_out), .count(controlled_buffer_3_out),
    .Q(counter_1_q), .carry(counter_1_carry), .clk(controlled_buffer_5_out), .clr(controlled_buffer_4_out));
  assign controlled_buffer_4_out = PWR ? CLR : 1'bz;  // Controlled_Buffer controlled_buffer_4
  assign controlled_buffer_5_out = PWR ? CLK : 1'bz;  // Controlled_Buffer controlled_buffer_5
  assign RCO = and_2_out ? counter_1_carry : 1'bz;  // Controlled_Buffer controlled_buffer_6
  and and_2 (and_2_out, ENT, PWR);
  assign {Q3, Q2, Q1, Q0} = PWR ? counter_1_q : 4'bz;  // Controlled_Buffer controlled_buffer_7
endmodule

module _74173 (
  input  VCC,
  input  GND,
  input  _1D,
  input  _2D,
  input  nG1,
  input  _3D,
  input  nG2,
  input  _4D,
  input  CLR,
  input  CLK,
  input  M,
  input  N,
  output _1Q,
  output _2Q,
  output _3Q,
  output _4Q
);

  wire and_2_out, and_3_out, and_4_out, and_5_out, nor_1_out, nor_2_out, not_1_out, PWR;
  wire [3:0] register_1_q;

  not not_1 (not_1_out, GND);
  and and_1 (PWR, VCC, not_1_out);
  nor nor_1 (nor_1_out, nG1, nG2);
  and and_2 (and_2_out, nor_1_out, PWR);
  Register #(.width(4)) register_1 (
    .D({_4D, _3D, _2D, _1D}), .en(and_2_out), .Q(register_1_q), .clk(and_4_out), .clr(and_3_out));
  and and_3 (and_3_out, CLR, PWR);
  and and_4 (and_4_out, CLK, PWR);
  assign {_4Q, _3Q, _2Q, _1Q} = and_5_out ? register_1_q : 4'bz;  // Controlled_Buffer controlled_buffer_1
  and and_5 (and_5_out, nor_2_out, PWR);
  nor nor_2 (nor_2_out, M, N);
endmodule

module _74245 (
  input  VCC,
  input  GND,
  input  nOE,
  input  DIR,
  input  A0,
  input  A1,
  input  A2,
  input  A3,
  input  A4,
  input  A5,
  input  A6,
  input  A7,
  output B0,
  output B1,
  output B2,
  output B3,
  output B4,
  output B5,
  output B6,
  output B7
);

  wire and_2_out, and_3_out, not_1_out, not_2_out, PWR;

  not not_1 (not_1_out, GND);
  and and_1 (PWR, VCC, not_1_out);
  not not_2 (not_2_out, nOE);
  and and_2 (and_2_out, not_2_out, PWR);
  and and_3 (and_3_out, and_2_out, DIR);
  assign B0 = and_3_out ? A0 : 1'bz;  // Controlled_Buffer controlled_buffer_1
  assign B1 = and_3_out ? A1 : 1'bz;  // Controlled_Buffer controlled_buffer_2
  assign B2 = and_3_out ? A2 : 1'bz;  // Controlled_Buffer controlled_buffer_3
  assign B3 = and_3_out ? A3 : 1'bz;  // Controlled_Buffer controlled_buffer_4
  assign B4 = and_3_out ? A4 : 1'bz;  // Controlled_Buffer controlled_buffer_5
  assign B5 = and_3_out ? A5 : 1'bz;  // Controlled_Buffer controlled_buffer_6
  assign B6 = and_3_out ? A6 : 1'bz;  // Controlled_Buffer controlled_buffer_7
  assign B7 = and_3_out ? A7 : 1'bz;  // Controlled_Buffer controlled_buffer_8
endmodule

module _74273 (
  input  VCC,
  input  GND,
  input  CLK,
  input  nCLR,
  input  D0,
  input  D1,
  input  D2,
  input  D3,
  input  D4,
  input  D5,
  input  D6,
  input  D7,
  output Q0,
  output Q4,
  output Q1,
  output Q5,
  output Q2,
  output Q6,
  output Q3,
  output Q7
);

  wire controlled_buffer_1_out, controlled_buffer_2_out, controlled_buffer_3_out, controlled_buffer_4_out,
       controlled_buffer_9_out, controlled_buffer_10_out, controlled_buffer_11_out, controlled_buffer_12_out,
       d_ff_1_q, d_ff_2_q, d_ff_3_q, d_ff_4_q, d_ff_5_q, d_ff_6_q, d_ff_7_q, d_ff_8_q, not_1_out, not_2_out,
       not_3_out, not_4_out, not_5_out, not_6_out, not_7_out, not_8_out, not_9_out, PWR;

  not not_1 (not_1_out, GND);
  and and_1 (PWR, VCC, not_1_out);
  assign controlled_buffer_1_out = PWR ? D0 : 1'bz;  // Controlled_Buffer controlled_buffer_1
  assign controlled_buffer_2_out = PWR ? D1 : 1'bz;  // Controlled_Buffer controlled_buffer_2
  assign controlled_buffer_3_out = PWR ? D2 : 1'bz;  // Controlled_Buffer controlled_buffer_3
  assign controlled_buffer_4_out = PWR ? D3 : 1'bz;  // Controlled_Buffer controlled_buffer_4
  D_Flip_Flop d_ff_1 (
    .clk(CLK), .D(controlled_buffer_1_out), .Q(d_ff_1_q), .en(PWR), .reset(not_2_out));  // open: Qn, preset
  assign Q0 = PWR ? d_ff_1_q : 1'bz;  // Controlled_Buffer controlled_buffer_5
  not not_2 (not_2_out, nCLR);
  D_Flip_Flop d_ff_2 (
    .clk(CLK), .D(controlled_buffer_2_out), .Q(d_ff_2_q), .en(PWR), .reset(not_3_out));  // open: Qn, preset
  assign Q1 = PWR ? d_ff_2_q : 1'bz;  // Controlled_Buffer controlled_buffer_6
  not not_3 (not_3_out, nCLR);
  D_Flip_Flop d_ff_3 (
    .clk(CLK), .D(controlled_buffer_3_out), .Q(d_ff_3_q), .en(PWR), .reset(not_4_out));  // open: Qn, preset
  assign Q2 = PWR ? d_ff_3_q : 1'bz;  // Controlled_Buffer controlled_buffer_7
  not not_4 (not_4_out, nCLR);
  assign Q3 = PWR ? d_ff_4_q : 1'bz;  // Controlled_Buffer controlled_buffer_8
  D_Flip_Flop d_ff_4 (
    .clk(CLK), .D(controlled_buffer_4_out), .Q(d_ff_4_q), .en(PWR), .reset(not_5_out));  // open: Qn, preset
  not not_5 (not_5_out, nCLR);
  assign controlled_buffer_9_out = PWR ? D4 : 1'bz;  // Controlled_Buffer controlled_buffer_9
  assign controlled_buffer_10_out = PWR ? D5 : 1'bz;  // Controlled_Buffer controlled_buffer_10
  assign controlled_buffer_11_out = PWR ? D6 : 1'bz;  // Controlled_Buffer controlled_buffer_11
  assign controlled_buffer_12_out = PWR ? D7 : 1'bz;  // Controlled_Buffer controlled_buffer_12
  D_Flip_Flop d_ff_5 (
    .clk(CLK), .D(controlled_buffer_9_out), .Q(d_ff_5_q), .en(PWR), .reset(not_6_out));  // open: Qn, preset
  not not_6 (not_6_out, nCLR);
  D_Flip_Flop d_ff_6 (
    .clk(CLK), .D(controlled_buffer_10_out), .Q(d_ff_6_q), .en(PWR), .reset(not_7_out));  // open: Qn, preset
  not not_7 (not_7_out, nCLR);
  D_Flip_Flop d_ff_7 (
    .clk(CLK), .D(controlled_buffer_11_out), .Q(d_ff_7_q), .en(PWR), .reset(not_8_out));  // open: Qn, preset
  not not_8 (not_8_out, nCLR);
  D_Flip_Flop d_ff_8 (
    .clk(CLK), .D(controlled_buffer_12_out), .Q(d_ff_8_q), .en(PWR), .reset(not_9_out));  // open: Qn, preset
  not not_9 (not_9_out, nCLR);
  assign Q4 = PWR ? d_ff_5_q : 1'bz;  // Controlled_Buffer controlled_buffer_13
  assign Q5 = PWR ? d_ff_6_q : 1'bz;  // Controlled_Buffer controlled_buffer_14
  assign Q6 = PWR ? d_ff_7_q : 1'bz;  // Controlled_Buffer controlled_buffer_15
  assign Q7 = PWR ? d_ff_8_q : 1'bz;  // Controlled_Buffer controlled_buffer_16
endmodule

module _74283 (
  input  VCC,
  input  GND,
  input  C0,
  input  A1,
  input  A2,
  input  A3,
  input  A4,
  input  B1,
  input  B2,
  input  B3,
  input  B4,
  output E1,
  output E2,
  output E3,
  output E4,
  output C4
);

  wire adder_1_cout, controlled_buffer_1_out, not_1_out, PWR;
  wire [3:0] adder_1_out, controlled_buffer_2_out, controlled_buffer_3_out;

  and and_1 (PWR, VCC, not_1_out);
  not not_1 (not_1_out, GND);
  assign controlled_buffer_1_out = PWR ? C0 : 1'bz;  // Controlled_Buffer controlled_buffer_1
  assign controlled_buffer_2_out = PWR ? {A4, A3, A2, A1} : 4'bz;  // Controlled_Buffer controlled_buffer_2
  assign controlled_buffer_3_out = PWR ? {B4, B3, B2, B1} : 4'bz;  // Controlled_Buffer controlled_buffer_3
  assign C4 = PWR ? adder_1_cout : 1'bz;  // Controlled_Buffer controlled_buffer_4
  Adder #(.width(4)) adder_1 (
    .a(controlled_buffer_2_out), .b(controlled_buffer_3_out), .out(adder_1_out),
    .cin(controlled_buffer_1_out), .cout(adder_1_cout));
  assign {E4, E3, E2, E1} = PWR ? adder_1_out : 4'bz;  // Controlled_Buffer controlled_buffer_5
endmodule

module _74189 (
  input  VCC,
  input  GND,
  input  D0,
  input  D1,
  input  D2,
  input  nWE,
  input  D3,
  input  A0,
  input  A1,
  input  A2,
  input  A3,
  input  nCE,
  output nQ0,
  output nQ1,
  output nQ2,
  output nQ3
);

  wire and_2_out, and_3_out, controlled_buffer_2_out, controlled_inverter_1_out, not_1_out, not_2_out, PWR;
  wire [3:0] controlled_buffer_1_out, controlled_buffer_3_out, controlled_buffer_4_out;

  and and_1 (PWR, VCC, not_1_out);
  not not_1 (not_1_out, GND);
  assign controlled_buffer_1_out = PWR ? {A3, A2, A1, A0} : 4'bz;  // Controlled_Buffer controlled_buffer_1
  assign controlled_buffer_2_out = PWR ? nWE : 1'bz;  // Controlled_Buffer controlled_buffer_2
  assign controlled_inverter_1_out = PWR ? ~nCE : 1'bz;  // Controlled_Inverter controlled_inverter_1
  not not_2 (not_2_out, nWE);
  and and_2 (and_2_out, not_2_out, PWR);
  assign controlled_buffer_3_out = and_2_out ? {D3, D2, D1, D0} : 4'bz;  // Controlled_Buffer controlled_buffer_3
  RAM #(.addrWidth(4), .dataWidth(4), .bus("asynch")) ram_1 (
    .addr(controlled_buffer_1_out), .data(controlled_buffer_3_out), .sel(controlled_inverter_1_out),
    .ld(controlled_buffer_2_out));  // open: clr
  assign controlled_buffer_4_out = and_3_out ? controlled_buffer_3_out : 4'bz;  // Controlled_Buffer controlled_buffer_4
  and and_3 (and_3_out, nWE, PWR);
  not not_3 (nQ0, controlled_buffer_4_out[0]);
  not not_4 (nQ1, controlled_buffer_4_out[1]);
  not not_5 (nQ2, controlled_buffer_4_out[2]);
  not not_6 (nQ3, controlled_buffer_4_out[3]);
endmodule

module _28C16 (
  input  VCC,
  input  GND,
  input  nWE,
  input  A0,
  input  A1,
  input  A2,
  input  A3,
  input  A4,
  input  A5,
  input  nOE,
  input  A6,
  input  nCE,
  input  A7,
  input  A8,
  input  A9,
  input  A10,
  output IO0,
  output IO1,
  output IO2,
  output IO3,
  output IO4,
  output IO5,
  output IO6,
  output IO7
);

  wire and_2_out, and_3_out, not_1_out, not_2_out, not_3_out, PWR;
  wire [7:0] rom_1_data;
  wire [10:0] controlled_buffer_1_out;

  and and_1 (PWR, VCC, not_1_out);
  not not_1 (not_1_out, GND);
  assign controlled_buffer_1_out = PWR ? {A10, A9, A8, A7, A6, A5, A4, A3, A2, A1, A0} : 11'bz;  // Controlled_Buffer controlled_buffer_1
  and and_2 (and_2_out, not_2_out, PWR);
  not not_2 (not_2_out, nCE);
  ROM #(.addrWidth(11)) rom_1 (.addr(controlled_buffer_1_out), .data(rom_1_data), .sel(and_2_out));
  assign {IO7, IO6, IO5, IO4, IO3, IO2, IO1, IO0} = and_3_out ? rom_1_data : 8'bz;  // Controlled_Buffer controlled_buffer_2
  and and_3 (and_3_out, not_3_out, PWR);
  not not_3 (not_3_out, nOE);
endmodule
