// Logisim project 7400-lib.circ as structural Verilog: 41 circuits, main circuit L_7400_1f1ca38e
// 7400
module L_7400_1f1ca38e (
  input  L_1_1A_14e525db,
  input  L_14_Vcc_b6e81b46,
  input  L_2_1B_6e949205,
  input  L_13_4B_c97254ab,
  input  L_12_4A_3e44c035,
  input  L_4_2A_18dde0be,
  input  L_5_2B_e40955d9,
  input  L_10_3B_18491fd5,
  input  L_9_3A_dd04c70b,
  input  L_7_GND_d4026f45,
  output L_3_1Y_9c6ef4a9,
  output L_11_4Y_23f02bf5,
  output L_6_2Y_287f65cc,
  output L_8_3Y_87559555
);

  nand nand_1 (L_3_1Y_9c6ef4a9, L_2_1B_6e949205, L_1_1A_14e525db);
  nand nand_2 (L_6_2Y_287f65cc, L_5_2B_e40955d9, L_4_2A_18dde0be);
  nand nand_3 (L_11_4Y_23f02bf5, L_13_4B_c97254ab, L_12_4A_3e44c035);
  nand nand_4 (L_8_3Y_87559555, L_10_3B_18491fd5, L_9_3A_dd04c70b);

  // Notes on the sheet:
  //   7400: quad NAND
endmodule

// 7402
module L_7402_6203944e (
  input  L_14_Vcc_b6e81b46,
  input  L_2_1A_17bdbafd,
  input  L_3_1B_1ed48573,
  input  L_12_4B_bdda3737,
  input  L_11_4A_ca8071da,
  input  L_5_2A_d3859b79,
  input  L_6_2B_8195364d,
  input  L_9_3B_232be9ea,
  input  L_7_GND_d4026f45,
  input  L_8_3A_b640dc94,
  output L_1_1Y_d39ecfa5,
  output L_13_4Y_15b721ba,
  output L_4_2Y_68966694,
  output L_10_3Y_9e576e78
);

  nor nor_1 (L_1_1Y_d39ecfa5, L_2_1A_17bdbafd, L_3_1B_1ed48573);
  nor nor_2 (L_4_2Y_68966694, L_5_2A_d3859b79, L_6_2B_8195364d);
  nor nor_3 (L_13_4Y_15b721ba, L_11_4A_ca8071da, L_12_4B_bdda3737);
  nor nor_4 (L_10_3Y_9e576e78, L_8_3A_b640dc94, L_9_3B_232be9ea);

  // Notes on the sheet:
  //   7402: quad NOR
endmodule

// 7404
module L_7404_64483892 (
  input  L_1_1A_14e525db,
  input  L_14_Vcc_b6e81b46,
  input  L_13_6A_694335e6,
  input  L_3_2A_ca98e641,
  input  L_11_5A_bd063c69,
  input  L_5_3A_a55f7d46,
  input  L_9_4A_aed1ffd2,
  input  L_7_GND_d4026f45,
  output L_2_1Y_2402a10b,
  output L_12_6Y_533153e7,
  output L_4_2Y_68966694,
  output L_10_5Y_106ec1d8,
  output L_6_3Y_27675488,
  output L_8_4Y_affcbff8
);

  not not_1 (L_2_1Y_2402a10b, L_1_1A_14e525db);
  not not_2 (L_4_2Y_68966694, L_3_2A_ca98e641);
  not not_3 (L_6_3Y_27675488, L_5_3A_a55f7d46);
  not not_4 (L_12_6Y_533153e7, L_13_6A_694335e6);
  not not_5 (L_10_5Y_106ec1d8, L_11_5A_bd063c69);
  not not_6 (L_8_4Y_affcbff8, L_9_4A_aed1ffd2);

  // Notes on the sheet:
  //   7407: hex inverter
endmodule

// 7407
module L_7407_070b58e2 (
  input  L_1_1A_14e525db,
  input  L_14_Vcc_b6e81b46,
  input  L_13_6A_694335e6,
  input  L_3_2A_ca98e641,
  input  L_11_5A_bd063c69,
  input  L_5_3A_a55f7d46,
  input  L_9_4A_aed1ffd2,
  input  L_7_GND_d4026f45,
  output L_2_1Y_2402a10b,
  output L_12_6Y_533153e7,
  output L_4_2Y_68966694,
  output L_10_5Y_106ec1d8,
  output L_6_3Y_27675488,
  output L_8_4Y_affcbff8
);

  buf buffer_1 (L_2_1Y_2402a10b, L_1_1A_14e525db);
  buf buffer_2 (L_4_2Y_68966694, L_3_2A_ca98e641);
  buf buffer_3 (L_6_3Y_27675488, L_5_3A_a55f7d46);
  buf buffer_4 (L_12_6Y_533153e7, L_13_6A_694335e6);
  buf buffer_5 (L_10_5Y_106ec1d8, L_11_5A_bd063c69);
  buf buffer_6 (L_8_4Y_affcbff8, L_9_4A_aed1ffd2);

  // Notes on the sheet:
  //   7407: hex buffer
endmodule

// 7408
module L_7408_a4c2b82c (
  input  L_1_1A_14e525db,
  input  L_14_Vcc_b6e81b46,
  input  L_2_1B_6e949205,
  input  L_13_4B_c97254ab,
  input  L_12_4A_3e44c035,
  input  L_4_2A_18dde0be,
  input  L_5_2B_e40955d9,
  input  L_10_3B_18491fd5,
  input  L_9_3A_dd04c70b,
  input  L_7_GND_d4026f45,
  output L_3_1Y_9c6ef4a9,
  output L_11_4Y_23f02bf5,
  output L_6_2Y_287f65cc,
  output L_8_3Y_87559555
);

  and and_1 (L_3_1Y_9c6ef4a9, L_2_1B_6e949205, L_1_1A_14e525db);
  and and_2 (L_6_2Y_287f65cc, L_5_2B_e40955d9, L_4_2A_18dde0be);
  and and_3 (L_11_4Y_23f02bf5, L_13_4B_c97254ab, L_12_4A_3e44c035);
  and and_4 (L_8_3Y_87559555, L_10_3B_18491fd5, L_9_3A_dd04c70b);

  // Notes on the sheet:
  //   7408: quad AND
endmodule

// 7410
module L_7410_d85e8957 (
  input  L_1_1A_14e525db,
  input  L_14_Vcc_b6e81b46,
  input  L_2_1B_6e949205,
  input  L_13_1C_dc87a617,
  input  L_3_2A_ca98e641,
  input  L_4_2B_ddad564f,
  input  L_11_3C_18c077aa,
  input  L_5_2C_ee07c05c,
  input  L_10_3B_18491fd5,
  input  L_9_3A_dd04c70b,
  input  L_7_GND_d4026f45,
  output L_12_1Y_850f9390,
  output L_6_2Y_287f65cc,
  output L_8_3Y_87559555
);

  nand nand_1 (L_6_2Y_287f65cc, L_5_2C_ee07c05c, L_4_2B_ddad564f, L_3_2A_ca98e641);
  nand nand_2 (L_12_1Y_850f9390, L_2_1B_6e949205, L_1_1A_14e525db, L_13_1C_dc87a617);
  nand nand_3 (L_8_3Y_87559555, L_11_3C_18c077aa, L_10_3B_18491fd5, L_9_3A_dd04c70b);

  // Notes on the sheet:
  //   7410: triple 3-input NAND 
endmodule

// 7411
module L_7411_968dc30f (
  input  L_1_1A_14e525db,
  input  L_14_Vcc_b6e81b46,
  input  L_2_1B_6e949205,
  input  L_13_1C_dc87a617,
  input  L_3_2A_ca98e641,
  input  L_4_2B_ddad564f,
  input  L_11_3C_18c077aa,
  input  L_5_2C_ee07c05c,
  input  L_10_3B_18491fd5,
  input  L_9_3A_dd04c70b,
  input  L_7_GND_d4026f45,
  output L_12_1Y_850f9390,
  output L_6_2Y_287f65cc,
  output L_8_3Y_87559555
);

  and and_1 (L_6_2Y_287f65cc, L_5_2C_ee07c05c, L_3_2A_ca98e641);
  and and_2 (L_12_1Y_850f9390, L_2_1B_6e949205, L_13_1C_dc87a617);
  and and_3 (L_8_3Y_87559555, L_11_3C_18c077aa, L_9_3A_dd04c70b);

  // Notes on the sheet:
  //   7411: triple 3-input AND 
endmodule

// 7420
module L_7420_69e7e47a (
  input  L_1_1A_14e525db,
  input  L_14_Vcc_b6e81b46,
  input  L_2_1B_6e949205,
  input  L_13_2D_cb7d826a,
  input  L_3_NC_5a18ab8e,
  input  L_12_2C_5782681d,
  input  L_4_1C_ee472e27,
  input  L_11_NC_7aced954,
  input  L_5_1D_a3e06dab,
  input  L_10_2B_4ef7271a,
  input  L_9_2A_ba945aa9,
  input  L_7_GND_d4026f45,
  output L_6_1Y_f45f5244,
  output L_8_2Y_0031f173
);

  nand nand_1 (L_6_1Y_f45f5244, L_5_1D_a3e06dab, L_4_1C_ee472e27, L_2_1B_6e949205, L_1_1A_14e525db);
  nand nand_2 (L_8_2Y_0031f173, L_13_2D_cb7d826a, L_12_2C_5782681d, L_10_2B_4ef7271a, L_9_2A_ba945aa9);

  // Notes on the sheet:
  //   7420: dual 4-input NAND
endmodule

// 7421
module L_7421_de1cece9 (
  input  L_1_1A_14e525db,
  input  L_14_Vcc_b6e81b46,
  input  L_2_1B_6e949205,
  input  L_13_2D_cb7d826a,
  input  L_3_NC_5a18ab8e,
  input  L_12_2C_5782681d,
  input  L_4_1C_ee472e27,
  input  L_11_NC_7aced954,
  input  L_5_1D_a3e06dab,
  input  L_10_2B_4ef7271a,
  input  L_9_2A_ba945aa9,
  input  L_7_GND_d4026f45,
  output L_6_1Y_f45f5244,
  output L_8_2Y_0031f173
);

  and and_1 (L_6_1Y_f45f5244, L_5_1D_a3e06dab, L_4_1C_ee472e27, L_2_1B_6e949205, L_1_1A_14e525db);
  and and_2 (L_8_2Y_0031f173, L_13_2D_cb7d826a, L_12_2C_5782681d, L_10_2B_4ef7271a, L_9_2A_ba945aa9);

  // Notes on the sheet:
  //   7421: dual 4-input AND
endmodule

// 7425
module L_7425_bd56b46e (
  input  L_1_1A_14e525db,
  input  L_14_Vcc_b6e81b46,
  input  L_2_1B_6e949205,
  input  L_13_2D_cb7d826a,
  input  L_3_NC_5a18ab8e,
  input  L_12_2C_5782681d,
  input  L_4_1C_ee472e27,
  input  L_11_NC_7aced954,
  input  L_5_1D_a3e06dab,
  input  L_10_2B_4ef7271a,
  input  L_9_2A_ba945aa9,
  input  L_7_GND_d4026f45,
  output L_6_1Y_f45f5244,
  output L_8_2Y_0031f173
);

  nor nor_1 (L_6_1Y_f45f5244, L_5_1D_a3e06dab, L_4_1C_ee472e27, L_2_1B_6e949205, L_1_1A_14e525db);
  nor nor_2 (L_8_2Y_0031f173, L_13_2D_cb7d826a, L_12_2C_5782681d, L_10_2B_4ef7271a, L_9_2A_ba945aa9);

  // Notes on the sheet:
  //   7425: dual 4-input NOR
endmodule

// 7427
module L_7427_34b8bb1f (
  input  L_1_1A_14e525db,
  input  L_14_Vcc_b6e81b46,
  input  L_2_1B_6e949205,
  input  L_13_1C_dc87a617,
  input  L_3_2A_ca98e641,
  input  L_4_2B_ddad564f,
  input  L_11_3C_18c077aa,
  input  L_5_2C_ee07c05c,
  input  L_10_3B_18491fd5,
  input  L_9_3A_dd04c70b,
  input  L_7_GND_d4026f45,
  output L_12_1Y_850f9390,
  output L_6_2Y_287f65cc,
  output L_8_3Y_87559555
);

  nor nor_1 (L_6_2Y_287f65cc, L_5_2C_ee07c05c, L_4_2B_ddad564f, L_3_2A_ca98e641);
  nor nor_2 (L_12_1Y_850f9390, L_2_1B_6e949205, L_1_1A_14e525db, L_13_1C_dc87a617);
  nor nor_3 (L_8_3Y_87559555, L_11_3C_18c077aa, L_10_3B_18491fd5, L_9_3A_dd04c70b);

  // Notes on the sheet:
  //   7427: triple 3-input NOR 
endmodule

// 7430
module L_7430_5e3633cc (
  input  L_1_1A_14e525db,
  input  L_14_Vcc_b6e81b46,
  input  L_2_1B_6e949205,
  input  L_13_NC_8db4142f,
  input  L_3_1C_f1d62a26,
  input  L_12_1H_e3c28cfb,
  input  L_4_1D_50b104ea,
  input  L_11_1G_155fba15,
  input  L_5_1E_d55646de,
  input  L_10_NC_43a6149a,
  input  L_6_1F_a1ac75d6,
  input  L_9_NC_5b334392,
  input  L_7_GND_d4026f45,
  output L_8_3Y_87559555
);

  nand nand_1 (L_8_3Y_87559555, L_6_1F_a1ac75d6, L_5_1E_d55646de, L_4_1D_50b104ea, L_3_1C_f1d62a26, L_2_1B_6e949205, L_1_1A_14e525db, L_12_1H_e3c28cfb, L_11_1G_155fba15);

  // Notes on the sheet:
  //   7430: 8-input NAND 
endmodule

// 7432
module L_7432_6e2e7e52 (
  input  L_1_1A_14e525db,
  input  L_14_Vcc_b6e81b46,
  input  L_2_1B_6e949205,
  input  L_13_4B_c97254ab,
  input  L_12_4A_3e44c035,
  input  L_4_2A_18dde0be,
  input  L_5_2B_e40955d9,
  input  L_10_3B_18491fd5,
  input  L_9_3A_dd04c70b,
  input  L_7_GND_d4026f45,
  output L_3_1Y_9c6ef4a9,
  output L_11_4Y_23f02bf5,
  output L_6_2Y_287f65cc,
  output L_8_3Y_87559555
);

  or or_1 (L_3_1Y_9c6ef4a9, L_2_1B_6e949205, L_1_1A_14e525db);
  or or_2 (L_6_2Y_287f65cc, L_5_2B_e40955d9, L_4_2A_18dde0be);
  or or_3 (L_11_4Y_23f02bf5, L_13_4B_c97254ab, L_12_4A_3e44c035);
  or or_4 (L_8_3Y_87559555, L_10_3B_18491fd5, L_9_3A_dd04c70b);

  // Notes on the sheet:
  //   7432: quad OR
endmodule

// 7448
module L_7448_376bda1e (
  input  L_1_B_b113a03f,
  input  L_16_Vcc_2c4a322e,
  input  L_2_C_22d60c57,
  input  L_3_LT_d06a3562,
  input  L_4_NC_c8eef7fe,
  input  L_5_RBI_66813b0b,
  input  L_6_D_14db2bfc,
  input  L_7_A_939fc430,
  input  L_8_GND_7238c13b,
  output L_15_f_8f17d194,
  output L_14_g_1f2896e0,
  output L_13_a_157640c9,
  output L_12_b_be8709f5,
  output L_11_c_d1464ccb,
  output L_10_d_464702f8,
  output L_9_e_12f9562e
);

  wire nand_1_out, nand_2_out, nand_3_out, nand_4_out, nand_5_out, nand_6_out, nand_7_out, nand_8_out,
       nand_9_out, nand_10_out, nand_11_out, nand_12_out, nand_13_out, nand_14_out, nand_15_out, nand_16_out,
       nand_17_out, nand_18_out, nand_19_out, nand_20_out, nand_21_out, nand_22_out, nand_23_out,
       nand_24_out, nand_25_out, not_1_out, not_2_out, not_3_out;

  nand nand_1 (nand_1_out, L_7_A_939fc430, L_3_LT_d06a3562);
  nand nand_2 (nand_2_out, L_1_B_b113a03f, L_3_LT_d06a3562);
  nand nand_3 (nand_3_out, L_2_C_22d60c57, L_3_LT_d06a3562);
  not not_1 (not_1_out, L_6_D_14db2bfc);
  not not_2 (not_2_out, L_5_RBI_66813b0b);
  nand nand_4 (nand_4_out, nand_1_out, nand_8_out);
  nand nand_5 (nand_5_out, nand_2_out, nand_8_out);
  nand nand_6 (nand_6_out, nand_3_out, nand_8_out);
  nand nand_7 (nand_7_out, not_1_out, nand_8_out);
  nand nand_8 (nand_8_out, L_3_LT_d06a3562, not_2_out, not_1_out, nand_3_out, nand_2_out, nand_1_out);
  nand nand_9 (nand_9_out, nand_5_out, nand_7_out);
  nand nand_10 (nand_10_out, nand_1_out, nand_6_out);
  nand nand_11 (nand_11_out, nand_4_out, nand_3_out);
  nand nand_12 (nand_12_out, nand_5_out, nand_7_out);
  nand nand_13 (nand_13_out, nand_4_out, nand_2_out, nand_6_out);
  nand nand_14 (nand_14_out, nand_1_out, nand_5_out, nand_6_out);
  nand nand_15 (nand_15_out, nand_6_out, nand_7_out);
  nand nand_16 (nand_16_out, nand_1_out, nand_5_out, nand_3_out);
  nand nand_17 (nand_17_out, nand_4_out, nand_2_out, nand_3_out);
  nand nand_18 (nand_18_out, nand_1_out, nand_2_out, nand_6_out);
  nand nand_19 (nand_19_out, nand_4_out, nand_5_out, nand_6_out);
  not not_3 (not_3_out, nand_4_out);
  nand nand_20 (nand_20_out, nand_2_out, nand_6_out);
  nand nand_21 (nand_21_out, nand_4_out, nand_5_out);
  nand nand_22 (nand_22_out, nand_5_out, nand_3_out);
  nand nand_23 (nand_23_out, nand_4_out, nand_3_out, not_1_out);
  nand nand_24 (nand_24_out, nand_4_out, nand_5_out, nand_6_out);
  nand nand_25 (nand_25_out, nand_2_out, not_1_out);
  and and_1 (L_13_a_157640c9, nand_9_out, nand_10_out, nand_11_out);
  and and_2 (L_12_b_be8709f5, nand_12_out, nand_13_out, nand_14_out);
  and and_3 (L_11_c_d1464ccb, nand_15_out, nand_16_out);
  and and_4 (L_10_d_464702f8, nand_17_out, nand_18_out, nand_19_out);
  and and_5 (L_9_e_12f9562e, not_3_out, nand_20_out);
  and and_6 (L_15_f_8f17d194, nand_21_out, nand_22_out, nand_23_out);
  and and_7 (L_14_g_1f2896e0, nand_24_out, nand_25_out);

  // Notes on the sheet:
  //   7448: BCD to 7-segment decoder
endmodule

// 7451
module L_7451_90511207 (
  input  L_1_1A_14e525db,
  input  L_14_Vcc_b6e81b46,
  input  L_2_2A_36ad2dea,
  input  L_13_1B_e338f40f,
  input  L_3_2B_94850d9e,
  input  L_12_NC_4463e4c0,
  input  L_4_2C_c65fba20,
  input  L_11_NC_7aced954,
  input  L_5_2D_cb9d2bf4,
  input  L_10_1D_30be0351,
  input  L_9_1C_b8364dba,
  input  L_7_GND_d4026f45,
  output L_6_2Y_287f65cc,
  output L_8_1Y_e48566bd
);

  wire and_1_out, and_2_out, and_3_out, and_4_out;

  nor nor_1 (L_8_1Y_e48566bd, and_3_out, and_4_out);
  and and_1 (and_1_out, L_2_2A_36ad2dea, L_3_2B_94850d9e);
  and and_2 (and_2_out, L_4_2C_c65fba20, L_5_2D_cb9d2bf4);
  and and_3 (and_3_out, L_1_1A_14e525db, L_13_1B_e338f40f);
  and and_4 (and_4_out, L_10_1D_30be0351, L_9_1C_b8364dba);
  nor nor_2 (L_6_2Y_287f65cc, and_2_out, and_1_out);

  // Notes on the sheet:
  //   7451: dual 2-wide 2-input AND-OR-Invert gate
endmodule

// 7474
module L_7474_40de9376 (
  input  L_1_CLR1_48669d3d,
  input  L_14_Vcc_b6e81b46,
  input  L_2_D1_92dccd0d,
  input  L_13_CLR2_eba526e9,
  input  L_3_CLK1_4301d347,
  input  L_12_D2_2ce35a2a,
  input  L_4_PR1_03c2248c,
  input  L_11_CLK2_2e4c0e32,
  input  L_10_PR2_c894c123,
  input  L_7_GND_d4026f45,
  output L_5_Q1_03cecf36,
  output L_6_Q1_7e4316a3,
  output L_9_Q2_4f87d294,
  output L_8_Q2_983d7aa7
);

  D_Flip_Flop d_ff_1 (
    .clk(L_3_CLK1_4301d347), .D(L_2_D1_92dccd0d), .Q(L_5_Q1_03cecf36), .Qn(L_6_Q1_7e4316a3),
    .preset(L_4_PR1_03c2248c), .reset(L_1_CLR1_48669d3d));
  D_Flip_Flop d_ff_2 (
    .clk(L_11_CLK2_2e4c0e32), .D(L_12_D2_2ce35a2a), .Q(L_9_Q2_4f87d294), .Qn(L_8_Q2_983d7aa7),
    .preset(L_10_PR2_c894c123), .reset(L_13_CLR2_eba526e9));

  // Notes on the sheet:
  //   7474: dual D-type flip flop
endmodule

// 7476
module L_7476_563af610 (
  input  L_1_CLK1_ed4f6026,
  input  L_16_K1_109edc98,
  input  L_2_PR1_8987f957,
  input  L_3_CLR1_05d4b833,
  input  L_4_J1_46c2d317,
  input  L_13_GND_e0c1210c,
  input  L_5_VCC_e04b933a,
  input  L_12_K2_e9731bb0,
  input  L_6_CLK2_55d903a1,
  input  L_7_PR2_2d83aec3,
  input  L_8_CLR2_940a8405,
  input  L_9_J2_30b4de90,
  output L_15_Q1_9b115fc9,
  output L_14_Q1_57d2f338,
  output L_11_Q2_79736b31,
  output L_10_Q2_ffa4bcf6
);

  J_K_Flip_Flop j_k_ff_1 (
    .J(L_4_J1_46c2d317), .clk(L_1_CLK1_ed4f6026), .K(L_16_K1_109edc98), .Q(L_15_Q1_9b115fc9),
    .Qn(L_14_Q1_57d2f338), .preset(L_2_PR1_8987f957), .reset(L_3_CLR1_05d4b833));
  J_K_Flip_Flop j_k_ff_2 (
    .J(L_9_J2_30b4de90), .clk(L_6_CLK2_55d903a1), .K(L_12_K2_e9731bb0), .Q(L_11_Q2_79736b31),
    .Qn(L_10_Q2_ffa4bcf6), .preset(L_7_PR2_2d83aec3), .reset(L_8_CLR2_940a8405));

  // Notes on the sheet:
  //   7476: dual JK-type flip flop
endmodule

// 7483
module L_7483_b0b8294f (
  input  L_1_A4_416a3137,
  input  L_16_B4_bb775e11,
  input  L_3_A3_607a1031,
  input  L_14_Cout_13a33020,
  input  L_4_B3_602b513c,
  input  L_13_Cin_2447466a,
  input  L_5_Vcc_1802d2fc,
  input  L_12_GND_92cafb02,
  input  L_11_B1_1163dc2d,
  input  L_7_B2_9afdf295,
  input  L_10_A1_c62c00e2,
  input  L_8_A2_fcded6d2,
  output L_2_S3_2153c1f9,
  output L_15_S4_67d57a46,
  output L_6_S2_137055bb,
  output L_9_S1_04ac758a
);

  wire and_1_out, and_2_out, and_3_out, and_4_out, and_5_out, and_6_out, and_7_out, and_8_out, and_9_out,
       and_10_out, and_11_out, and_12_out, and_13_out, and_14_out, nand_1_out, nand_2_out, nand_3_out,
       nand_4_out, nor_1_out, nor_2_out, nor_3_out, nor_4_out, nor_6_out, nor_7_out, nor_8_out, not_1_out,
       not_2_out, not_3_out, not_4_out, not_5_out, not_6_out;

  nand nand_1 (nand_1_out, L_16_B4_bb775e11, L_1_A4_416a3137);
  nor nor_1 (nor_1_out, L_16_B4_bb775e11, L_1_A4_416a3137);
  nand nand_2 (nand_2_out, L_4_B3_602b513c, L_3_A3_607a1031);
  nor nor_2 (nor_2_out, L_4_B3_602b513c, L_3_A3_607a1031);
  nand nand_3 (nand_3_out, L_7_B2_9afdf295, L_8_A2_fcded6d2);
  nor nor_3 (nor_3_out, L_7_B2_9afdf295, L_8_A2_fcded6d2);
  nand nand_4 (nand_4_out, L_11_B1_1163dc2d, L_10_A1_c62c00e2);
  nor nor_4 (nor_4_out, L_11_B1_1163dc2d, L_10_A1_c62c00e2);
  and and_1 (and_1_out, nor_2_out, nand_1_out);
  and and_2 (and_2_out, nor_3_out, nand_1_out, nand_2_out);
  and and_3 (and_3_out, nor_4_out, nand_2_out);
  and and_4 (and_4_out, nand_2_out, nand_4_out);
  not not_1 (not_1_out, nor_1_out);
  and and_5 (and_5_out, nor_3_out, nand_2_out);
  and and_6 (and_6_out, nor_4_out, nand_2_out, nand_3_out);
  and and_7 (and_7_out, nand_2_out, nand_4_out);
  not not_2 (not_2_out, L_13_Cin_2447466a);
  not not_3 (not_3_out, nor_2_out);
  and and_8 (and_8_out, nor_4_out, nand_3_out);
  and and_9 (and_9_out, nand_3_out, nand_4_out, not_2_out);
  not not_4 (not_4_out, nor_3_out);
  and and_10 (and_10_out, nand_4_out, not_2_out);
  not not_5 (not_5_out, nor_4_out);
  not not_6 (not_6_out, not_2_out);
  nor nor_5 (L_14_Cout_13a33020, and_1_out, and_3_out);
  and and_11 (and_11_out, nand_1_out, not_1_out);
  and and_12 (and_12_out, nand_2_out, not_3_out);
  and and_13 (and_13_out, nand_3_out, not_4_out);
  and and_14 (and_14_out, nand_4_out, not_5_out);
  xor xor_1 (L_15_S4_67d57a46, and_11_out, nor_6_out);
  not nor_6 (nor_6_out, and_5_out);  // NOR_Gate
  xor xor_2 (L_2_S3_2153c1f9, and_12_out, nor_7_out);
  nor nor_7 (nor_7_out, nor_3_out, and_8_out, and_9_out);
  xor xor_3 (L_6_S2_137055bb, and_13_out, nor_8_out);
  nor nor_8 (nor_8_out, nor_4_out, and_10_out);
  xor xor_4 (L_9_S1_04ac758a, and_14_out, not_6_out);

  // Notes on the sheet:
  //   7483: 4-bit full adder
endmodule

// 7486
module L_7486_0847b3db (
  input  L_1_1A_14e525db,
  input  L_14_Vcc_b6e81b46,
  input  L_2_1B_6e949205,
  input  L_13_4B_c97254ab,
  input  L_12_4A_3e44c035,
  input  L_4_2A_18dde0be,
  input  L_5_2B_e40955d9,
  input  L_10_3B_18491fd5,
  input  L_9_3A_dd04c70b,
  input  L_7_GND_d4026f45,
  output L_3_1Y_9c6ef4a9,
  output L_11_4Y_23f02bf5,
  output L_6_2Y_287f65cc,
  output L_8_3Y_87559555
);

  xor xor_1 (L_3_1Y_9c6ef4a9, L_2_1B_6e949205, L_1_1A_14e525db);
  xor xor_2 (L_6_2Y_287f65cc, L_5_2B_e40955d9, L_4_2A_18dde0be);
  xor xor_3 (L_11_4Y_23f02bf5, L_13_4B_c97254ab, L_12_4A_3e44c035);
  xor xor_4 (L_8_3Y_87559555, L_10_3B_18491fd5, L_9_3A_dd04c70b);

  // Notes on the sheet:
  //   7486: quad XOR
endmodule

// 7489
module L_7489_8a49301a (
  input  L_1_A0_1d1e702a,
  input  L_16_Vcc_2c4a322e,
  input  L_2_CS_f67c7ca6,
  input  L_15_A1_6022b7bf,
  input  L_3_WE_2f557b5c,
  input  L_14_A2_8198c591,
  input  L_4_D1_09909867,
  input  L_13_A3_7b49f8f8,
  input  L_12_D4_d7bc7bf8,
  input  L_6_D2_b10a357d,
  input  L_10_D3_d8bb6690,
  input  L_8_GND_7238c13b,
  output L_5_O1_d4feaddd,
  output L_11_O4_4eac863b,
  output L_7_O2_e834e3a3,
  output L_9_O3_28f00aac
);

  wire not_1_out, not_2_out, or_1_out;
  wire [3:0] ram_1_data;

  not not_1 (not_1_out, L_2_CS_f67c7ca6);
  not not_2 (not_2_out, L_3_WE_2f557b5c);
  or or_1 (or_1_out, not_2_out, not_1_out);
  RAM #(.addrWidth(4), .dataWidth(4)) ram_1 (
    .addr({L_13_A3_7b49f8f8, L_14_A2_8198c591, L_15_A1_6022b7bf, L_1_A0_1d1e702a}), .data(ram_1_data),
    .sel(not_1_out), .clk(not_2_out), .ld(or_1_out));  // open: clr
  assign {L_11_O4_4eac863b, L_9_O3_28f00aac, L_7_O2_e834e3a3, L_5_O1_d4feaddd} = ~ram_1_data;  // NOT_Gate not_3, 4 bits wide

  // Notes on the sheet:
  //   7489: 64-bit RAM
endmodule

// 74116
module L_74116_4729d6f8 (
  input  L_1_MRa_edff1c3a,
  input  L_24_Vcc_efe97306,
  input  L_2_E0a_01e2d2a5,
  input  L_3_E1a_3c8f5095,
  input  L_22_D3b_bb4c7de5,
  input  L_4_D0a_bda68a14,
  input  L_20_D2b_9b534520,
  input  L_6_D1a_cac9a4ac,
  input  L_18_D1b_6217dc06,
  input  L_8_D2a_82d71d4d,
  input  L_16_D0b_02b4b886,
  input  L_10_D3a_caf206e2,
  input  L_15_E1b_5d0e0481,
  input  L_14_E0b_efc1e34f,
  input  L_12_GND_92cafb02,
  input  L_13_MRb_b0d6d140,
  output L_23_Q3b_78223f84,
  output L_21_Q2b_a580262f,
  output L_5_Q0a_ce0f4691,
  output L_19_Q1b_ff71d202,
  output L_7_Q1a_cb160767,
  output L_17_Q0b_1110e2c1,
  output L_9_Q2a_f44d964f,
  output L_11_Q3a_4852f627
);

  wire and_1_out, and_2_out, not_2_out;

  not not_1 (L_5_Q0a_ce0f4691, L_1_MRa_edff1c3a);
  and and_1 (and_1_out, ~L_2_E0a_01e2d2a5, ~L_3_E1a_3c8f5095);  // AND_Gate
  D_Flip_Flop #(.trigger("high")) d_ff_1 (
    .clk(L_5_Q0a_ce0f4691), .preset(L_5_Q0a_ce0f4691), .reset(L_5_Q0a_ce0f4691));  // open: D, Q, Qn
  D_Flip_Flop #(.trigger("high")) d_ff_2 (
    .clk(L_5_Q0a_ce0f4691), .preset(L_5_Q0a_ce0f4691), .reset(L_5_Q0a_ce0f4691));  // open: D, Q, Qn
  D_Flip_Flop #(.trigger("high")) d_ff_3 (
    .clk(L_5_Q0a_ce0f4691), .preset(L_5_Q0a_ce0f4691), .reset(L_5_Q0a_ce0f4691));  // open: D, Q, Qn
  D_Flip_Flop #(.trigger("high")) d_ff_4 (.clk(L_5_Q0a_ce0f4691), .preset(L_5_Q0a_ce0f4691));  // open: D, Q, Qn, reset
  D_Flip_Flop #(.trigger("high")) d_ff_5 (.clk(not_2_out), .preset(L_23_Q3b_78223f84));  // open: D, Q, Qn, reset
  D_Flip_Flop #(.trigger("high")) d_ff_6 (.clk(not_2_out), .preset(L_21_Q2b_a580262f));  // open: D, Q, Qn, reset
  D_Flip_Flop #(.trigger("high")) d_ff_7 (.clk(not_2_out), .preset(L_19_Q1b_ff71d202));  // open: D, Q, Qn, reset
  D_Flip_Flop #(.trigger("high")) d_ff_8 (.clk(not_2_out), .preset(L_17_Q0b_1110e2c1));  // open: D, Q, Qn, reset
  and and_2 (and_2_out, ~L_15_E1b_5d0e0481, ~L_14_E0b_efc1e34f);  // AND_Gate
  not not_2 (not_2_out, L_13_MRb_b0d6d140);

  assign L_7_Q1a_cb160767 = L_5_Q0a_ce0f4691;
  assign L_9_Q2a_f44d964f = L_5_Q0a_ce0f4691;
  assign L_11_Q3a_4852f627 = L_5_Q0a_ce0f4691;

  // Notes on the sheet:
  //   74116: dual 4-bit latches
endmodule

// 74133
module L_74133_b6679575 (
  input  L_1_A_ce3ff1c6,
  input  L_16_Vcc_2c4a322e,
  input  L_2_B_787e0352,
  input  L_15_M_adc3a9bc,
  input  L_3_C_943bc0c4,
  input  L_14_L_28800d7e,
  input  L_4_D_226206a4,
  input  L_13_K_582869aa,
  input  L_5_E_22d8a557,
  input  L_12_J_cb13f3b9,
  input  L_6_F_ee3ae8b4,
  input  L_11_I_d1ded807,
  input  L_7_G_c22fca1a,
  input  L_10_H_4ea1c3aa,
  input  L_8_GND_7238c13b,
  output L_9_Y_02f723b8
);

  nand nand_1 (L_9_Y_02f723b8, L_7_G_c22fca1a, L_6_F_ee3ae8b4, L_5_E_22d8a557, L_4_D_226206a4, L_3_C_943bc0c4, L_2_B_787e0352, L_1_A_ce3ff1c6, L_15_M_adc3a9bc, L_14_L_28800d7e, L_13_K_582869aa, L_12_J_cb13f3b9, L_11_I_d1ded807, L_10_H_4ea1c3aa);

  // Notes on the sheet:
  //   74133: 13-input NAND
endmodule

// 74138
module L_74138_fe370a68 (
  input  L_1_A_ce3ff1c6,
  input  L_16_Vcc_2c4a322e,
  input  L_2_B_787e0352,
  input  L_3_C_943bc0c4,
  input  L_4_G2A_e8162ae2,
  input  L_5_G2B_f6417b2a,
  input  L_6_G1_cbc736e8,
  input  L_8_GND_7238c13b,
  output L_15_Y0_22f2d3da,
  output L_14_Y1_66300113,
  output L_13_Y2_bf3aae29,
  output L_12_Y3_60b3d81a,
  output L_11_Y4_e187eac2,
  output L_7_Y7_80811157,
  output L_10_Y5_a083d511,
  output L_9_Y6_ccf28fb3
);

  wire and_1_out, and_2_out, and_3_out, and_4_out, and_5_out, and_6_out, and_7_out, and_8_out, and_9_out,
       decoder_1_out0, decoder_1_out1, decoder_1_out2, decoder_1_out3, decoder_1_out4, decoder_1_out5,
       decoder_1_out6, decoder_1_out7, not_1_out, not_2_out;

  not not_1 (not_1_out, L_4_G2A_e8162ae2);
  not not_2 (not_2_out, L_5_G2B_f6417b2a);
  and and_1 (and_1_out, and_2_out, decoder_1_out7);
  not not_3 (L_7_Y7_80811157, and_1_out);
  and and_2 (and_2_out, not_1_out, not_2_out, L_6_G1_cbc736e8);
  Decoder #(.enable("false"), .select(3)) decoder_1 (
    .out0(decoder_1_out0), .out1(decoder_1_out1), .out2(decoder_1_out2), .out3(decoder_1_out3),
    .out4(decoder_1_out4), .out5(decoder_1_out5), .out6(decoder_1_out6), .out7(decoder_1_out7),
    .sel({L_3_C_943bc0c4, L_2_B_787e0352, L_1_A_ce3ff1c6}));
  and and_3 (and_3_out, and_2_out, decoder_1_out0);
  not not_4 (L_15_Y0_22f2d3da, and_3_out);
  and and_4 (and_4_out, and_2_out, decoder_1_out1);
  not not_5 (L_14_Y1_66300113, and_4_out);
  and and_5 (and_5_out, and_2_out, decoder_1_out2);
  not not_6 (L_13_Y2_bf3aae29, and_5_out);
  and and_6 (and_6_out, and_2_out, decoder_1_out3);
  not not_7 (L_12_Y3_60b3d81a, and_6_out);
  and and_7 (and_7_out, and_2_out, decoder_1_out4);
  not not_8 (L_11_Y4_e187eac2, and_7_out);
  and and_8 (and_8_out, and_2_out, decoder_1_out5);
  not not_9 (L_10_Y5_a083d511, and_8_out);
  and and_9 (and_9_out, and_2_out, decoder_1_out6);
  not not_10 (L_9_Y6_ccf28fb3, and_9_out);

  // Notes on the sheet:
  //   74138: 3-Line to 8-Line Decoder
endmodule

// 74139
module L_74139_2bbf2a0e (
  input  L_1_1G_e7be49a9,
  input  L_16_Vcc_2c4a322e,
  input  L_2_1A_17bdbafd,
  input  L_15_2G_7ba95554,
  input  L_3_1B_1ed48573,
  input  L_14_2A_d426e4e6,
  input  L_13_2B_32045bd4,
  input  L_8_GND_7238c13b,
  output L_4_1Y0_7510e46f,
  output L_5_1Y1_4414c212,
  output L_12_2Y0_6e2f9367,
  output L_6_1Y2_3fbc9f2b,
  output L_11_2Y1_65a2f84d,
  output L_7_1Y3_fae66b0f,
  output L_10_2Y2_e0facbf5,
  output L_9_2Y3_6908b714
);

  wire decoder_1_out0, decoder_1_out1, decoder_1_out2, decoder_1_out3, decoder_2_out0, decoder_2_out1,
       decoder_2_out2, decoder_2_out3, not_1_out, not_2_out, not_3_out, not_4_out, not_5_out, not_6_out,
       not_7_out, not_8_out, not_9_out, not_10_out;

  not not_1 (not_1_out, L_1_1G_e7be49a9);
  and and_1 (L_4_1Y0_7510e46f, not_1_out, not_2_out);
  not not_2 (not_2_out, decoder_1_out0);
  and and_2 (L_5_1Y1_4414c212, not_1_out, not_3_out);
  not not_3 (not_3_out, decoder_1_out1);
  and and_3 (L_6_1Y2_3fbc9f2b, not_1_out, not_4_out);
  not not_4 (not_4_out, decoder_1_out2);
  and and_4 (L_7_1Y3_fae66b0f, not_1_out, not_5_out);
  not not_5 (not_5_out, decoder_1_out3);
  Decoder #(.enable("false"), .select(2)) decoder_1 (
    .out0(decoder_1_out0), .out1(decoder_1_out1), .out2(decoder_1_out2), .out3(decoder_1_out3),
    .sel({L_3_1B_1ed48573, L_2_1A_17bdbafd}));
  Decoder #(.enable("false"), .select(2)) decoder_2 (
    .out0(decoder_2_out0), .out1(decoder_2_out1), .out2(decoder_2_out2), .out3(decoder_2_out3),
    .sel({L_13_2B_32045bd4, L_14_2A_d426e4e6}));
  not not_6 (not_6_out, L_15_2G_7ba95554);
  not not_7 (not_7_out, decoder_2_out0);
  not not_8 (not_8_out, decoder_2_out1);
  not not_9 (not_9_out, decoder_2_out2);
  not not_10 (not_10_out, decoder_2_out3);
  and and_5 (L_12_2Y0_6e2f9367, not_6_out, not_7_out);
  and and_6 (L_11_2Y1_65a2f84d, not_6_out, not_8_out);
  and and_7 (L_10_2Y2_e0facbf5, not_6_out, not_9_out);
  and and_8 (L_9_2Y3_6908b714, not_6_out, not_10_out);

  // Notes on the sheet:
  //   74139: Dual 2-Line to 4-Line Decoder
endmodule

// 74147
module L_74147_f859a647 (
  input  L_1_I4_8804ad76,
  input  L_16_Vcc_2c4a322e,
  input  L_2_I5_497e3a28,
  input  L_15_NC_b1fb3b53,
  input  L_3_I6_9847c3ec,
  input  L_4_I7_7f94cefc,
  input  L_13_I3_d756c63c,
  input  L_5_I8_afb037c5,
  input  L_12_I2_162e87a6,
  input  L_11_I1_bbe09f98,
  input  L_10_I9_b807cc75,
  input  L_8_GND_7238c13b,
  output L_14_A3_83f077f8,
  output L_6_A2_e9017930,
  output L_7_A1_dbd5ffee,
  output L_9_A0_f992e408
);

  Priority_Encoder #(.select(4)) priority_encoder_1 (
    .in0(L_11_I1_bbe09f98), .in1(L_12_I2_162e87a6), .in2(L_13_I3_d756c63c), .in3(L_1_I4_8804ad76),
    .in4(L_2_I5_497e3a28), .in5(L_3_I6_9847c3ec), .in6(L_4_I7_7f94cefc), .in7(L_5_I8_afb037c5),
    .in8(L_10_I9_b807cc75), .out({L_14_A3_83f077f8, L_6_A2_e9017930, L_7_A1_dbd5ffee, L_9_A0_f992e408}));  // open: in9, in10, in11, in12, in13, in14, in15, gs, en_out, en_in

  // Notes on the sheet:
  //   74147: 9-Line to 4-Line Priority Encoder
endmodule

// 74148
module L_74148_2633e4af (
  input  L_1_I4_8804ad76,
  input  L_16_Vcc_2c4a322e,
  input  L_2_I5_497e3a28,
  input  L_15_EO_NC_fcd7d0a0,
  input  L_3_I6_9847c3ec,
  input  L_14_GS_NC_7e3d2c03,
  input  L_4_I7_7f94cefc,
  input  L_13_I3_d756c63c,
  input  L_5_EI_NC_cc889428,
  input  L_12_I2_162e87a6,
  input  L_6_A2_e9017930,
  input  L_11_I1_bbe09f98,
  input  L_7_A1_dbd5ffee,
  input  L_10_I0_4556816a,
  input  L_8_GND_7238c13b,
  input  L_9_A0_f992e408
);

  Priority_Encoder priority_encoder_1 (
    .in0(L_10_I0_4556816a), .in1(L_11_I1_bbe09f98), .in2(L_12_I2_162e87a6), .in3(L_13_I3_d756c63c),
    .in4(L_1_I4_8804ad76), .in5(L_2_I5_497e3a28), .in6(L_3_I6_9847c3ec), .in7(L_4_I7_7f94cefc),
    .out({L_7_A1_dbd5ffee, L_6_A2_e9017930, L_9_A0_f992e408}));  // open: en_in, gs, en_out

  // Notes on the sheet:
  //   74148: 9-Line to 4-Line Priority Encoder
  //   NOTE: Pins 5, 14, and 15 have connections normally, but I chose not to model them
endmodule

// 74150
module L_74150_8a390209 (
  input  L_1_E7_783aaa0d,
  input  L_24_Vcc_efe97306,
  input  L_2_E6_a1152608,
  input  L_23_E8_a97586c1,
  input  L_3_E5_d9303efe,
  input  L_22_E9_061a626a,
  input  L_4_E4_06911f3a,
  input  L_21_E10_940b65f3,
  input  L_5_E3_d1093fa0,
  input  L_20_E11_02ba0633,
  input  L_6_E2_a4f51a14,
  input  L_19_E12_e95a11b5,
  input  L_7_E1_c2edec87,
  input  L_18_E13_2a5643a3,
  input  L_8_E0_9ce19829,
  input  L_17_E14_8c3fb364,
  input  L_9_G_4d05c847,
  input  L_16_E15_0bd5ff7d,
  input  L_15_A_8ca36977,
  input  L_11_D_6e064de5,
  input  L_14_B_5c45bd9c,
  input  L_12_GND_92cafb02,
  input  L_13_C_4dc04003,
  output L_10_W_0152b53d
);

  wire multiplexer_1_out, not_1_out;

  or or_1 (L_10_W_0152b53d, L_9_G_4d05c847, not_1_out);
  not not_1 (not_1_out, multiplexer_1_out);
  Multiplexer #(.select(4)) multiplexer_1 (
    .in0(L_8_E0_9ce19829), .in1(L_7_E1_c2edec87), .in2(L_6_E2_a4f51a14), .in3(L_5_E3_d1093fa0),
    .in4(L_4_E4_06911f3a), .in5(L_3_E5_d9303efe), .in6(L_2_E6_a1152608), .in7(L_1_E7_783aaa0d),
    .in8(L_23_E8_a97586c1), .in9(L_22_E9_061a626a), .in10(L_21_E10_940b65f3), .in11(L_20_E11_02ba0633),
    .in12(L_19_E12_e95a11b5), .in13(L_18_E13_2a5643a3), .in14(L_17_E14_8c3fb364), .in15(L_16_E15_0bd5ff7d),
    .out(multiplexer_1_out), .sel({L_11_D_6e064de5, L_13_C_4dc04003, L_14_B_5c45bd9c, L_15_A_8ca36977}));

  // Notes on the sheet:
  //   74150: 16-Line to 1-Line Multiplexer
endmodule

// 74151
module L_74151_d232e329 (
  input  L_1_D3_cc9ed74b,
  input  L_16_Vcc_2c4a322e,
  input  L_2_D2_bab4bb10,
  input  L_15_D4_8275e74b,
  input  L_3_D1_eb5144f4,
  input  L_14_D5_53112324,
  input  L_4_D0_176ffcea,
  input  L_13_D6_442a4922,
  input  L_12_D7_3ebce941,
  input  L_11_A_96ffb7e5,
  input  L_7_G_2421d088,
  input  L_10_B_265116c1,
  input  L_8_GND_7238c13b,
  input  L_9_C_7fb14356,
  output L_5_Y_df4e2f6c,
  output L_6_W_4061abdd
);

  wire multiplexer_1_out, not_2_out;

  not not_1 (L_5_Y_df4e2f6c, L_6_W_4061abdd);
  or or_1 (L_6_W_4061abdd, not_2_out, L_7_G_2421d088);
  not not_2 (not_2_out, multiplexer_1_out);
  Multiplexer #(.select(3)) multiplexer_1 (
    .in0(L_4_D0_176ffcea), .in1(L_3_D1_eb5144f4), .in2(L_2_D2_bab4bb10), .in3(L_1_D3_cc9ed74b),
    .in4(L_15_D4_8275e74b), .in5(L_14_D5_53112324), .in6(L_13_D6_442a4922), .in7(L_12_D7_3ebce941),
    .out(multiplexer_1_out), .sel({L_9_C_7fb14356, L_10_B_265116c1, L_11_A_96ffb7e5}));

  // Notes on the sheet:
  //   74151: 8-Line to 1-Line Multiplexer
endmodule

// 74153
module L_74153_967ef5bb (
  input  L_1_G1_d320191e,
  input  L_16_Vcc_2c4a322e,
  input  L_2_B_787e0352,
  input  L_15_G2_8c568f83,
  input  L_3_1C3_3688884c,
  input  L_14_A_f3dc9f8c,
  input  L_4_1C2_9e963928,
  input  L_13_2C3_ede6f057,
  input  L_5_1C1_57a80b8e,
  input  L_12_2C2_81752be0,
  input  L_6_1C0_8ece1da3,
  input  L_11_2C1_73cefb20,
  input  L_10_2C0_db306049,
  input  L_8_GND_7238c13b,
  output L_7_Y1_d2ec90fb,
  output L_9_Y2_bfd2ca5b
);

  wire multiplexer_1_out, multiplexer_2_out, not_1_out, not_2_out;

  not not_1 (not_1_out, L_1_G1_d320191e);
  Multiplexer #(.select(2)) multiplexer_1 (
    .in0(L_6_1C0_8ece1da3), .in1(L_5_1C1_57a80b8e), .in2(L_4_1C2_9e963928), .in3(L_3_1C3_3688884c),
    .out(multiplexer_1_out), .sel({L_2_B_787e0352, L_14_A_f3dc9f8c}));
  and and_1 (L_7_Y1_d2ec90fb, multiplexer_1_out, not_1_out);
  not not_2 (not_2_out, L_15_G2_8c568f83);
  Multiplexer #(.select(2)) multiplexer_2 (
    .in0(L_10_2C0_db306049), .in1(L_11_2C1_73cefb20), .in2(L_12_2C2_81752be0), .in3(L_13_2C3_ede6f057),
    .out(multiplexer_2_out), .sel({L_2_B_787e0352, L_14_A_f3dc9f8c}));
  and and_2 (L_9_Y2_bfd2ca5b, multiplexer_2_out, not_2_out);

  // Notes on the sheet:
  //   74153: Dual 4-Line to 1-Line Multiplexer
endmodule

// 74154
module L_74154_ca0be00a (
  input  L_24_Vcc_efe97306,
  input  L_23_A_d20b84ac,
  input  L_22_B_35caca1a,
  input  L_21_C_a4808d66,
  input  L_20_D_c5e011af,
  input  L_19_G2_0092f278,
  input  L_18_G1_8e2783d5,
  input  L_12_GND_92cafb02,
  output L_1_Y0_86047643,
  output L_2_Y1_82c1943a,
  output L_3_Y2_e30d174b,
  output L_4_Y3_950daddb,
  output L_5_Y4_106702f0,
  output L_6_Y5_4524a04c,
  output L_7_Y6_5c4eca50,
  output L_8_Y7_5d798d3e,
  output L_17_Y15_7952b3fc,
  output L_9_Y8_0f54a762,
  output L_16_Y14_787c8a53,
  output L_10_Y9_8a1abaab,
  output L_15_Y13_fecf5aed,
  output L_11_Y10_93957c82,
  output L_14_Y12_cabf0cae,
  output L_13_Y11_5b38353b
);

  wire and_12_out, decoder_1_out0, decoder_1_out1, decoder_1_out2, decoder_1_out3, decoder_1_out4,
       decoder_1_out5, decoder_1_out6, decoder_1_out7, decoder_1_out8, decoder_1_out9, decoder_1_out10,
       decoder_1_out11, decoder_1_out12, decoder_1_out13, decoder_1_out14, decoder_1_out15, not_1_out,
       not_2_out, not_3_out, not_4_out, not_5_out, not_6_out, not_7_out, not_8_out, not_9_out, not_10_out,
       not_11_out, not_12_out, not_13_out, not_14_out, not_15_out, not_16_out, not_17_out, not_18_out;

  not not_1 (not_1_out, decoder_1_out0);
  and and_1 (L_1_Y0_86047643, not_1_out, and_12_out);
  not not_2 (not_2_out, decoder_1_out1);
  and and_2 (L_2_Y1_82c1943a, not_2_out, and_12_out);
  not not_3 (not_3_out, decoder_1_out2);
  and and_3 (L_3_Y2_e30d174b, not_3_out, and_12_out);
  not not_4 (not_4_out, decoder_1_out3);
  and and_4 (L_4_Y3_950daddb, not_4_out, and_12_out);
  not not_5 (not_5_out, decoder_1_out4);
  and and_5 (L_5_Y4_106702f0, not_5_out, and_12_out);
  not not_6 (not_6_out, decoder_1_out5);
  and and_6 (L_6_Y5_4524a04c, not_6_out, and_12_out);
  not not_7 (not_7_out, decoder_1_out6);
  and and_7 (L_7_Y6_5c4eca50, not_7_out, and_12_out);
  not not_8 (not_8_out, decoder_1_out7);
  and and_8 (L_8_Y7_5d798d3e, not_8_out, and_12_out);
  not not_9 (not_9_out, decoder_1_out8);
  and and_9 (L_9_Y8_0f54a762, not_9_out, and_12_out);
  not not_10 (not_10_out, decoder_1_out9);
  and and_10 (L_10_Y9_8a1abaab, not_10_out, and_12_out);
  not not_11 (not_11_out, decoder_1_out10);
  and and_11 (L_11_Y10_93957c82, not_11_out, and_12_out);
  and and_12 (and_12_out, not_12_out, not_13_out);
  Decoder #(.enable("false"), .select(4)) decoder_1 (
    .out0(decoder_1_out0), .out1(decoder_1_out1), .out2(decoder_1_out2), .out3(decoder_1_out3),
    .out4(decoder_1_out4), .out5(decoder_1_out5), .out6(decoder_1_out6), .out7(decoder_1_out7),
    .out8(decoder_1_out8), .out9(decoder_1_out9), .out10(decoder_1_out10), .out11(decoder_1_out11),
    .out12(decoder_1_out12), .out13(decoder_1_out13), .out14(decoder_1_out14), .out15(decoder_1_out15),
    .sel({L_20_D_c5e011af, L_21_C_a4808d66, L_22_B_35caca1a, L_23_A_d20b84ac}));
  not not_12 (not_12_out, L_19_G2_0092f278);
  not not_13 (not_13_out, L_18_G1_8e2783d5);
  not not_14 (not_14_out, decoder_1_out15);
  and and_13 (L_17_Y15_7952b3fc, not_14_out, and_12_out);
  not not_15 (not_15_out, decoder_1_out14);
  and and_14 (L_16_Y14_787c8a53, not_15_out, and_12_out);
  not not_16 (not_16_out, decoder_1_out13);
  and and_15 (L_15_Y13_fecf5aed, not_16_out, and_12_out);
  not not_17 (not_17_out, decoder_1_out12);
  and and_16 (L_14_Y12_cabf0cae, not_17_out, and_12_out);
  not not_18 (not_18_out, decoder_1_out11);
  and and_17 (L_13_Y11_5b38353b, not_18_out, and_12_out);

  // Notes on the sheet:
  //   74154: 4-Line to 16-Line Decoder
endmodule

// 74157
module L_74157_6f61a7ec (
  input  L_1_S_a6910581,
  input  L_16_Vcc_2c4a322e,
  input  L_2_A1_14f8ba50,
  input  L_15_G_9165f571,
  input  L_3_B1_e8c43654,
  input  L_14_A4_73bde12c,
  input  L_13_B4_8f9f4bcf,
  input  L_5_A2_3fd80c13,
  input  L_6_B2_f39197b4,
  input  L_11_A3_b8fab366,
  input  L_10_B3_806df849,
  input  L_8_GND_7238c13b,
  output L_4_Y1_8a261b35,
  output L_12_Y4_e09cb323,
  output L_7_Y2_b6acc335,
  output L_9_Y3_9c80703d
);

  wire multiplexer_1_out, multiplexer_2_out, multiplexer_3_out, multiplexer_4_out, not_1_out;

  Multiplexer multiplexer_1 (
    .in0(L_2_A1_14f8ba50), .in1(L_3_B1_e8c43654), .out(multiplexer_1_out), .sel(L_1_S_a6910581));
  and and_1 (L_4_Y1_8a261b35, multiplexer_1_out, not_1_out);
  Multiplexer multiplexer_2 (
    .in0(L_5_A2_3fd80c13), .in1(L_6_B2_f39197b4), .out(multiplexer_2_out), .sel(L_1_S_a6910581));
  and and_2 (L_7_Y2_b6acc335, multiplexer_2_out, not_1_out);
  not not_1 (not_1_out, L_15_G_9165f571);
  Multiplexer multiplexer_3 (
    .in0(L_14_A4_73bde12c), .in1(L_13_B4_8f9f4bcf), .out(multiplexer_3_out), .sel(L_1_S_a6910581));
  and and_3 (L_12_Y4_e09cb323, multiplexer_3_out, not_1_out);
  Multiplexer multiplexer_4 (
    .in0(L_11_A3_b8fab366), .in1(L_10_B3_806df849), .out(multiplexer_4_out), .sel(L_1_S_a6910581));
  and and_4 (L_9_Y3_9c80703d, multiplexer_4_out, not_1_out);

  // Notes on the sheet:
  //   74157: Quad 2-Line to 1-Line Multiplexer
endmodule

// 74161
module L_74161_50cdbbd8 (
  input  L_1_MR_8ccbb311,
  input  L_16_Vcc_2c4a322e,
  input  L_2_CP_462e71da,
  input  L_3_D0_2be1e632,
  input  L_4_D1_09909867,
  input  L_5_D2_8186c128,
  input  L_6_D3_43144684,
  input  L_7_CEP_a151107a,
  input  L_10_CET_9703f2ea,
  input  L_8_GND_7238c13b,
  input  L_9_PE_809987f1,
  output L_15_TC_67018374,
  output L_14_Q0_edd7971f,
  output L_13_Q1_a7dd0b82,
  output L_12_Q2_6fc6432d,
  output L_11_O3_b46da7ac
);

  wire and_1_out, counter_1_carry, not_1_out, not_2_out;

  not not_1 (not_1_out, L_1_MR_8ccbb311);
  and and_1 (and_1_out, L_7_CEP_a151107a, L_9_PE_809987f1, L_10_CET_9703f2ea);
  Counter #(.max('hf), .width(4)) counter_1 (
    .load(not_2_out), .D({L_6_D3_43144684, L_5_D2_8186c128, L_4_D1_09909867, L_3_D0_2be1e632}),
    .count(and_1_out), .Q({L_11_O3_b46da7ac, L_12_Q2_6fc6432d, L_13_Q1_a7dd0b82, L_14_Q0_edd7971f}),
    .carry(counter_1_carry), .clk(L_2_CP_462e71da), .clr(not_1_out));  // open: up
  and and_2 (L_15_TC_67018374, counter_1_carry, L_10_CET_9703f2ea);
  not not_2 (not_2_out, L_9_PE_809987f1);

  // Notes on the sheet:
  //   74161: Synchronous 4-bit Binary Counter with Asynchronous Clear 
endmodule

// 74163
module L_74163_b8bcd66f (
  input  L_1_MR_8ccbb311,
  input  L_16_Vcc_2c4a322e,
  input  L_2_CP_462e71da,
  input  L_3_D0_2be1e632,
  input  L_4_D1_09909867,
  input  L_5_D2_8186c128,
  input  L_6_D3_43144684,
  input  L_7_CEP_a151107a,
  input  L_10_CET_9703f2ea,
  input  L_8_GND_7238c13b,
  input  L_9_PE_809987f1,
  output L_15_TC_67018374,
  output L_14_Q0_edd7971f,
  output L_13_Q1_a7dd0b82,
  output L_12_Q2_6fc6432d,
  output L_11_O3_b46da7ac
);

  wire and_1_out, and_2_out, counter_1_carry, not_1_out, not_2_out;
  wire [3:0] multiplexer_1_out;

  not not_1 (not_1_out, L_1_MR_8ccbb311);
  Multiplexer #(.width(4)) multiplexer_1 (
    .in0({L_6_D3_43144684, L_5_D2_8186c128, L_4_D1_09909867, L_3_D0_2be1e632}), .in1(4'b0000),
    .out(multiplexer_1_out), .sel(not_1_out));
  and and_1 (and_1_out, L_7_CEP_a151107a, and_2_out, L_10_CET_9703f2ea);
  not not_2 (not_2_out, and_2_out);
  Counter #(.max('hf), .width(4)) counter_1 (
    .load(not_2_out), .D(multiplexer_1_out), .count(and_1_out),
    .Q({L_11_O3_b46da7ac, L_12_Q2_6fc6432d, L_13_Q1_a7dd0b82, L_14_Q0_edd7971f}), .carry(counter_1_carry),
    .clk(L_2_CP_462e71da));  // open: up, clr
  and and_2 (and_2_out, ~not_1_out, L_9_PE_809987f1);  // AND_Gate
  and and_3 (L_15_TC_67018374, counter_1_carry, L_10_CET_9703f2ea);

  // Notes on the sheet:
  //   74163: Synchronous 4-bit Binary Counter with Synchronous Clear 
endmodule

// 74174
module L_74174_ae703469 (
  input  L_1_MR_48d9ebef,
  input  L_16_Vcc_2c4a322e,
  input  L_3_D0_2be1e632,
  input  L_14_D5_53112324,
  input  L_4_D1_09909867,
  input  L_13_D4_42b82a40,
  input  L_6_D2_b10a357d,
  input  L_11_D3_7ad20abb,
  input  L_8_GND_7238c13b,
  input  L_9_CP_15456b38,
  output L_2_Q0_e17b504f,
  output L_15_Q5_0451d593,
  output L_5_Q1_03cecf36,
  output L_12_Q4_70fec626,
  output L_7_Q2_eb6f2842,
  output L_10_Q3_f8ee9421
);

  wire undriven;

  not not_1 (L_9_CP_15456b38, L_1_MR_48d9ebef);
  D_Flip_Flop #(.trigger("high")) d_ff_1 (
    .Q(L_9_CP_15456b38), .Qn(L_9_CP_15456b38), .reset(undriven));  // open: D, clk, preset
  D_Flip_Flop #(.trigger("high")) d_ff_2 (
    .clk(L_9_CP_15456b38), .Q(L_9_CP_15456b38), .Qn(L_9_CP_15456b38), .preset(undriven));  // open: D, reset
  D_Flip_Flop #(.trigger("high")) d_ff_3 (
    .clk(L_9_CP_15456b38), .Q(L_9_CP_15456b38), .Qn(L_9_CP_15456b38));  // open: D, preset, reset
  D_Flip_Flop #(.trigger("high")) d_ff_4 (.clk(L_9_CP_15456b38), .preset(L_15_Q5_0451d593));  // open: D, Q, Qn, reset
  D_Flip_Flop #(.trigger("high")) d_ff_5 (.clk(L_9_CP_15456b38), .preset(L_12_Q4_70fec626));  // open: D, Q, Qn, reset
  D_Flip_Flop #(.trigger("high")) d_ff_6 (
    .clk(L_9_CP_15456b38), .D(L_11_D3_7ad20abb), .Q(L_10_Q3_f8ee9421), .reset(L_9_CP_15456b38));  // open: Qn, preset

  // Notes on the sheet:
  //   74174: Hex D-type flip-flop with reset; positive-edge trigger
endmodule

// 74198
module L_74198_33aca2b6 (
  input  L_1_S0_9ff2131d,
  input  L_24_Vcc_efe97306,
  input  L_2_Dsr_dc69461d,
  input  L_23_S1_4f8d239a,
  input  L_3_P0_f74146f6,
  input  L_22_Dsl_65a1a77d,
  input  L_21_P7_6b7be439,
  input  L_5_P1_50c2be2c,
  input  L_19_P6_3ba3f0a1,
  input  L_7_P2_d6c40b3c,
  input  L_17_P5_8656745b,
  input  L_9_P3_9a18ccb6,
  input  L_15_P4_a0374f43,
  input  L_11_CP_5d1e2665,
  input  L_12_GND_92cafb02,
  input  L_13_MR_32e244a9,
  output L_4_Q0_e406443e,
  output L_20_Q7_74c2474a,
  output L_6_Q1_c0e53a20,
  output L_18_Q6_d404c914,
  output L_8_Q2_5a639318,
  output L_16_Q5_6bed31a6,
  output L_10_Q3_f8ee9421,
  output L_14_Q4_98d3a219
);

  wire and_1_out, and_2_out, and_3_out, and_4_out, and_5_out, and_6_out, and_7_out, and_8_out, and_9_out,
       and_10_out, and_11_out, and_12_out, and_13_out, and_14_out, and_15_out, and_16_out, and_17_out,
       and_18_out, and_19_out, and_20_out, and_21_out, and_22_out, and_23_out, and_24_out, and_25_out,
       nor_1_out, not_1_out, not_2_out, not_3_out, or_1_out, or_2_out, or_3_out, or_4_out, or_5_out,
       or_6_out, or_7_out, or_8_out, or_9_out;

  not not_1 (not_1_out, L_1_S0_9ff2131d);
  not not_2 (not_2_out, L_23_S1_4f8d239a);
  nor nor_1 (nor_1_out, not_1_out, not_2_out);
  and and_1 (and_1_out, not_2_out, not_1_out);
  and and_2 (and_2_out, L_22_Dsl_65a1a77d, not_1_out);
  and and_3 (and_3_out, L_21_P7_6b7be439, nor_1_out);
  and and_4 (and_4_out, L_18_Q6_d404c914, not_2_out);
  and and_5 (and_5_out, L_20_Q7_74c2474a, not_1_out);
  and and_6 (and_6_out, L_19_P6_3ba3f0a1, nor_1_out);
  and and_7 (and_7_out, L_16_Q5_6bed31a6, not_2_out);
  and and_8 (and_8_out, L_18_Q6_d404c914, not_1_out);
  and and_9 (and_9_out, L_17_P5_8656745b, nor_1_out);
  and and_10 (and_10_out, L_14_Q4_98d3a219, not_2_out);
  and and_11 (and_11_out, L_16_Q5_6bed31a6, not_1_out);
  and and_12 (and_12_out, L_15_P4_a0374f43, nor_1_out);
  and and_13 (and_13_out, L_10_Q3_f8ee9421, not_2_out);
  and and_14 (and_14_out, L_14_Q4_98d3a219, not_1_out);
  and and_15 (and_15_out, L_9_P3_9a18ccb6, nor_1_out);
  and and_16 (and_16_out, L_8_Q2_5a639318, not_2_out);
  and and_17 (and_17_out, L_10_Q3_f8ee9421, not_1_out);
  and and_18 (and_18_out, L_7_P2_d6c40b3c, nor_1_out);
  and and_19 (and_19_out, L_6_Q1_c0e53a20, not_2_out);
  and and_20 (and_20_out, L_8_Q2_5a639318, not_1_out);
  and and_21 (and_21_out, L_5_P1_50c2be2c, nor_1_out);
  and and_22 (and_22_out, L_4_Q0_e406443e, not_2_out);
  and and_23 (and_23_out, L_6_Q1_c0e53a20, not_1_out);
  and and_24 (and_24_out, L_3_P0_f74146f6, nor_1_out);
  and and_25 (and_25_out, L_2_Dsr_dc69461d, not_2_out);
  or or_1 (or_1_out, L_11_CP_5d1e2665, and_1_out);
  or or_2 (or_2_out, and_2_out, and_3_out, and_4_out);
  or or_3 (or_3_out, and_5_out, and_6_out, and_7_out);
  or or_4 (or_4_out, and_8_out, and_9_out, and_10_out);
  or or_5 (or_5_out, and_11_out, and_12_out, and_13_out);
  or or_6 (or_6_out, and_14_out, and_15_out, and_16_out);
  or or_7 (or_7_out, and_17_out, and_18_out, and_19_out);
  or or_8 (or_8_out, and_20_out, and_21_out, and_22_out);
  or or_9 (or_9_out, and_23_out, and_24_out, and_25_out);
  D_Flip_Flop d_ff_1 (.clk(or_1_out), .D(or_2_out), .Q(L_20_Q7_74c2474a), .reset(not_3_out));  // open: Qn, preset
  D_Flip_Flop d_ff_2 (.preset(L_19_P6_3ba3f0a1), .reset(L_19_P6_3ba3f0a1));  // open: D, clk, Q, Qn
  D_Flip_Flop d_ff_3 (
    .Q(L_16_Q5_6bed31a6), .Qn(L_15_P4_a0374f43), .preset(L_17_P5_8656745b), .reset(L_17_P5_8656745b));  // open: D, clk
  D_Flip_Flop d_ff_4 (.clk(or_1_out), .D(or_5_out), .Q(L_14_Q4_98d3a219), .reset(not_3_out));  // open: Qn, preset
  not not_3 (not_3_out, L_13_MR_32e244a9);
  D_Flip_Flop d_ff_5 (.clk(or_1_out), .D(or_6_out), .Q(L_10_Q3_f8ee9421), .reset(not_3_out));  // open: Qn, preset
  D_Flip_Flop d_ff_6 (.clk(or_1_out), .D(or_7_out), .Q(L_8_Q2_5a639318), .reset(not_3_out));  // open: Qn, preset
  D_Flip_Flop d_ff_7 (.clk(or_1_out), .D(or_8_out), .Q(L_6_Q1_c0e53a20), .reset(not_3_out));  // open: Qn, preset
  D_Flip_Flop d_ff_8 (.clk(or_1_out), .D(or_9_out), .Q(L_4_Q0_e406443e), .reset(not_3_out));  // open: Qn, preset

  // Notes on the sheet:
  //   74198: 8-bit universal shift register
endmodule

// 74238
module L_74238_e7674b53 (
  input  L_1_A0_1d1e702a,
  input  L_16_Vcc_2c4a322e,
  input  L_2_A1_14f8ba50,
  input  L_3_A2_67ceb71f,
  input  L_4_E1_db3fb008,
  input  L_5_E2_3fea7676,
  input  L_6_E3_28fdb159,
  input  L_8_GND_7238c13b,
  output L_15_Y0_22f2d3da,
  output L_14_Y1_66300113,
  output L_13_Y2_bf3aae29,
  output L_12_Y3_60b3d81a,
  output L_11_Y4_e187eac2,
  output L_7_Y7_80811157,
  output L_10_Y5_a083d511,
  output L_9_Y6_ccf28fb3
);

  wire and_1_out;

  and and_1 (and_1_out, ~L_4_E1_db3fb008, ~L_5_E2_3fea7676, L_6_E3_28fdb159);  // AND_Gate
  Demultiplexer #(.select(3)) demultiplexer_1 (
    .out0(L_15_Y0_22f2d3da), .out1(L_14_Y1_66300113), .out2(L_13_Y2_bf3aae29), .out3(L_12_Y3_60b3d81a),
    .out4(L_11_Y4_e187eac2), .out5(L_10_Y5_a083d511), .out6(L_9_Y6_ccf28fb3), .out7(L_7_Y7_80811157),
    .in(and_1_out), .sel({L_3_A2_67ceb71f, L_2_A1_14f8ba50, L_1_A0_1d1e702a}));

  // Notes on the sheet:
  //   74238: 3-to-8 line decoder/demultiplexer; non-inverting
endmodule

// 74253
module L_74253_c1017743 (
  input  L_1_1G_e7be49a9,
  input  L_16_Vcc_2c4a322e,
  input  L_2_Sb_16bb522a,
  input  L_15_2G_7ba95554,
  input  L_3_1C3_3688884c,
  input  L_14_Sa_552c6879,
  input  L_4_1C2_9e963928,
  input  L_13_2C3_ede6f057,
  input  L_5_1C1_57a80b8e,
  input  L_12_2C2_81752be0,
  input  L_6_1C0_8ece1da3,
  input  L_11_2C1_73cefb20,
  input  L_10_2C0_db306049,
  input  L_8_GND_7238c13b,
  output L_7_1Y_f77e02aa,
  output L_9_2Y_12a55f13
);

  wire multiplexer_1_out, multiplexer_2_out, not_1_out, not_3_out;
  wire [1:0] not_4_out;

  not not_1 (not_1_out, L_1_1G_e7be49a9);
  not not_2 (not_4_out[1], L_2_Sb_16bb522a);
  Multiplexer #(.select(2)) multiplexer_1 (
    .in0(L_3_1C3_3688884c), .in1(L_4_1C2_9e963928), .in2(L_5_1C1_57a80b8e), .in3(L_6_1C0_8ece1da3),
    .out(multiplexer_1_out), .sel(not_4_out));
  and and_1 (L_7_1Y_f77e02aa, multiplexer_1_out, not_1_out);
  Multiplexer #(.select(2)) multiplexer_2 (
    .in0(L_13_2C3_ede6f057), .in1(L_12_2C2_81752be0), .in2(L_11_2C1_73cefb20), .in3(L_10_2C0_db306049),
    .out(multiplexer_2_out), .sel(not_4_out));
  not not_3 (not_3_out, L_15_2G_7ba95554);
  not not_4 (not_4_out[0], L_14_Sa_552c6879);
  and and_2 (L_9_2Y_12a55f13, multiplexer_2_out, not_3_out);

  // Notes on the sheet:
  //   74253: Dual 4-Lin to 1-Line Multiplexer
endmodule

// 74260
module L_74260_b2e0d1b6 (
  input  L_1_1A_14e525db,
  input  L_14_Vcc_b6e81b46,
  input  L_2_1B_6e949205,
  input  L_13_2D_cb7d826a,
  input  L_3_1E_ba121f58,
  input  L_12_2C_5782681d,
  input  L_4_1C_ee472e27,
  input  L_11_2E_002c2b08,
  input  L_5_1D_a3e06dab,
  input  L_10_2B_4ef7271a,
  input  L_9_2A_ba945aa9,
  input  L_7_GND_d4026f45,
  output L_6_1Y_f45f5244,
  output L_8_2Y_0031f173
);

  nor nor_1 (L_6_1Y_f45f5244, L_4_1C_ee472e27, L_2_1B_6e949205);
  nor nor_2 (L_8_2Y_0031f173, L_12_2C_5782681d, L_10_2B_4ef7271a);

  // Notes on the sheet:
  //   74260: dual 5-input NOR
endmodule

// 74371
module L_74371_6d40970d (
  input  L_1_AD_A_33656739,
  input  L_20_Vcc_8754ae4b,
  input  L_2_AD_B_05aa468a,
  input  L_19_AD_H_e98bf86d,
  input  L_3_AD_C_345618fe,
  input  L_18_AD_G_0cb1419d,
  input  L_4_AD_D_ce04eaa4,
  input  L_17_AD_F_af1f0780,
  input  L_5_AD_E_dc060b15,
  input  L_16_S_2_54aa7b08,
  input  L_6_DO_1_c4de128b,
  input  L_15_S_1_f4457b3c,
  input  L_7_DO_2_1b384ce5,
  input  L_14_DO_8_d749ce06,
  input  L_8_DO_3_69a96d4b,
  input  L_13_DO_7_28050654,
  input  L_9_DO_4_771da0f7,
  input  L_12_DO_6_37833876,
  input  L_10_GND_b5a7dde8,
  input  L_11_DO_5_a141a4ce
);

  wire or_1_out;

  or or_1 (or_1_out, L_16_S_2_54aa7b08, L_15_S_1_f4457b3c);
  ROM rom_1 (
    .addr({L_19_AD_H_e98bf86d, L_18_AD_G_0cb1419d, L_17_AD_F_af1f0780, L_5_AD_E_dc060b15, L_4_AD_D_ce04eaa4, L_3_AD_C_345618fe, L_2_AD_B_05aa468a, L_1_AD_A_33656739}),
    .data({L_14_DO_8_d749ce06, L_13_DO_7_28050654, L_12_DO_6_37833876, L_11_DO_5_a141a4ce, L_9_DO_4_771da0f7, L_8_DO_3_69a96d4b, L_7_DO_2_1b384ce5, L_6_DO_1_c4de128b}),
    .sel(or_1_out));

  // Notes on the sheet:
  //   74371: 2048-bit ROM, 256x8
endmodule

// 74682
module L_74682_bcb34149 (
  input  L_20_Vcc_8754ae4b,
  input  L_2_A0_b28c8f0b,
  input  L_3_B0_4ea88c8c,
  input  L_18_B7_b396c412,
  input  L_4_A1_d4ead95a,
  input  L_17_A7_f10da864,
  input  L_5_B1_2b074ae4,
  input  L_16_B6_9a47bd15,
  input  L_6_A2_e9017930,
  input  L_15_A6_f24380a8,
  input  L_7_B2_9afdf295,
  input  L_14_B5_58a6a219,
  input  L_8_A3_9823c5db,
  input  L_13_A5_680f1357,
  input  L_9_B3_64efadbe,
  input  L_12_B4_d220d56a,
  input  L_10_GND_b5a7dde8,
  input  L_11_A4_694e129a,
  output L_1_A_B_b62273af,
  output L_19_A_B_a745b743
);

  wire and_1_out, and_2_out, and_3_out, and_4_out, and_5_out, and_6_out, and_7_out, and_8_out, not_1_out,
       not_2_out, not_3_out, not_4_out, not_5_out, not_6_out, not_7_out, not_8_out, not_9_out, not_10_out,
       not_11_out, not_12_out, not_13_out, not_14_out, not_15_out, not_16_out, not_17_out, not_18_out,
       not_19_out, not_20_out, not_21_out, not_22_out, not_23_out, not_24_out, xnor_1_out, xnor_3_out,
       xnor_4_out, xnor_5_out, xnor_6_out, xnor_8_out;

  not not_1 (not_1_out, L_2_A0_b28c8f0b);
  not not_2 (not_2_out, L_3_B0_4ea88c8c);
  not not_3 (not_3_out, L_4_A1_d4ead95a);
  not not_4 (not_4_out, L_5_B1_2b074ae4);
  not not_5 (not_5_out, L_6_A2_e9017930);
  not not_6 (not_6_out, L_7_B2_9afdf295);
  not not_7 (not_7_out, L_8_A3_9823c5db);
  not not_8 (not_8_out, L_9_B3_64efadbe);
  not not_9 (not_9_out, L_11_A4_694e129a);
  not not_10 (not_10_out, L_12_B4_d220d56a);
  not not_11 (not_11_out, L_13_A5_680f1357);
  not not_12 (not_12_out, L_14_B5_58a6a219);
  not not_13 (not_13_out, L_15_A6_f24380a8);
  not not_14 (not_14_out, L_16_B6_9a47bd15);
  not not_15 (not_15_out, L_17_A7_f10da864);
  not not_16 (not_16_out, L_18_B7_b396c412);
  xnor xnor_1 (xnor_1_out, not_1_out, not_2_out);
  xnor xnor_2 (not_16_out, not_3_out, not_4_out);
  xnor xnor_3 (xnor_3_out, not_5_out, not_6_out);
  xnor xnor_4 (xnor_4_out, not_7_out, not_8_out);
  xnor xnor_5 (xnor_5_out, not_9_out, not_10_out);
  xnor xnor_6 (xnor_6_out, not_11_out, not_12_out);
  xnor xnor_7 (xnor_4_out, not_13_out, not_14_out);
  xnor xnor_8 (xnor_8_out, not_15_out, not_16_out);
  not not_17 (not_17_out, not_15_out);
  not not_18 (not_18_out, not_13_out);
  not not_19 (not_19_out, not_11_out);
  not not_20 (not_20_out, not_9_out);
  not not_21 (not_21_out, not_7_out);
  not not_22 (not_22_out, not_5_out);
  not not_23 (not_23_out, not_3_out);
  not not_24 (not_24_out, not_1_out);
  and and_1 (and_1_out, xnor_1_out, not_16_out, xnor_3_out, xnor_4_out, xnor_5_out, xnor_6_out, xnor_4_out, not_16_out, not_17_out);
  and and_2 (and_2_out, xnor_1_out, not_16_out, xnor_3_out, xnor_4_out, xnor_5_out, xnor_6_out, not_14_out, not_18_out);
  and and_3 (and_3_out, xnor_1_out, not_16_out, xnor_3_out, xnor_4_out, xnor_5_out, not_12_out, not_19_out);
  and and_4 (and_4_out, xnor_1_out, not_16_out, xnor_3_out, xnor_4_out, not_10_out, not_20_out);
  and and_5 (and_5_out, not_16_out, not_8_out);
  buf and_6 (and_6_out, not_16_out);  // AND_Gate
  and and_7 (and_7_out, xnor_1_out, not_4_out, not_23_out);
  and and_8 (and_8_out, not_2_out, not_24_out);
  nand nand_1 (L_19_A_B_a745b743, xnor_1_out, not_16_out, xnor_3_out, xnor_4_out, xnor_5_out, xnor_6_out, xnor_4_out, xnor_8_out);
  nor nor_1 (L_1_A_B_b62273af, and_1_out, and_2_out, and_3_out, and_4_out, and_5_out, and_6_out, and_7_out, and_8_out);

  // Notes on the sheet:
  //   74682: 8-bit magnitude comparator 
endmodule

// 744075
module L_744075_b945401f (
  input  L_1_1A_14e525db,
  input  L_14_Vcc_b6e81b46,
  input  L_2_1B_6e949205,
  input  L_13_1C_dc87a617,
  input  L_3_2A_ca98e641,
  input  L_4_2B_ddad564f,
  input  L_11_3C_18c077aa,
  input  L_5_2C_ee07c05c,
  input  L_10_3B_18491fd5,
  input  L_9_3A_dd04c70b,
  input  L_7_GND_d4026f45,
  output L_12_1Y_850f9390,
  output L_6_2Y_287f65cc,
  output L_8_3Y_87559555
);

  or or_1 (L_6_2Y_287f65cc, L_5_2C_ee07c05c, L_4_2B_ddad564f, L_3_2A_ca98e641);
  or or_2 (L_12_1Y_850f9390, L_2_1B_6e949205, L_1_1A_14e525db, L_13_1C_dc87a617);
  or or_3 (L_8_3Y_87559555, L_11_3C_18c077aa, L_10_3B_18491fd5, L_9_3A_dd04c70b);

  // Notes on the sheet:
  //   744075: triple 3-input OR 
endmodule
