// Logisim project DIP_74x.circ as structural Verilog
// 7474
module L_7474_94b34f73 (
  input  CP1,
  input  D1,
  input  iSD1,
  input  iRD1,
  input  CP2,
  input  D2,
  input  iSD2,
  input  iRD2,
  output Q1,
  output iQ1,
  output Q2,
  output iQ2
);

  wire d_ff_1_q, d_ff_1_qn, d_ff_2_q, d_ff_2_qn, nor_1_out, nor_2_out, not_1_out, not_2_out, not_3_out,
       not_4_out;

  not not_1 (not_1_out, iSD1);
  not not_2 (not_2_out, iRD1);
  not not_3 (not_3_out, iSD2);
  not not_4 (not_4_out, iRD2);
  D_Flip_Flop d_ff_1 (.clk(CP1), .D(D1), .Q(d_ff_1_q), .Qn(d_ff_1_qn), .preset(not_1_out), .reset(not_2_out));
  nor nor_1 (nor_1_out, iSD1, iRD1);
  D_Flip_Flop d_ff_2 (.clk(CP2), .D(D2), .Q(d_ff_2_q), .Qn(d_ff_2_qn), .preset(not_3_out), .reset(not_4_out));
  nor nor_2 (nor_2_out, iSD2, iRD2);
  Multiplexer multiplexer_1 (.in0(d_ff_1_q), .in1(1'b1), .out(Q1), .sel(nor_1_out));
  Multiplexer multiplexer_2 (.in0(d_ff_1_qn), .in1(1'b1), .out(iQ1), .sel(nor_1_out));
  Multiplexer multiplexer_3 (.in0(d_ff_2_q), .in1(1'b1), .out(Q2), .sel(nor_2_out));
  Multiplexer multiplexer_4 (.in0(d_ff_2_qn), .in1(1'b1), .out(iQ2), .sel(nor_2_out));
endmodule

// 7476
module L_7476_b3d893ea (
  input  J1,
  input  iCP1,
  input  K1,
  input  iRD1,
  input  iSD1,
  input  J2,
  input  iCP2,
  input  K2,
  input  iRD2,
  input  iSD2,
  output Q1,
  output iQ1,
  output Q2,
  output iQ2
);

  wire j_k_ff_1_q, j_k_ff_1_qn, j_k_ff_2_q, j_k_ff_2_qn, nor_1_out, nor_2_out, not_1_out, not_2_out,
       not_3_out, not_4_out;

  J_K_Flip_Flop #(.trigger("falling")) j_k_ff_1 (
    .J(J1), .clk(iCP1), .K(K1), .Q(j_k_ff_1_q), .Qn(j_k_ff_1_qn), .preset(not_1_out), .reset(not_2_out));
  not not_1 (not_1_out, iSD1);
  not not_2 (not_2_out, iRD1);
  J_K_Flip_Flop #(.trigger("falling")) j_k_ff_2 (
    .J(J2), .clk(iCP2), .K(K2), .Q(j_k_ff_2_q), .Qn(j_k_ff_2_qn), .preset(not_3_out), .reset(not_4_out));
  not not_3 (not_3_out, iSD2);
  not not_4 (not_4_out, iRD2);
  Multiplexer multiplexer_1 (.in0(j_k_ff_1_q), .in1(1'b1), .out(Q1), .sel(nor_1_out));
  Multiplexer multiplexer_2 (.in0(j_k_ff_1_qn), .in1(1'b1), .out(iQ1), .sel(nor_1_out));
  nor nor_1 (nor_1_out, iSD1, iRD1);
  Multiplexer multiplexer_3 (.in0(j_k_ff_2_q), .in1(1'b1), .out(Q2), .sel(nor_2_out));
  Multiplexer multiplexer_4 (.in0(j_k_ff_2_qn), .in1(1'b1), .out(iQ2), .sel(nor_2_out));
  nor nor_2 (nor_2_out, iSD2, iRD2);
endmodule

// 74109
module L_74109_df9abc63 (
  input  J1,
  input  CP1,
  input  iK1,
  input  iSD1,
  input  iRD1,
  input  J2,
  input  CP2,
  input  iK2,
  input  iSD2,
  input  iRD2,
  output Q1,
  output NOT_Q1_0b3b4ead,
  output Q2,
  output iQ2
);

  wire j_k_ff_1_q, j_k_ff_1_qn, j_k_ff_2_q, j_k_ff_2_qn, nor_1_out, nor_2_out, not_1_out, not_2_out,
       not_3_out, not_4_out, not_5_out, not_6_out;

  J_K_Flip_Flop j_k_ff_1 (
    .J(J1), .clk(CP1), .K(not_1_out), .Q(j_k_ff_1_q), .Qn(j_k_ff_1_qn), .preset(not_2_out), .reset(not_3_out));
  not not_1 (not_1_out, iK1);
  not not_2 (not_2_out, iSD1);
  not not_3 (not_3_out, iRD1);
  J_K_Flip_Flop j_k_ff_2 (
    .J(J2), .clk(CP2), .K(not_4_out), .Q(j_k_ff_2_q), .Qn(j_k_ff_2_qn), .preset(not_5_out), .reset(not_6_out));
  not not_4 (not_4_out, iK2);
  not not_5 (not_5_out, iSD2);
  not not_6 (not_6_out, iRD2);
  nor nor_1 (nor_1_out, iSD1, iRD1);
  nor nor_2 (nor_2_out, iSD2, iRD2);
  Multiplexer multiplexer_1 (.in0(j_k_ff_1_q), .in1(1'b1), .out(Q1), .sel(nor_1_out));
  Multiplexer multiplexer_2 (.in0(j_k_ff_1_qn), .in1(1'b1), .out(NOT_Q1_0b3b4ead), .sel(nor_1_out));
  Multiplexer multiplexer_3 (.in0(j_k_ff_2_q), .in1(1'b1), .out(Q2), .sel(nor_2_out));
  Multiplexer multiplexer_4 (.in0(j_k_ff_2_qn), .in1(1'b1), .out(iQ2), .sel(nor_2_out));
endmodule

// 74138
module L_74138_de378928 (
  input  E3,
  input  iE2,
  input  iE1,
  input  A0,
  input  A1,
  input  A2,
  output Y0,
  output Y1,
  output Y2,
  output Y3,
  output Y4,
  output Y5,
  output Y6,
  output Y7
);

  wire and_1_out, and_2_out, and_3_out, and_4_out, and_5_out, and_6_out, and_7_out, and_8_out, and_9_out,
       buffer_1_out, not_4_out, not_7_out, not_9_out, not_10_out, not_12_out, not_13_out, not_15_out,
       not_16_out;

  not not_1 (Y0, and_1_out);
  and and_1 (and_1_out, not_16_out, not_10_out);
  not not_2 (Y1, and_2_out);
  and and_2 (and_2_out, not_9_out, not_16_out);
  not not_3 (Y2, and_3_out);
  and and_3 (and_3_out, not_10_out, not_16_out);
  and and_4 (and_4_out, buffer_1_out, not_4_out, not_7_out);
  buf buffer_1 (buffer_1_out, E3);
  not not_4 (not_4_out, iE2);
  not not_5 (Y3, and_5_out);
  not not_6 (Y4, and_6_out);
  and and_5 (and_5_out, not_9_out, not_16_out);
  and and_6 (and_6_out, not_10_out, not_15_out);
  not not_7 (not_7_out, iE1);
  not not_8 (Y5, and_7_out);
  and and_7 (and_7_out, not_13_out, not_9_out);
  not not_9 (not_9_out, not_10_out);
  not not_10 (not_10_out, A0);
  not not_11 (Y6, and_8_out);
  and and_8 (and_8_out, not_10_out, not_12_out);
  not not_12 (not_12_out, not_13_out);
  not not_13 (not_13_out, A1);
  not not_14 (Y7, and_9_out);
  and and_9 (and_9_out, and_4_out, not_9_out);
  not not_15 (not_15_out, not_16_out);
  not not_16 (not_16_out, A2);
endmodule

// 74154
module L_74154_ceb6fd3e (
  input  iE0,
  input  iE1,
  input  A0,
  input  A1,
  input  A2,
  input  A3,
  output Y0,
  output Y1,
  output Y2,
  output Y3,
  output Y4,
  output Y5,
  output Y6,
  output Y7,
  output Y8,
  output Y9,
  output Y10,
  output Y11,
  output Y12,
  output Y13,
  output Y14,
  output Y15
);

  wire decoder_1_out0, decoder_1_out1, decoder_1_out2, decoder_1_out3, decoder_1_out4, decoder_1_out5,
       decoder_1_out6, decoder_1_out7, decoder_1_out8, decoder_1_out9, decoder_1_out10, decoder_1_out11,
       decoder_1_out12, decoder_1_out13, decoder_1_out14, decoder_1_out15, nor_1_out;
  wire [3:0] buffer_1_out;

  not not_1 (Y0, decoder_1_out0);
  not not_2 (Y1, decoder_1_out1);
  not not_3 (Y2, decoder_1_out2);
  not not_4 (Y3, decoder_1_out3);
  not not_5 (Y4, decoder_1_out4);
  not not_6 (Y5, decoder_1_out5);
  not not_7 (Y6, decoder_1_out6);
  not not_8 (Y7, decoder_1_out7);
  not not_9 (Y8, decoder_1_out8);
  not not_10 (Y9, decoder_1_out9);
  not not_11 (Y10, decoder_1_out10);
  not not_12 (Y11, decoder_1_out11);
  not not_13 (Y12, decoder_1_out12);
  not not_14 (Y13, decoder_1_out13);
  not not_15 (Y14, decoder_1_out14);
  not not_16 (Y15, decoder_1_out15);
  Decoder #(.select(4)) decoder_1 (
    .out0(decoder_1_out0), .out1(decoder_1_out1), .out2(decoder_1_out2), .out3(decoder_1_out3),
    .out4(decoder_1_out4), .out5(decoder_1_out5), .out6(decoder_1_out6), .out7(decoder_1_out7),
    .out8(decoder_1_out8), .out9(decoder_1_out9), .out10(decoder_1_out10), .out11(decoder_1_out11),
    .out12(decoder_1_out12), .out13(decoder_1_out13), .out14(decoder_1_out14), .out15(decoder_1_out15),
    .sel(buffer_1_out), .en(nor_1_out));
  nor nor_1 (nor_1_out, iE0, iE1);
  assign buffer_1_out = {A3, A2, A1, A0};  // Buffer buffer_1, 4 bits wide
endmodule

// 74160
module L_74160_e71b3637 (
  input  D0,
  input  D1,
  input  D2,
  input  D3,
  input  CET,
  input  CEP,
  input  iPE,
  input  iMR,
  input  CP,
  output Q0,
  output Q1,
  output Q2,
  output Q3,
  output TC
);

  wire and_1_out, and_2_out, and_3_out, and_4_out, and_5_out, and_6_out, and_7_out, and_8_out, and_9_out,
       buffer_1_out, buffer_2_out, buffer_3_out, buffer_4_out, buffer_5_out, buffer_6_out, d_ff_4_q,
       d_ff_4_qn, nand_1_out, nand_2_out, nor_1_out, nor_2_out, nor_3_out, nor_4_out, nor_5_out, nor_6_out,
       not_1_out, not_2_out, not_3_out, not_4_out, not_5_out, or_1_out, or_2_out, or_3_out, or_4_out,
       or_5_out, undriven, undriven_2, undriven_3, xnor_1_out, xnor_2_out, xnor_3_out;

  buf buffer_1 (buffer_1_out, CET);
  buf buffer_2 (buffer_2_out, CEP);
  not not_1 (not_1_out, iPE);
  not not_2 (not_2_out, not_1_out);
  not not_3 (not_3_out, iMR);
  not not_4 (not_4_out, CP);
  buf buffer_3 (buffer_3_out, D0);
  nand nand_1 (nand_1_out, buffer_1_out, buffer_2_out);
  and and_1 (and_1_out, buffer_3_out, not_1_out);
  not not_5 (not_5_out, nand_1_out);
  xnor xnor_1 (xnor_1_out, not_5_out, undriven_2);
  and and_2 (and_2_out, xnor_1_out, not_2_out);
  or or_1 (or_1_out, and_1_out, and_2_out);
  D_Flip_Flop #(.trigger("falling")) d_ff_1 (
    .clk(not_4_out), .Qn(not_4_out), .preset(undriven_2), .reset(undriven_2));  // open: D, Q
  buf buffer_4 (buffer_4_out, D1);
  nor nor_1 (nor_1_out, undriven_2, nand_1_out, d_ff_4_q);
  xnor xnor_2 (xnor_2_out, nor_1_out, undriven_3);
  and and_3 (and_3_out, buffer_4_out, not_1_out);
  and and_4 (and_4_out, xnor_2_out, not_2_out);
  or or_2 (or_2_out, and_3_out, and_4_out);
  not not_6 (Q0, undriven_2);
  buf buffer_5 (buffer_5_out, D2);
  D_Flip_Flop #(.trigger("falling")) d_ff_2 (
    .clk(not_4_out), .Qn(not_4_out), .preset(undriven_3), .reset(undriven_3));  // open: D, Q
  not not_7 (Q1, undriven_3);
  nor nor_2 (nor_2_out, nand_1_out, undriven_3, undriven_2);
  xnor xnor_3 (xnor_3_out, nor_2_out, d_ff_4_q);
  and and_5 (and_5_out, buffer_5_out, not_1_out);
  and and_6 (and_6_out, xnor_3_out, not_2_out);
  or or_3 (or_3_out, and_5_out, and_6_out);
  buf buffer_6 (buffer_6_out, D3);
  nor nor_3 (nor_3_out, nand_1_out, d_ff_4_q, undriven_3, undriven_2);
  and and_7 (and_7_out, buffer_6_out, not_1_out);
  or or_4 (or_4_out, and_7_out, and_9_out);
  D_Flip_Flop #(.trigger("falling")) d_ff_3 (
    .clk(not_4_out), .Qn(not_4_out), .preset(d_ff_4_q), .reset(d_ff_4_q));  // open: D, Q
  not not_8 (Q2, d_ff_4_q);
  nor nor_4 (nor_4_out, nand_1_out, nor_6_out);
  and and_8 (and_8_out, nor_3_out, d_ff_4_qn);
  nor nor_5 (nor_5_out, d_ff_4_qn, nor_4_out);
  or or_5 (or_5_out, and_8_out, nor_5_out);
  and and_9 (and_9_out, not_2_out, or_5_out);
  D_Flip_Flop #(.trigger("falling")) d_ff_4 (
    .clk(not_4_out), .D(or_4_out), .Q(d_ff_4_q), .Qn(d_ff_4_qn), .reset(not_3_out));  // open: preset
  not not_9 (Q3, d_ff_4_qn);
  nor nor_6 (nor_6_out, undriven, d_ff_4_qn);
  nand nand_2 (nand_2_out, d_ff_4_q, undriven);
  not not_10 (TC, nand_2_out);
endmodule

// 74161
module L_74161_c39caa33 (
  input  D0,
  input  D1,
  input  D2,
  input  D3,
  input  CET,
  input  CEP,
  input  iPE,
  input  iMR,
  input  CP,
  output Q0,
  output Q1,
  output Q2,
  output Q3,
  output TC
);

  wire and_1_out, and_2_out, and_3_out, and_4_out, and_5_out, and_6_out, and_7_out, and_8_out, and_9_out,
       buffer_1_out, buffer_2_out, d_ff_4_q, nand_1_out, nand_2_out, nor_1_out, nor_2_out, nor_3_out,
       nor_4_out, not_1_out, not_2_out, not_3_out, not_4_out, not_5_out, or_1_out, or_2_out, or_3_out,
       or_4_out, or_5_out, undriven, undriven_2, undriven_3, undriven_4, undriven_5, xnor_1_out, xnor_2_out,
       xnor_3_out;

  buf buffer_1 (buffer_1_out, CET);
  buf buffer_2 (buffer_2_out, CEP);
  not not_1 (not_1_out, iPE);
  not not_2 (not_2_out, not_1_out);
  not not_3 (not_3_out, iMR);
  not not_4 (not_4_out, CP);
  nand nand_1 (nand_1_out, buffer_1_out, buffer_2_out);
  and and_1 (and_1_out, D0, not_1_out);
  not not_5 (not_5_out, nand_1_out);
  xnor xnor_1 (xnor_1_out, not_5_out, undriven_2);
  and and_2 (and_2_out, xnor_1_out, not_2_out);
  or or_1 (or_1_out, and_1_out, and_2_out);
  D_Flip_Flop #(.trigger("falling")) d_ff_1 (
    .clk(not_4_out), .Qn(not_4_out), .preset(undriven_2), .reset(undriven_2));  // open: D, Q
  nor nor_1 (nor_1_out, nand_1_out, undriven_2);
  xnor xnor_2 (xnor_2_out, nor_1_out, undriven_3);
  and and_3 (and_3_out, D1, not_1_out);
  and and_4 (and_4_out, xnor_2_out, not_2_out);
  or or_2 (or_2_out, and_3_out, and_4_out);
  not not_6 (Q0, undriven_2);
  D_Flip_Flop #(.trigger("falling")) d_ff_2 (
    .clk(not_4_out), .Qn(not_4_out), .preset(undriven_3), .reset(undriven_3));  // open: D, Q
  not not_7 (Q1, undriven_3);
  nor nor_2 (nor_2_out, nand_1_out, undriven_3, undriven_2);
  xnor xnor_3 (xnor_3_out, nor_2_out, undriven_4);
  and and_5 (and_5_out, D2, not_1_out);
  and and_6 (and_6_out, xnor_3_out, not_2_out);
  or or_3 (or_3_out, and_5_out, and_6_out);
  nor nor_3 (nor_3_out, nand_1_out, undriven_4, undriven_3, undriven_2);
  and and_7 (and_7_out, D3, not_1_out);
  or or_4 (or_4_out, and_7_out, and_9_out);
  D_Flip_Flop #(.trigger("falling")) d_ff_3 (
    .clk(not_4_out), .Qn(not_4_out), .preset(undriven_4), .reset(undriven_4));  // open: D, Q
  not not_8 (Q2, undriven_4);
  and and_8 (and_8_out, nor_3_out, undriven_5);
  nor nor_4 (nor_4_out, nor_3_out, undriven_5);
  or or_5 (or_5_out, and_8_out, nor_4_out);
  and and_9 (and_9_out, not_2_out, or_5_out);
  D_Flip_Flop #(.trigger("falling")) d_ff_4 (
    .Q(d_ff_4_q), .preset(undriven_5), .reset(undriven_5));  // open: D, clk, Qn
  not not_9 (Q3, undriven_5);
  nand nand_2 (nand_2_out, d_ff_4_q, undriven);
  not not_10 (TC, nand_2_out);
endmodule

// 74163
module L_74163_b93cf454 (
  input  D0,
  input  D1,
  input  D2,
  input  D3,
  input  CET,
  input  CEP,
  input  iPE,
  input  iMR,
  input  CP,
  output Q0,
  output Q1,
  output Q2,
  output Q3,
  output TC
);

  wire and_1_out, and_2_out, and_3_out, and_4_out, and_5_out, and_6_out, and_7_out, and_8_out, and_9_out,
       buffer_1_out, buffer_2_out, buffer_3_out, d_ff_4_q, nand_1_out, nand_2_out, nor_1_out, nor_2_out,
       nor_3_out, nor_4_out, nor_5_out, nor_6_out, not_1_out, not_2_out, not_3_out, or_1_out, or_2_out,
       or_3_out, or_4_out, or_5_out, undriven, undriven_2, undriven_3, undriven_4, undriven_5, xnor_1_out,
       xnor_2_out, xnor_3_out;

  buf buffer_1 (buffer_1_out, iPE);
  buf buffer_2 (buffer_2_out, CET);
  buf buffer_3 (buffer_3_out, CEP);
  nor nor_1 (nor_1_out, buffer_1_out, not_1_out);
  not not_1 (not_1_out, iMR);
  not not_2 (not_2_out, CP);
  nand nand_1 (nand_1_out, buffer_2_out, buffer_3_out);
  nor nor_2 (nor_2_out, nor_1_out, not_1_out);
  and and_1 (and_1_out, D0, nor_1_out);
  not not_3 (not_3_out, nand_1_out);
  xnor xnor_1 (xnor_1_out, not_3_out, undriven_2);
  and and_2 (and_2_out, xnor_1_out, nor_2_out);
  or or_1 (or_1_out, and_1_out, and_2_out);
  D_Flip_Flop #(.trigger("falling")) d_ff_1 (
    .clk(not_2_out), .Qn(not_2_out), .preset(undriven_2), .reset(undriven_2));  // open: D, Q
  nor nor_3 (nor_3_out, nand_1_out, undriven_2);
  xnor xnor_2 (xnor_2_out, nor_3_out, undriven_3);
  and and_3 (and_3_out, D1, nor_1_out);
  and and_4 (and_4_out, xnor_2_out, nor_2_out);
  or or_2 (or_2_out, and_3_out, and_4_out);
  not not_4 (Q0, undriven_2);
  D_Flip_Flop #(.trigger("falling")) d_ff_2 (
    .clk(not_2_out), .Qn(not_2_out), .preset(undriven_3), .reset(undriven_3));  // open: D, Q
  not not_5 (Q1, undriven_3);
  nor nor_4 (nor_4_out, nand_1_out, undriven_3, undriven_2);
  xnor xnor_3 (xnor_3_out, nor_4_out, undriven_4);
  and and_5 (and_5_out, D2, nor_1_out);
  and and_6 (and_6_out, xnor_3_out, nor_2_out);
  or or_3 (or_3_out, and_5_out, and_6_out);
  nor nor_5 (nor_5_out, nand_1_out, undriven_4, undriven_3, undriven_2);
  and and_7 (and_7_out, D3, nor_1_out);
  or or_4 (or_4_out, and_7_out, and_9_out);
  D_Flip_Flop #(.trigger("falling")) d_ff_3 (
    .clk(not_2_out), .Qn(not_2_out), .preset(undriven_4), .reset(undriven_4));  // open: D, Q
  not not_6 (Q2, undriven_4);
  and and_8 (and_8_out, nor_5_out, undriven_5);
  nor nor_6 (nor_6_out, nor_5_out, undriven_5);
  or or_5 (or_5_out, and_8_out, nor_6_out);
  and and_9 (and_9_out, nor_2_out, or_5_out);
  D_Flip_Flop #(.trigger("falling")) d_ff_4 (
    .Q(d_ff_4_q), .preset(undriven_5), .reset(undriven_5));  // open: D, clk, Qn
  not not_7 (Q3, undriven_5);
  nand nand_2 (nand_2_out, d_ff_4_q, undriven);
  not not_8 (TC, nand_2_out);
endmodule

// 74669
module L_74669_3c58340c (
  input  D0,
  input  D1,
  input  D2,
  input  D3,
  input  iPE,
  input  iCEP,
  input  iCET,
  input  UD,
  input  CP,
  output iTC,
  output Q0,
  output Q1,
  output Q2,
  output Q3
);

  wire and_1_out, and_2_out, and_3_out, and_4_out, and_5_out, and_6_out, and_7_out, and_8_out, and_9_out,
       and_10_out, and_11_out, and_12_out, and_13_out, and_14_out, and_15_out, and_16_out, and_17_out,
       and_18_out, and_19_out, and_20_out, and_21_out, nand_1_out, nand_2_out, nand_3_out, nand_4_out,
       nand_5_out, nand_6_out, not_1_out, not_2_out, not_3_out, not_4_out, not_5_out, not_6_out, or_1_out,
       or_2_out, or_3_out, or_4_out, undriven, undriven_2, undriven_3, undriven_4;

  and and_1 (and_1_out, ~iCEP, ~iCET);  // AND_Gate
  not not_1 (not_1_out, UD);
  not not_2 (not_2_out, iPE);
  not not_3 (not_3_out, not_2_out);
  not not_4 (not_4_out, iCET);
  not not_5 (not_5_out, not_1_out);
  not not_6 (not_6_out, CP);
  and and_2 (and_2_out, not_3_out, ~and_1_out, Q0);  // AND_Gate
  and and_3 (and_3_out, not_2_out, D0);
  and and_4 (and_4_out, and_1_out, not_3_out, ~Q0);  // AND_Gate
  or or_1 (or_1_out, and_2_out, and_3_out, and_4_out);
  D_Flip_Flop #(.trigger("falling")) d_ff_1 (.preset(Q0), .reset(Q0));  // open: D, clk, Q, Qn
  nand nand_1 (nand_1_out, undriven, and_1_out);
  and and_5 (and_5_out, nand_1_out, not_3_out, Q1, not_1_out);
  and and_6 (and_6_out, not_2_out, D1);
  and and_7 (and_7_out, ~not_1_out, undriven);  // AND_Gate
  or or_2 (or_2_out, and_7_out, and_8_out);
  nand nand_2 (nand_2_out, Q0, and_1_out);
  and and_8 (and_8_out, Q1, nand_2_out, not_3_out, not_5_out);
  D_Flip_Flop #(.trigger("falling")) d_ff_2 (.preset(Q1), .reset(Q1));  // open: D, clk, Q, Qn
  and and_9 (and_9_out, ~not_3_out, and_1_out);  // AND_Gate
  nand nand_3 (nand_3_out, Q1, Q0, and_1_out);
  and and_10 (and_10_out, nand_3_out, not_3_out, Q2, not_5_out);
  and and_11 (and_11_out, not_5_out, not_3_out, Q1, Q0, and_1_out, ~Q2);  // AND_Gate
  and and_12 (and_12_out, not_2_out, D2);
  nand nand_4 (nand_4_out, undriven_2, and_1_out, undriven);
  and and_13 (and_13_out, Q2, nand_4_out, not_3_out, not_1_out);
  or or_3 (or_3_out, and_11_out, and_13_out);
  D_Flip_Flop #(.trigger("falling")) d_ff_3 (.preset(Q2), .reset(Q2));  // open: D, clk, Q, Qn
  and and_14 (and_14_out, ~Q2, not_1_out, and_1_out, not_3_out, undriven_2, undriven);  // AND_Gate
  nand nand_5 (nand_5_out, undriven_3, undriven_2, undriven, and_1_out);
  and and_15 (and_15_out, nand_5_out, Q3, not_3_out, not_1_out);
  and and_16 (and_16_out, not_1_out, not_3_out, and_1_out, undriven_3, undriven_2, undriven, ~Q3);  // AND_Gate
  and and_17 (and_17_out, not_2_out, D3);
  nand nand_6 (nand_6_out, Q2, Q1, Q0, and_1_out);
  or or_4 (or_4_out, and_16_out, and_18_out);
  and and_18 (and_18_out, Q3, nand_6_out, not_3_out, not_5_out);
  D_Flip_Flop #(.trigger("falling")) d_ff_4 (.preset(Q3), .reset(Q3));  // open: D, clk, Q, Qn
  and and_19 (and_19_out, ~Q3, not_3_out, not_5_out, and_1_out, Q2, Q1, Q0);  // AND_Gate
  and and_20 (and_20_out, not_1_out, undriven, undriven_2, undriven_3, undriven_4, not_4_out);
  and and_21 (and_21_out, not_4_out, not_5_out, Q0, Q1, Q2, Q3);
  nor nor_1 (iTC, and_20_out, and_21_out);
endmodule

// 74193
module L_74193_569541ca (
  input  D0,
  input  D1,
  input  D2,
  input  D3,
  input  iPL,
  input  CPu,
  input  CPd,
  input  MR,
  output iTCu,
  output iTCd,
  output Q0,
  output Q1,
  output Q2,
  output Q3
);

  wire and_1_out, and_2_out, and_3_out, and_4_out, and_5_out, and_6_out, buffer_1_out, buffer_2_out,
       buffer_3_out, buffer_5_out, buffer_7_out, buffer_9_out, nand_1_out, nand_2_out, nand_3_out,
       nand_4_out, nand_5_out, nand_6_out, nand_7_out, nand_8_out, nand_9_out, nand_10_out, nor_1_out,
       nor_2_out, nor_3_out, nor_4_out, not_1_out, not_2_out, not_3_out, not_4_out, not_5_out, not_6_out,
       not_7_out, not_8_out, or_1_out, or_2_out, or_3_out, or_4_out, t_ff_1_q, t_ff_1_qn, t_ff_2_qn,
       t_ff_3_q, t_ff_3_qn, t_ff_4_q, t_ff_4_qn, undriven;

  not not_1 (not_1_out, iPL);
  not not_2 (not_2_out, CPu);
  buf buffer_1 (buffer_1_out, not_2_out);
  buf buffer_2 (buffer_2_out, not_3_out);
  not not_3 (not_3_out, CPd);
  not not_4 (not_4_out, MR);
  buf buffer_3 (buffer_3_out, D0);
  nand nand_1 (nand_1_out, not_1_out, buffer_3_out);
  not not_5 (not_5_out, nand_1_out);
  nor nor_1 (nor_1_out, buffer_1_out, buffer_2_out);
  or or_1 (or_1_out, ~not_4_out, ~nand_2_out);  // OR_Gate
  nand nand_2 (nand_2_out, nand_1_out, not_1_out);
  T_Flip_Flop t_ff_1 (
    .clk(nor_1_out), .T(nor_1_out), .Q(t_ff_1_q), .Qn(t_ff_1_qn), .preset(not_5_out), .reset(or_1_out));
  buf buffer_4 (Q0, t_ff_1_q);
  and and_1 (and_1_out, not_2_out, t_ff_1_q);
  nor nor_2 (nor_2_out, and_1_out, and_2_out);
  and and_2 (and_2_out, t_ff_1_qn, not_3_out);
  buf buffer_5 (buffer_5_out, D1);
  nand nand_3 (nand_3_out, not_1_out, buffer_5_out);
  nand nand_4 (nand_4_out, nand_3_out, not_1_out);
  not not_6 (not_6_out, nand_3_out);
  T_Flip_Flop t_ff_2 (.clk(or_2_out), .Qn(t_ff_2_qn), .reset(undriven), .preset(undriven));  // open: T, Q
  or or_2 (or_2_out, ~not_4_out, ~nand_4_out);  // OR_Gate
  buf buffer_6 (Q1, undriven);
  and and_3 (and_3_out, not_2_out, t_ff_1_q, undriven);
  and and_4 (and_4_out, t_ff_2_qn, t_ff_1_qn, not_3_out);
  nor nor_3 (nor_3_out, and_3_out, and_4_out);
  buf buffer_7 (buffer_7_out, D2);
  nand nand_5 (nand_5_out, not_1_out, buffer_7_out);
  nand nand_6 (nand_6_out, nand_5_out, not_1_out);
  not not_7 (not_7_out, nand_5_out);
  T_Flip_Flop t_ff_3 (
    .clk(nor_3_out), .T(nor_3_out), .Q(t_ff_3_q), .Qn(t_ff_3_qn), .preset(not_7_out), .reset(or_3_out));
  or or_3 (or_3_out, ~not_4_out, ~nand_6_out);  // OR_Gate
  buf buffer_8 (Q2, t_ff_3_q);
  and and_5 (and_5_out, undriven, not_2_out, t_ff_1_q, t_ff_3_q);
  nor nor_4 (nor_4_out, and_5_out, and_6_out);
  and and_6 (and_6_out, t_ff_3_qn, t_ff_2_qn, t_ff_1_qn, not_3_out);
  buf buffer_9 (buffer_9_out, D3);
  nand nand_7 (nand_7_out, nand_8_out, not_1_out);
  nand nand_8 (nand_8_out, not_1_out, buffer_9_out);
  not not_8 (not_8_out, nand_8_out);
  T_Flip_Flop t_ff_4 (
    .clk(nor_4_out), .T(nor_4_out), .Q(t_ff_4_q), .Qn(t_ff_4_qn), .preset(not_8_out), .reset(or_4_out));
  or or_4 (or_4_out, ~not_4_out, ~nand_7_out);  // OR_Gate
  buf buffer_10 (Q3, t_ff_4_q);
  nand nand_9 (nand_9_out, not_2_out, undriven);
  nand nand_10 (nand_10_out, t_ff_4_qn, t_ff_2_qn);
  buf buffer_11 (iTCu, nand_9_out);
  buf buffer_12 (iTCd, nand_10_out);
endmodule

// 74164
module L_74164_daec004b (
  input  DSA,
  input  DSB,
  input  CP,
  input  MR,
  output Q0,
  output Q1,
  output Q2,
  output Q3,
  output Q4,
  output Q5,
  output Q6,
  output Q7
);

  wire and_1_out, buffer_1_out, not_1_out;

  and and_1 (and_1_out, DSA, DSB);
  buf buffer_1 (buffer_1_out, CP);
  not not_1 (not_1_out, MR);
  D_Flip_Flop d_ff_1 (.clk(not_1_out), .Qn(not_1_out), .preset(Q0), .reset(Q0));  // open: D, Q
  D_Flip_Flop d_ff_2 (.clk(not_1_out), .Qn(not_1_out), .preset(Q1), .reset(Q1));  // open: D, Q
  D_Flip_Flop d_ff_3 (.clk(not_1_out), .Qn(not_1_out), .preset(Q2), .reset(Q2));  // open: D, Q
  D_Flip_Flop d_ff_4 (.clk(not_1_out), .Qn(not_1_out), .preset(Q3), .reset(Q3));  // open: D, Q
  D_Flip_Flop d_ff_5 (.clk(not_1_out), .Qn(not_1_out), .preset(Q4), .reset(Q4));  // open: D, Q
  D_Flip_Flop d_ff_6 (.clk(not_1_out), .Qn(not_1_out), .preset(Q5), .reset(Q5));  // open: D, Q
  D_Flip_Flop d_ff_7 (.clk(not_1_out), .Qn(not_1_out), .preset(Q6), .reset(Q6));  // open: D, Q
  D_Flip_Flop d_ff_8 (.clk(not_1_out), .preset(Q7), .reset(Q7));  // open: D, Q, Qn
endmodule

// 74165
module L_74165_149472d7 (
  input  D0,
  input  D1,
  input  D2,
  input  D3,
  input  D4,
  input  D5,
  input  D6,
  input  D7,
  input  iPL,
  input  DS,
  input  iCE,
  input  CP,
  output Q7,
  output iQ7
);

  wire nand_1_out, nand_2_out, nand_3_out, nand_4_out, nand_5_out, nand_6_out, nand_7_out, nand_8_out,
       nand_9_out, nand_10_out, nand_11_out, nand_12_out, nand_13_out, nand_14_out, nand_15_out, nand_16_out,
       nor_1_out, not_1_out, not_2_out, not_3_out, not_4_out, not_5_out, not_6_out, not_7_out, not_8_out,
       not_9_out, not_10_out, not_11_out, not_12_out, not_13_out, not_14_out, not_15_out, not_16_out,
       not_17_out;
  wire [6:0] d_ff_1_q;

  not not_1 (not_1_out, iPL);
  nand nand_1 (nand_1_out, not_1_out, D0);
  nor nor_1 (nor_1_out, iCE, CP);
  D_Flip_Flop d_ff_1 (.clk(nor_1_out), .D(DS), .Q(d_ff_1_q[0]), .preset(not_2_out), .reset(not_3_out));  // open: Qn
  not not_2 (not_2_out, nand_1_out);
  not not_3 (not_3_out, nand_2_out);
  nand nand_2 (nand_2_out, nand_1_out, not_1_out);
  nand nand_3 (nand_3_out, not_1_out, D1);
  D_Flip_Flop d_ff_2 (
    .clk(nor_1_out), .D(d_ff_1_q[0]), .Q(d_ff_1_q[1]), .preset(not_4_out), .reset(not_5_out));  // open: Qn
  not not_4 (not_4_out, nand_3_out);
  not not_5 (not_5_out, nand_4_out);
  nand nand_4 (nand_4_out, nand_3_out, not_1_out);
  nand nand_5 (nand_5_out, not_1_out, D2);
  not not_6 (not_6_out, nand_5_out);
  not not_7 (not_7_out, nand_6_out);
  nand nand_6 (nand_6_out, nand_5_out, not_1_out);
  nand nand_7 (nand_7_out, not_1_out, D3);
  D_Flip_Flop d_ff_3 (
    .clk(nor_1_out), .D(d_ff_1_q[1]), .Q(d_ff_1_q[2]), .preset(not_6_out), .reset(not_7_out));  // open: Qn
  not not_8 (not_8_out, nand_7_out);
  nand nand_8 (nand_8_out, not_1_out, D4);
  D_Flip_Flop d_ff_4 (
    .clk(nor_1_out), .D(d_ff_1_q[2]), .Q(d_ff_1_q[3]), .preset(not_8_out), .reset(not_9_out));  // open: Qn
  not not_9 (not_9_out, nand_9_out);
  nand nand_9 (nand_9_out, nand_7_out, not_1_out);
  D_Flip_Flop d_ff_5 (
    .clk(nor_1_out), .D(d_ff_1_q[3]), .Q(d_ff_1_q[4]), .preset(not_10_out), .reset(not_11_out));  // open: Qn
  not not_10 (not_10_out, nand_8_out);
  not not_11 (not_11_out, nand_10_out);
  nand nand_10 (nand_10_out, nand_8_out, not_1_out);
  nand nand_11 (nand_11_out, not_1_out, D5);
  D_Flip_Flop d_ff_6 (
    .clk(nor_1_out), .D(d_ff_1_q[4]), .Q(d_ff_1_q[5]), .preset(not_12_out), .reset(not_13_out));  // open: Qn
  not not_12 (not_12_out, nand_11_out);
  not not_13 (not_13_out, nand_12_out);
  nand nand_12 (nand_12_out, nand_11_out, not_1_out);
  nand nand_13 (nand_13_out, not_1_out, D6);
  not not_14 (not_14_out, nand_13_out);
  not not_15 (not_15_out, nand_14_out);
  nand nand_14 (nand_14_out, nand_13_out, not_1_out);
  nand nand_15 (nand_15_out, not_1_out, D7);
  D_Flip_Flop d_ff_7 (
    .clk(nor_1_out), .D(d_ff_1_q[5]), .Q(d_ff_1_q[6]), .preset(not_14_out), .reset(not_15_out));  // open: Qn
  not not_16 (not_16_out, nand_15_out);
  D_Flip_Flop d_ff_8 (.clk(nor_1_out), .D(d_ff_1_q[6]), .Q(Q7), .Qn(iQ7), .preset(not_16_out), .reset(not_17_out));
  not not_17 (not_17_out, nand_16_out);
  nand nand_16 (nand_16_out, nand_15_out, not_1_out);
endmodule

// 74166
module L_74166_8b3b4793 (
  input  D0,
  input  D1,
  input  D2,
  input  D3,
  input  D4,
  input  D5,
  input  D6,
  input  D7,
  input  iPE,
  input  DS,
  input  CP,
  input  iCE,
  input  iMR,
  output Q7
);

  wire and_1_out, and_2_out, and_3_out, and_4_out, and_5_out, and_6_out, and_7_out, and_8_out, and_9_out,
       and_10_out, and_11_out, and_12_out, and_13_out, and_14_out, and_15_out, and_16_out, buffer_1_out,
       buffer_2_out, buffer_3_out, buffer_4_out, buffer_5_out, buffer_6_out, buffer_7_out, buffer_8_out,
       buffer_9_out, buffer_10_out, buffer_11_out, nor_1_out, nor_2_out, not_1_out, not_2_out, not_3_out,
       not_4_out, not_5_out, not_6_out, not_7_out, not_8_out, not_9_out, not_10_out, not_11_out, undriven;
  wire [7:1] undriven_2;

  not not_1 (not_1_out, iPE);
  not not_2 (not_2_out, not_1_out);
  buf buffer_1 (buffer_1_out, DS);
  buf buffer_2 (buffer_2_out, CP);
  buf buffer_3 (buffer_3_out, iCE);
  not not_3 (not_3_out, iMR);
  buf buffer_4 (buffer_4_out, D0);
  and and_1 (and_1_out, buffer_1_out, not_2_out);
  and and_2 (and_2_out, not_1_out, buffer_4_out);
  nor nor_1 (nor_1_out, and_1_out, and_2_out);
  not not_4 (not_4_out, nor_1_out);
  nor nor_2 (nor_2_out, buffer_2_out, buffer_3_out);
  and and_3 (and_3_out, undriven_2[7], not_2_out);
  nor nor_3 (nor_2_out, and_3_out, and_4_out);
  not not_5 (not_5_out, nor_2_out);
  S_R_Flip_Flop #(.trigger("falling")) s_r_ff_1 (
    .R(not_3_out), .clk(not_3_out), .Q(nor_2_out));  // open: S, reset, Qn, preset
  buf buffer_5 (buffer_5_out, D1);
  and and_4 (and_4_out, not_1_out, buffer_5_out);
  and and_5 (and_5_out, undriven_2[6], not_2_out);
  S_R_Flip_Flop #(.trigger("falling")) s_r_ff_2 (
    .R(not_3_out), .clk(not_3_out), .Q(nor_2_out));  // open: S, reset, Qn, preset
  buf buffer_6 (buffer_6_out, D2);
  and and_6 (and_6_out, not_1_out, buffer_6_out);
  nor nor_4 (nor_2_out, and_5_out, and_6_out);
  not not_6 (not_6_out, nor_2_out);
  S_R_Flip_Flop #(.trigger("falling")) s_r_ff_3 (
    .R(not_3_out), .clk(not_3_out), .Q(nor_2_out));  // open: S, reset, Qn, preset
  buf buffer_7 (buffer_7_out, D3);
  and and_7 (and_7_out, undriven_2[5], not_2_out);
  and and_8 (and_8_out, not_1_out, buffer_7_out);
  nor nor_5 (nor_2_out, and_7_out, and_8_out);
  not not_7 (not_7_out, nor_2_out);
  and and_9 (and_9_out, undriven_2[4], not_2_out);
  nor nor_6 (nor_2_out, and_9_out, and_10_out);
  not not_8 (not_8_out, nor_2_out);
  S_R_Flip_Flop #(.trigger("falling")) s_r_ff_4 (
    .R(not_3_out), .clk(not_3_out), .Q(nor_2_out));  // open: S, reset, Qn, preset
  buf buffer_8 (buffer_8_out, D4);
  and and_10 (and_10_out, not_1_out, buffer_8_out);
  S_R_Flip_Flop #(.trigger("falling")) s_r_ff_5 (
    .R(not_3_out), .clk(not_3_out), .Q(nor_2_out));  // open: S, reset, Qn, preset
  buf buffer_9 (buffer_9_out, D5);
  and and_11 (and_11_out, undriven_2[3], not_2_out);
  and and_12 (and_12_out, not_1_out, buffer_9_out);
  nor nor_7 (nor_2_out, and_11_out, and_12_out);
  not not_9 (not_9_out, nor_2_out);
  S_R_Flip_Flop #(.trigger("falling")) s_r_ff_6 (
    .R(not_3_out), .clk(not_3_out), .Q(nor_2_out));  // open: S, reset, Qn, preset
  and and_13 (and_13_out, undriven_2[2], not_2_out);
  and and_14 (and_14_out, not_1_out, buffer_10_out);
  nor nor_8 (nor_2_out, and_13_out, and_14_out);
  not not_10 (not_10_out, nor_2_out);
  buf buffer_10 (buffer_10_out, D6);
  and and_15 (and_15_out, undriven_2[1], not_2_out);
  S_R_Flip_Flop #(.trigger("falling")) s_r_ff_7 (
    .R(not_3_out), .clk(not_3_out), .Q(nor_2_out));  // open: S, reset, Qn, preset
  buf buffer_11 (buffer_11_out, D7);
  and and_16 (and_16_out, not_1_out, buffer_11_out);
  nor nor_9 (nor_2_out, and_15_out, and_16_out);
  not not_11 (not_11_out, nor_2_out);
  S_R_Flip_Flop #(.trigger("falling")) s_r_ff_8 (
    .R(not_3_out), .clk(not_3_out), .reset(Q7), .preset(undriven));  // open: S, Q, Qn
  buf buffer_12 (Q7, undriven);
endmodule

module L_74299_ed20e7e4 (
  input  DSR,
  input  S0,
  input  S1,
  input  CP,
  input  OE1,
  input  OE2,
  input  [7:0] in,
  input  DSL,
  input  MR,
  output [7:0] test,
  output Q0,
  output [7:0] out,
  output Q7
);

  wire and_1_out, and_2_out, and_3_out, and_4_out, and_5_out, and_6_out, and_7_out, and_8_out, and_9_out,
       and_10_out, and_11_out, and_12_out, and_13_out, and_14_out, and_15_out, and_16_out, and_17_out,
       and_18_out, and_19_out, and_20_out, and_21_out, and_22_out, and_23_out, and_24_out, and_25_out,
       and_26_out, and_27_out, and_28_out, and_29_out, and_30_out, and_31_out, and_32_out, buffer_1_out,
       buffer_2_out, buffer_3_out, buffer_6_out, buffer_7_out, buffer_8_out, buffer_9_out, buffer_10_out,
       buffer_11_out, buffer_12_out, buffer_13_out, nand_1_out, nand_2_out, not_1_out, not_2_out, not_3_out,
       not_4_out, not_5_out, not_6_out, not_7_out, or_1_out, or_2_out, or_3_out, or_4_out, or_5_out,
       or_6_out, or_7_out, or_8_out;

  nand nand_1 (nand_1_out, S0, S1);
  buf buffer_1 (buffer_1_out, DSR);
  buf buffer_2 (buffer_2_out, S0);
  not not_1 (not_1_out, buffer_2_out);
  buf buffer_3 (buffer_3_out, S1);
  not not_2 (not_2_out, buffer_3_out);
  not not_3 (not_3_out, CP);
  buf buffer_4 (Q0, test[0]);
  nand nand_2 (nand_2_out, nand_1_out, ~OE1, ~OE2);  // NAND_Gate
  not not_4 (not_4_out, not_1_out);
  not not_5 (not_5_out, not_2_out);
  buf buffer_5 (Q7, test[7]);
  not not_6 (not_6_out, MR);
  and and_1 (and_1_out, buffer_1_out, not_4_out, not_2_out);
  and and_2 (and_2_out, not_5_out, not_1_out, test[1]);
  and and_3 (and_3_out, not_5_out, not_4_out, buffer_6_out);
  and and_4 (and_4_out, not_2_out, not_1_out, test[0]);
  and and_5 (and_5_out, test[0], not_4_out, not_2_out);
  and and_6 (and_6_out, not_5_out, not_1_out, test[2]);
  and and_7 (and_7_out, not_5_out, not_4_out, buffer_7_out);
  and and_8 (and_8_out, not_2_out, not_1_out, test[1]);
  and and_9 (and_9_out, test[1], not_4_out, not_2_out);
  and and_10 (and_10_out, not_5_out, not_1_out, test[3]);
  and and_11 (and_11_out, not_5_out, not_4_out, buffer_8_out);
  and and_12 (and_12_out, not_2_out, not_1_out, test[2]);
  and and_13 (and_13_out, test[2], not_4_out, not_2_out);
  and and_14 (and_14_out, not_5_out, not_1_out, test[4]);
  and and_15 (and_15_out, not_5_out, not_4_out, buffer_9_out);
  and and_16 (and_16_out, not_2_out, not_1_out, test[3]);
  and and_17 (and_17_out, test[3], not_4_out, not_2_out);
  and and_18 (and_18_out, not_5_out, not_1_out, test[5]);
  and and_19 (and_19_out, not_5_out, not_4_out, buffer_10_out);
  and and_20 (and_20_out, not_2_out, not_1_out, test[4]);
  and and_21 (and_21_out, test[4], not_4_out, not_2_out);
  and and_22 (and_22_out, not_5_out, not_1_out, test[6]);
  and and_23 (and_23_out, not_5_out, not_4_out, buffer_11_out);
  and and_24 (and_24_out, not_2_out, not_1_out, test[5]);
  and and_25 (and_25_out, test[5], not_4_out, not_2_out);
  and and_26 (and_26_out, not_5_out, not_1_out, test[7]);
  and and_27 (and_27_out, not_5_out, not_4_out, buffer_12_out);
  and and_28 (and_28_out, not_2_out, not_1_out, test[6]);
  and and_29 (and_29_out, test[6], not_4_out, not_2_out);
  and and_30 (and_30_out, not_5_out, not_1_out, DSL);
  and and_31 (and_31_out, not_5_out, not_4_out, buffer_13_out);
  and and_32 (and_32_out, not_2_out, not_1_out, test[7]);
  or or_1 (or_1_out, and_1_out, and_2_out, and_3_out, and_4_out);
  or or_2 (or_2_out, and_5_out, and_6_out, and_7_out, and_8_out);
  or or_3 (or_3_out, and_9_out, and_10_out, and_11_out, and_12_out);
  or or_4 (or_4_out, and_13_out, and_14_out, and_15_out, and_16_out);
  or or_5 (or_5_out, and_17_out, and_18_out, and_19_out, and_20_out);
  or or_6 (or_6_out, and_21_out, and_22_out, and_23_out, and_24_out);
  or or_7 (or_7_out, and_25_out, and_26_out, and_27_out, and_28_out);
  or or_8 (or_8_out, and_29_out, and_30_out, and_31_out, and_32_out);
  buf buffer_6 (buffer_6_out, in[0]);
  assign out[0] = not_7_out ? test[0] : 1'bz;  // Controlled_Buffer controlled_buffer_1
  D_Flip_Flop #(.trigger("falling")) d_ff_1 (
    .clk(not_6_out), .Q(test[1]), .Qn(test[1]), .reset(not_7_out));  // open: D, preset
  not not_7 (not_7_out, nand_2_out);
  buf buffer_7 (buffer_7_out, in[1]);
  assign out[1] = not_7_out ? test[1] : 1'bz;  // Controlled_Buffer controlled_buffer_2
  D_Flip_Flop #(.trigger("falling")) d_ff_2 (
    .clk(not_6_out), .Q(in[1]), .Qn(in[1]), .preset(not_7_out), .reset(not_7_out));  // open: D
  buf buffer_8 (buffer_8_out, in[2]);
  assign out[2] = not_7_out ? test[2] : 1'bz;  // Controlled_Buffer controlled_buffer_3
  D_Flip_Flop #(.trigger("falling")) d_ff_3 (.clk(not_6_out), .preset(not_7_out), .reset(not_7_out));  // open: D, Q, Qn
  buf buffer_9 (buffer_9_out, in[3]);
  assign out[3] = not_7_out ? test[3] : 1'bz;  // Controlled_Buffer controlled_buffer_4
  D_Flip_Flop #(.trigger("falling")) d_ff_4 (.clk(not_6_out), .preset(not_7_out), .reset(not_7_out));  // open: D, Q, Qn
  buf buffer_10 (buffer_10_out, in[4]);
  assign out[4] = not_7_out ? test[4] : 1'bz;  // Controlled_Buffer controlled_buffer_5
  D_Flip_Flop #(.trigger("falling")) d_ff_5 (.clk(not_6_out), .preset(not_7_out), .reset(not_7_out));  // open: D, Q, Qn
  buf buffer_11 (buffer_11_out, in[5]);
  assign out[5] = not_7_out ? test[5] : 1'bz;  // Controlled_Buffer controlled_buffer_6
  D_Flip_Flop #(.trigger("falling")) d_ff_6 (.clk(not_6_out), .preset(not_7_out), .reset(not_7_out));  // open: D, Q, Qn
  buf buffer_12 (buffer_12_out, in[6]);
  assign out[6] = not_7_out ? test[6] : 1'bz;  // Controlled_Buffer controlled_buffer_7
  D_Flip_Flop #(.trigger("falling")) d_ff_7 (.clk(not_6_out), .preset(not_7_out), .reset(not_7_out));  // open: D, Q, Qn
  buf buffer_13 (buffer_13_out, in[7]);
  assign out[7] = not_7_out ? test[7] : 1'bz;  // Controlled_Buffer controlled_buffer_8
  D_Flip_Flop #(.trigger("falling")) d_ff_8 (.clk(not_6_out), .preset(not_7_out));  // open: D, Q, Qn, reset
endmodule

// 74181
module L_74181_e6f12ee4 (
  input  S3,
  input  S2,
  input  S1,
  input  S0,
  input  B3,
  input  A3,
  input  B2,
  input  A2,
  input  B1,
  input  A1,
  input  B0,
  input  A0,
  input  M,
  input  Cn,
  output G,
  output Cn_4_cb6af43f,
  output P,
  output F3,
  output F2,
  output A_B_66665e43,
  output F1,
  output F0
);

  wire and_1_out, and_2_out, and_3_out, and_4_out, and_5_out, and_6_out, and_7_out, and_8_out, and_9_out,
       and_10_out, and_11_out, and_12_out, and_13_out, and_14_out, and_15_out, and_16_out, and_17_out,
       and_18_out, and_19_out, and_20_out, and_21_out, and_22_out, and_23_out, and_24_out, and_25_out,
       and_26_out, and_28_out, and_29_out, and_30_out, and_31_out, and_32_out, and_33_out, and_34_out,
       and_35_out, and_36_out, and_37_out, and_38_out, nand_2_out, nand_4_out, nor_2_out, nor_3_out,
       nor_4_out, nor_5_out, nor_6_out, nor_7_out, nor_8_out, nor_9_out, nor_10_out, nor_11_out, nor_12_out,
       not_1_out, not_2_out, not_3_out, not_4_out, not_5_out, not_6_out, not_7_out, not_8_out, not_9_out;

  and and_1 (and_1_out, nor_3_out, nor_3_out);
  nor nor_1 (G, and_3_out, and_5_out);
  and and_2 (and_2_out, nor_2_out, nor_4_out, nor_9_out);
  and and_3 (and_3_out, nor_2_out, nor_6_out);
  and and_4 (and_4_out, B3, S3, A3);
  nand nand_1 (Cn_4_cb6af43f, G, nand_2_out);
  and and_5 (and_5_out, nor_4_out, nor_12_out);
  nor nor_2 (nor_2_out, and_4_out, and_6_out);
  and and_6 (and_6_out, A3, S2, not_1_out);
  not not_1 (not_1_out, B3);
  nand nand_2 (nand_2_out, nor_4_out, nor_11_out);
  nand nand_3 (P, nor_4_out, nor_11_out);
  nor nor_3 (nor_3_out, and_7_out, and_8_out, and_10_out);
  and and_7 (and_7_out, not_1_out, S1);
  and and_8 (and_8_out, S0, B3);
  and and_9 (and_9_out, nor_2_out, not_2_out);
  not not_2 (not_2_out, nor_3_out);
  and and_10 (and_10_out, A3, A3);
  and and_11 (and_11_out, nor_7_out, Cn);
  nor nor_4 (nor_4_out, and_12_out, and_13_out);
  and and_12 (and_12_out, B2, S3, A2);
  and and_13 (and_13_out, A2, S2, not_3_out);
  xor xor_1 (F3, and_9_out, nor_5_out);
  nor nor_5 (nor_5_out, and_14_out, and_18_out);
  and and_14 (and_14_out, nor_7_out, not_9_out);
  and and_15 (and_15_out, nor_4_out, nor_9_out, not_9_out);
  nor nor_6 (nor_6_out, and_16_out, and_17_out, and_19_out);
  and and_16 (and_16_out, not_3_out, S1);
  and and_17 (and_17_out, S0, B2);
  not not_3 (not_3_out, B2);
  and and_18 (and_18_out, nor_6_out, not_9_out);
  and and_19 (and_19_out, A2, A2);
  and and_20 (and_20_out, nor_4_out, not_4_out);
  and and_21 (and_21_out, nor_7_out, Cn);
  not not_4 (not_4_out, nor_6_out);
  nor nor_7 (nor_7_out, and_22_out, and_25_out);
  and and_22 (and_22_out, B1, S3, A1);
  xor xor_2 (F2, and_20_out, nor_8_out);
  nor nor_8 (nor_8_out, and_21_out, and_23_out, and_24_out);
  and and_23 (and_23_out, nor_7_out, nor_12_out, not_9_out);
  and and_24 (and_24_out, nor_9_out, not_9_out);
  and and_25 (and_25_out, A1, S2, not_5_out);
  and and_26 (and_26_out, not_5_out, S1);
  not not_5 (not_5_out, B1);
  and and_27 (A_B_66665e43, F3, F1);
  and and_28 (and_28_out, nor_7_out, not_6_out);
  not not_6 (not_6_out, nor_9_out);
  nor nor_9 (nor_9_out, and_26_out, and_29_out, and_30_out);
  and and_29 (and_29_out, S0, B1);
  and and_30 (and_30_out, A1, A1);
  xor xor_3 (F1, and_28_out, nor_10_out);
  and and_31 (and_31_out, Cn, nor_11_out, not_9_out);
  and and_32 (and_32_out, B0, S3, A0);
  nor nor_10 (nor_10_out, and_31_out, and_33_out);
  and and_33 (and_33_out, nor_12_out, not_9_out);
  nor nor_11 (nor_11_out, and_32_out, and_34_out);
  and and_34 (and_34_out, A0, S2, not_7_out);
  not not_7 (not_7_out, B0);
  and and_35 (and_35_out, nor_11_out, not_8_out);
  not not_8 (not_8_out, nor_12_out);
  nor nor_12 (nor_12_out, and_36_out, and_37_out, and_38_out);
  and and_36 (and_36_out, not_7_out, S1);
  and and_37 (and_37_out, S0, B0);
  xor xor_4 (F0, and_35_out, nand_4_out);
  nand nand_4 (nand_4_out, not_9_out, Cn);
  and and_38 (and_38_out, A0, A0);
  not not_9 (not_9_out, M);
endmodule

// 74182
module L_74182_4f460642 (
  input  iG0,
  input  iP0,
  input  Cn,
  input  iG1,
  input  iP1,
  input  iG2,
  input  iP2,
  input  iG3,
  input  iP3,
  output Cn_x_c4f77548,
  output Cn_y_925745ef,
  output Cn_z_5d92889f,
  output iG,
  output iP
);

  wire and_1_out, and_2_out, and_3_out, and_4_out, and_5_out, and_6_out, and_7_out, and_8_out, and_9_out,
       and_10_out, and_11_out, and_12_out, and_13_out, not_1_out;

  nor nor_1 (Cn_x_c4f77548, and_2_out, and_1_out);
  and and_1 (and_1_out, iG0, not_1_out);
  and and_2 (and_2_out, iG0, iP0);
  not not_1 (not_1_out, Cn);
  and and_3 (and_3_out, iG1, iP1);
  nor nor_2 (Cn_y_925745ef, and_3_out, and_4_out, and_5_out);
  and and_4 (and_4_out, iG0, iP0, iG1);
  and and_5 (and_5_out, not_1_out, iG0, iG1);
  and and_6 (and_6_out, iG2, iP2);
  nor nor_3 (Cn_z_5d92889f, and_6_out, and_7_out, and_8_out, and_9_out);
  and and_7 (and_7_out, iG1, iP1, iG2);
  and and_8 (and_8_out, iG0, iG1);
  and and_9 (and_9_out, not_1_out, iG1);
  and and_10 (and_10_out, iG3, iP3);
  or or_1 (iG, and_10_out, and_11_out, and_12_out, and_13_out);
  and and_11 (and_11_out, iG2, iP2, iG3);
  and and_12 (and_12_out, iG1, iG2);
  and and_13 (and_13_out, iG0, iG2);
  or or_2 (iP, iP0, iP1, iP2, iP3);
endmodule

// 74381
module L_74381_e035d630 (
  input  Cn,
  input  B0,
  input  A0,
  input  B1,
  input  A1,
  input  B2,
  input  A2,
  input  B3,
  input  A3,
  input  S0,
  input  S1,
  input  S2,
  output F0,
  output F1,
  output F2,
  output F3,
  output P,
  output G
);

  wire and_1_out, and_2_out, and_3_out, and_4_out, and_5_out, and_6_out, and_7_out, and_8_out, and_9_out,
       and_10_out, and_11_out, and_12_out, and_13_out, and_14_out, and_15_out, and_16_out, and_17_out,
       and_18_out, and_19_out, and_20_out, and_21_out, and_22_out, and_23_out, and_24_out, and_25_out,
       and_26_out, and_27_out, and_28_out, and_29_out, and_30_out, and_31_out, and_32_out, and_33_out,
       and_34_out, and_35_out, and_36_out, and_37_out, and_38_out, and_39_out, and_40_out, and_41_out,
       and_42_out, and_43_out, and_44_out, nand_1_out, nand_3_out, nand_4_out, nand_5_out, nand_6_out,
       nor_1_out, nor_2_out, nor_3_out, nor_4_out, nor_5_out, nor_6_out, nor_7_out, nor_8_out, nor_9_out,
       nor_10_out, nor_11_out, nor_12_out, nor_14_out, not_1_out, not_2_out, not_3_out, not_4_out, not_5_out,
       not_6_out, not_7_out, not_8_out, not_9_out, not_10_out, not_11_out, not_12_out, not_13_out, not_14_out;

  and and_1 (and_1_out, not_2_out, nand_3_out);
  nor nor_1 (nor_1_out, and_1_out, and_2_out, and_3_out);
  and and_2 (and_2_out, nand_3_out, not_1_out);
  not not_1 (not_1_out, B0);
  and and_3 (and_3_out, nand_6_out, B0);
  nand nand_1 (nand_1_out, Cn, nor_12_out);
  and and_4 (and_4_out, not_1_out, nand_5_out);
  and and_5 (and_5_out, nand_6_out, not_1_out);
  not not_2 (not_2_out, A0);
  xor xor_1 (F0, nand_1_out, nor_2_out);
  nor nor_2 (nor_2_out, and_4_out, and_6_out);
  and and_6 (and_6_out, nand_6_out, B0);
  and and_7 (and_7_out, nand_4_out, B0);
  and and_8 (and_8_out, not_4_out, nand_3_out);
  nor nor_3 (nor_3_out, and_8_out, and_9_out, and_10_out);
  and and_9 (and_9_out, nand_3_out, not_3_out);
  not not_3 (not_3_out, B1);
  and and_10 (and_10_out, nand_6_out, B1);
  and and_11 (and_11_out, not_3_out, nand_5_out);
  xor xor_2 (F1, nor_4_out, nor_5_out);
  nor nor_4 (nor_4_out, and_12_out, and_13_out);
  and and_12 (and_12_out, Cn, nor_1_out, nor_12_out);
  and and_13 (and_13_out, nor_1_out, nor_2_out, nor_12_out);
  nor nor_5 (nor_5_out, and_11_out, and_15_out);
  and and_14 (and_14_out, nand_6_out, not_3_out);
  not not_4 (not_4_out, A1);
  and and_15 (and_15_out, nand_6_out, B1);
  and and_16 (and_16_out, nand_4_out, B1);
  and and_17 (and_17_out, not_6_out, nand_3_out);
  not not_5 (not_5_out, B2);
  and and_18 (and_18_out, Cn, nor_3_out);
  nor nor_6 (nor_6_out, and_17_out, and_19_out, and_20_out);
  and and_19 (and_19_out, nand_3_out, not_5_out);
  and and_20 (and_20_out, nand_6_out, B2);
  nor nor_7 (nor_7_out, and_18_out, and_21_out, and_23_out);
  and and_21 (and_21_out, nor_1_out, nor_2_out);
  and and_22 (and_22_out, not_5_out, nand_5_out);
  xor xor_3 (F2, nor_7_out, nor_8_out);
  and and_23 (and_23_out, nor_3_out, nor_5_out, nor_12_out);
  nor nor_8 (nor_8_out, and_22_out, and_25_out);
  and and_24 (and_24_out, nand_6_out, not_5_out);
  not not_6 (not_6_out, A2);
  and and_25 (and_25_out, nand_6_out, B2);
  and and_26 (and_26_out, nand_4_out, B2);
  and and_27 (and_27_out, nor_1_out, nor_6_out);
  nor nor_9 (nor_9_out, and_28_out, and_29_out, and_32_out);
  and and_28 (and_28_out, not_8_out, nand_3_out);
  and and_29 (and_29_out, nand_3_out, not_7_out);
  not not_7 (not_7_out, B3);
  nor nor_10 (nor_10_out, and_27_out, and_31_out);
  and and_30 (and_30_out, nor_3_out, nor_2_out);
  and and_31 (and_31_out, nor_3_out, nor_5_out);
  and and_32 (and_32_out, nand_6_out, B3);
  and and_33 (and_33_out, nor_6_out, nor_8_out, nor_12_out);
  and and_34 (and_34_out, not_7_out, nand_5_out);
  not not_8 (not_8_out, A3);
  xor xor_4 (F3, nor_10_out, nor_11_out);
  nor nor_11 (nor_11_out, and_34_out, and_36_out);
  and and_35 (and_35_out, nand_6_out, not_7_out);
  and and_36 (and_36_out, nand_6_out, B3);
  nand nand_2 (P, nor_1_out, nor_6_out);
  nor nor_12 (nor_12_out, not_14_out, and_40_out);
  and and_37 (and_37_out, nand_4_out, B3);
  and and_38 (and_38_out, nor_3_out, nor_9_out);
  and and_39 (and_39_out, nor_3_out, nor_9_out);
  and and_40 (and_40_out, not_9_out, not_11_out);
  nor nor_13 (G, and_38_out, and_41_out);
  and and_41 (and_41_out, nor_6_out, nor_9_out, nor_8_out);
  and and_42 (and_42_out, not_9_out, not_14_out);
  nand nand_3 (nand_3_out, not_9_out, not_12_out);
  nand nand_4 (nand_4_out, not_9_out, not_11_out);
  not not_9 (not_9_out, S0);
  and and_43 (and_43_out, nor_9_out, nor_11_out);
  nor nor_14 (nor_14_out, and_42_out, and_44_out);
  nand nand_5 (nand_5_out, not_10_out, not_12_out, not_13_out);
  and and_44 (and_44_out, not_11_out, not_14_out);
  nand nand_6 (nand_6_out, not_11_out, not_13_out);
  not not_10 (not_10_out, not_9_out);
  not not_11 (not_11_out, S1);
  not not_12 (not_12_out, not_11_out);
  not not_13 (not_13_out, S2);
  not not_14 (not_14_out, not_13_out);
endmodule

// 74382
module L_74382_89ac2290 (
  input  Cn,
  input  B0,
  input  A0,
  input  B1,
  input  A1,
  input  B2,
  input  A2,
  input  B3,
  input  A3,
  input  S0,
  input  S1,
  input  S2,
  output F0,
  output F1,
  output F2,
  output F3,
  output OVR,
  output Cn_4_cb6af43f
);

  wire and_1_out, and_2_out, and_3_out, and_4_out, and_5_out, and_6_out, and_7_out, and_8_out, and_9_out,
       and_10_out, and_11_out, and_12_out, and_13_out, and_14_out, and_15_out, and_16_out, and_17_out,
       and_18_out, and_19_out, and_20_out, and_21_out, and_22_out, and_23_out, and_24_out, and_25_out,
       and_26_out, and_27_out, and_28_out, and_29_out, and_30_out, and_31_out, and_32_out, and_33_out,
       and_34_out, and_35_out, and_36_out, and_37_out, and_38_out, and_39_out, and_40_out, and_41_out,
       and_42_out, and_43_out, and_44_out, and_45_out, nand_1_out, nand_2_out, nand_3_out, nand_4_out,
       nand_6_out, nand_7_out, nor_1_out, nor_2_out, nor_3_out, nor_4_out, nor_5_out, nor_6_out, nor_7_out,
       nor_8_out, nor_9_out, nor_10_out, nor_11_out, nor_12_out, nor_13_out, nor_14_out, not_1_out,
       not_2_out, not_3_out, not_4_out, not_5_out, not_6_out, not_7_out, not_8_out, not_9_out, not_10_out,
       not_11_out, not_12_out, not_13_out, not_14_out;

  and and_1 (and_1_out, not_2_out, nand_3_out);
  nor nor_1 (nor_1_out, and_1_out, and_2_out, and_3_out);
  and and_2 (and_2_out, nand_3_out, not_1_out);
  not not_1 (not_1_out, B0);
  and and_3 (and_3_out, nand_7_out, B0);
  and and_4 (and_4_out, not_1_out, nand_2_out);
  xor xor_1 (F0, nand_1_out, nor_2_out);
  nand nand_1 (nand_1_out, Cn, nor_12_out);
  nor nor_2 (nor_2_out, and_4_out, and_6_out);
  and and_5 (and_5_out, nand_7_out, not_1_out);
  not not_2 (not_2_out, A0);
  and and_6 (and_6_out, nand_7_out, B0);
  and and_7 (and_7_out, nand_4_out, B0);
  and and_8 (and_8_out, not_4_out, nand_3_out);
  not not_3 (not_3_out, B1);
  nor nor_3 (nor_3_out, and_8_out, and_9_out, and_10_out);
  and and_9 (and_9_out, nand_3_out, not_3_out);
  and and_10 (and_10_out, nand_7_out, B1);
  and and_11 (and_11_out, Cn, nor_1_out, nor_12_out);
  and and_12 (and_12_out, not_3_out, nand_2_out);
  xor xor_2 (F1, nor_4_out, nor_5_out);
  nor nor_4 (nor_4_out, and_11_out, and_13_out);
  and and_13 (and_13_out, nor_1_out, nor_2_out, nor_12_out);
  nor nor_5 (nor_5_out, and_12_out, and_16_out);
  and and_14 (and_14_out, nand_7_out, not_3_out);
  not not_4 (not_4_out, A1);
  and and_15 (and_15_out, nand_4_out, B1);
  and and_16 (and_16_out, nand_7_out, B1);
  nor nor_6 (nor_6_out, and_17_out, and_18_out, and_20_out);
  and and_17 (and_17_out, not_6_out, nand_3_out);
  and and_18 (and_18_out, nand_3_out, not_5_out);
  not not_5 (not_5_out, B2);
  and and_19 (and_19_out, Cn, nor_3_out);
  and and_20 (and_20_out, nand_7_out, B2);
  nor nor_7 (nor_7_out, and_19_out, and_21_out, and_23_out);
  and and_21 (and_21_out, nor_1_out, nor_2_out);
  and and_22 (and_22_out, not_5_out, nand_2_out);
  not not_6 (not_6_out, A2);
  xor xor_3 (F2, nor_7_out, nor_8_out);
  and and_23 (and_23_out, nor_3_out, nor_5_out, nor_12_out);
  nor nor_8 (nor_8_out, and_22_out, and_25_out);
  and and_24 (and_24_out, nand_7_out, not_5_out);
  and and_25 (and_25_out, nand_7_out, B2);
  and and_26 (and_26_out, nand_4_out, B2);
  and and_27 (and_27_out, not_8_out, nand_3_out);
  and and_28 (and_28_out, nor_1_out, nor_6_out);
  and and_29 (and_29_out, nor_3_out, nor_2_out);
  nor nor_9 (nor_9_out, and_27_out, and_30_out, and_32_out);
  and and_30 (and_30_out, nand_3_out, not_7_out);
  not not_7 (not_7_out, B3);
  nor nor_10 (nor_10_out, and_28_out, and_31_out);
  and and_31 (and_31_out, nor_3_out, nor_5_out);
  and and_32 (and_32_out, nand_7_out, B3);
  and and_33 (and_33_out, nor_6_out, nor_8_out, nor_12_out);
  and and_34 (and_34_out, not_7_out, nand_2_out);
  and and_35 (and_35_out, nand_7_out, not_7_out);
  not not_8 (not_8_out, A3);
  xor xor_4 (F3, nor_10_out, nor_11_out);
  nor nor_11 (nor_11_out, and_34_out, and_36_out);
  and and_36 (and_36_out, nand_7_out, B3);
  and and_37 (and_37_out, nor_3_out, nor_9_out);
  nor nor_12 (nor_12_out, not_13_out, and_40_out);
  and and_38 (and_38_out, nand_4_out, B3);
  nor nor_13 (nor_13_out, and_37_out, and_42_out);
  and and_39 (and_39_out, nor_3_out, nor_9_out);
  and and_40 (and_40_out, not_10_out, not_11_out);
  xor xor_5 (OVR, nor_10_out, and_41_out);
  and and_41 (and_41_out, nor_13_out, nand_6_out);
  and and_42 (and_42_out, nor_6_out, nor_9_out, nor_8_out);
  and and_43 (and_43_out, nor_9_out, nor_11_out);
  and and_44 (and_44_out, not_10_out, not_13_out);
  nand nand_2 (nand_2_out, not_9_out, not_12_out, not_14_out);
  nand nand_3 (nand_3_out, not_10_out, not_12_out);
  nand nand_4 (nand_4_out, not_10_out, not_11_out);
  not not_9 (not_9_out, not_10_out);
  not not_10 (not_10_out, S0);
  nand nand_5 (Cn_4_cb6af43f, nor_13_out, nand_6_out);
  nand nand_6 (nand_6_out, nor_1_out, nor_6_out);
  nor nor_14 (nor_14_out, and_44_out, and_45_out);
  and and_45 (and_45_out, not_11_out, not_13_out);
  nand nand_7 (nand_7_out, not_11_out, not_14_out);
  not not_11 (not_11_out, S1);
  not not_12 (not_12_out, not_11_out);
  not not_13 (not_13_out, not_14_out);
  not not_14 (not_14_out, S2);
endmodule

// 74385
module L_74385_4fc13ed1 (
  input  CP,
  input  A0,
  input  B0,
  input  SA0,
  input  A1,
  input  B1,
  input  SA1,
  input  A2,
  input  B2,
  input  SA2,
  input  A3,
  input  B3,
  input  SA3,
  input  CLR,
  output Q0,
  output Q1,
  output Q2,
  output Q3
);

  wire and_1_out, and_2_out, and_3_out, and_4_out, and_5_out, and_6_out, and_7_out, and_8_out, and_9_out,
       and_10_out, and_11_out, and_12_out, d_ff_2_qn, nand_1_out, nand_2_out, nor_1_out, nor_2_out,
       nor_3_out, nor_4_out, not_1_out, not_2_out, not_3_out, not_4_out, not_5_out, not_6_out, not_7_out,
       not_8_out, not_9_out, not_10_out, not_11_out, not_12_out, not_13_out, not_14_out, not_15_out,
       not_18_out, not_19_out, not_20_out, undriven, undriven_2, undriven_3, xnor_1_out, xnor_2_out,
       xnor_3_out, xnor_4_out, xnor_5_out, xnor_6_out, xnor_7_out, xnor_8_out, xnor_9_out, xnor_10_out,
       xnor_11_out, xnor_12_out;

  not not_1 (not_1_out, CP);
  not not_2 (not_2_out, A0);
  not not_3 (not_3_out, B0);
  xnor xnor_1 (xnor_1_out, not_3_out, not_4_out);
  not not_4 (not_4_out, SA0);
  not not_5 (not_5_out, A1);
  not not_6 (not_6_out, B1);
  xnor xnor_2 (xnor_2_out, not_6_out, not_7_out);
  not not_7 (not_7_out, SA1);
  not not_8 (not_8_out, A2);
  not not_9 (not_9_out, B2);
  xnor xnor_3 (xnor_3_out, not_9_out, not_10_out);
  not not_10 (not_10_out, SA2);
  not not_11 (not_11_out, A3);
  not not_12 (not_12_out, B3);
  xnor xnor_4 (xnor_4_out, not_12_out, not_13_out);
  not not_13 (not_13_out, SA3);
  not not_14 (not_14_out, CLR);
  not not_15 (not_15_out, not_14_out);
  xnor xnor_5 (xnor_5_out, not_2_out, d_ff_2_qn);
  and and_1 (and_1_out, not_2_out, xnor_1_out);
  and and_2 (and_2_out, not_2_out, d_ff_2_qn);
  and and_3 (and_3_out, xnor_1_out, d_ff_2_qn);
  xnor xnor_6 (xnor_6_out, not_5_out, undriven);
  and and_4 (and_4_out, not_5_out, xnor_2_out);
  and and_5 (and_5_out, not_5_out, undriven);
  and and_6 (and_6_out, xnor_2_out, undriven);
  xnor xnor_7 (xnor_7_out, not_8_out, undriven_2);
  and and_7 (and_7_out, not_8_out, xnor_3_out);
  and and_8 (and_8_out, not_8_out, undriven_2);
  and and_9 (and_9_out, xnor_3_out, undriven_2);
  xnor xnor_8 (xnor_8_out, not_11_out, undriven_3);
  and and_10 (and_10_out, not_11_out, xnor_4_out);
  and and_11 (and_11_out, not_11_out, undriven_3);
  and and_12 (and_12_out, xnor_4_out, undriven_3);
  nand nand_1 (nand_1_out, ~not_13_out, not_14_out);  // NAND_Gate
  xnor xnor_9 (xnor_9_out, xnor_5_out, xnor_1_out);
  nor nor_1 (nor_1_out, and_1_out, and_2_out, and_3_out);
  xnor xnor_10 (xnor_10_out, xnor_6_out, xnor_2_out);
  nor nor_2 (nor_2_out, and_4_out, and_5_out, and_6_out);
  xnor xnor_11 (xnor_11_out, xnor_7_out, xnor_3_out);
  nor nor_3 (nor_3_out, and_7_out, and_8_out, and_9_out);
  xnor xnor_12 (xnor_12_out, xnor_8_out, xnor_4_out);
  nor nor_4 (nor_4_out, and_10_out, and_11_out, and_12_out);
  nand nand_2 (nand_2_out, not_13_out, not_14_out);
  // NOT_Gate not_16 has open pins: in=not_1_out, out=open
  // NOT_Gate not_17 has open pins: in=xnor_9_out, out=open
  not not_18 (not_18_out, not_1_out);
  not not_19 (not_19_out, nand_1_out);
  not not_20 (not_20_out, nand_2_out);
  // NOT_Gate not_21 has open pins: in=not_1_out, out=open
  // NOT_Gate not_22 has open pins: in=xnor_10_out, out=open
  // NOT_Gate not_23 has open pins: in=not_1_out, out=open
  // NOT_Gate not_24 has open pins: in=nand_1_out, out=open
  // NOT_Gate not_25 has open pins: in=nand_2_out, out=open
  // NOT_Gate not_26 has open pins: in=not_1_out, out=open
  // NOT_Gate not_27 has open pins: in=xnor_11_out, out=open
  // NOT_Gate not_28 has open pins: in=not_1_out, out=open
  // NOT_Gate not_29 has open pins: in=nand_1_out, out=open
  // NOT_Gate not_30 has open pins: in=nand_2_out, out=open
  // NOT_Gate not_31 has open pins: in=not_1_out, out=open
  // NOT_Gate not_32 has open pins: in=xnor_12_out, out=open
  // NOT_Gate not_33 has open pins: in=not_1_out, out=open
  // NOT_Gate not_34 has open pins: in=nand_1_out, out=open
  // NOT_Gate not_35 has open pins: in=nand_2_out, out=open
  D_Flip_Flop d_ff_1 (.clk(not_15_out), .preset(Q0));  // open: D, Q, Qn, reset
  // NOT_Gate not_36 has open pins: in=not_15_out, out=open
  D_Flip_Flop d_ff_2 (
    .clk(not_18_out), .D(nor_1_out), .Qn(d_ff_2_qn), .preset(not_19_out), .reset(not_20_out));  // open: Q
  D_Flip_Flop d_ff_3 (.clk(not_15_out), .Q(nand_2_out), .Qn(nand_2_out), .preset(Q1));  // open: D, reset
  // NOT_Gate not_37 has open pins: in=not_15_out, out=open
  D_Flip_Flop d_ff_4 (.clk(nand_2_out), .Q(nand_1_out), .Qn(nand_1_out), .reset(undriven));  // open: D, preset
  D_Flip_Flop d_ff_5 (.clk(not_15_out), .Q(nand_2_out), .Qn(nand_2_out), .preset(Q2));  // open: D, reset
  // NOT_Gate not_38 has open pins: in=not_15_out, out=open
  D_Flip_Flop d_ff_6 (.clk(nand_2_out), .Q(nand_1_out), .Qn(nand_1_out), .reset(undriven_2));  // open: D, preset
  D_Flip_Flop d_ff_7 (.clk(not_15_out), .Q(nand_2_out), .Qn(nand_2_out), .preset(Q3));  // open: D, reset
  // NOT_Gate not_39 has open pins: in=not_15_out, out=open
  D_Flip_Flop d_ff_8 (.clk(nand_2_out), .Q(nand_1_out), .Qn(nand_1_out), .reset(undriven_3));  // open: D, preset
endmodule

// 74173
module L_74173_2efb0ee3 (
  input  D0,
  input  D1,
  input  D2,
  input  D3,
  input  iE1,
  input  iE2,
  input  CP,
  input  MR,
  input  iOE1,
  input  iOE2,
  output Q0,
  output Q1,
  output Q2,
  output Q3
);

  wire and_1_out, and_2_out, and_3_out, and_4_out, and_5_out, and_6_out, and_7_out, and_8_out, and_9_out,
       and_10_out, buffer_1_out, buffer_2_out, buffer_3_out, buffer_4_out, buffer_5_out, buffer_6_out,
       buffer_7_out, buffer_8_out, buffer_9_out, buffer_10_out, buffer_11_out, d_ff_1_q, d_ff_1_qn, d_ff_2_q,
       d_ff_2_qn, d_ff_3_q, d_ff_3_qn, d_ff_4_q, d_ff_4_qn, not_1_out, not_2_out, or_1_out, or_2_out,
       or_3_out, or_4_out;

  buf buffer_1 (buffer_1_out, iE1);
  buf buffer_2 (buffer_2_out, iE2);
  buf buffer_3 (buffer_3_out, iOE1);
  buf buffer_4 (buffer_4_out, iOE2);
  and and_1 (and_1_out, ~buffer_1_out, ~buffer_2_out);  // AND_Gate
  buf buffer_5 (buffer_5_out, CP);
  not not_1 (not_1_out, buffer_5_out);
  buf buffer_6 (buffer_6_out, MR);
  buf buffer_7 (buffer_7_out, buffer_6_out);
  and and_2 (and_2_out, ~buffer_3_out, ~buffer_4_out);  // AND_Gate
  buf buffer_8 (buffer_8_out, D0);
  not not_2 (not_2_out, and_1_out);
  and and_3 (and_3_out, and_1_out, buffer_8_out);
  or or_1 (or_1_out, and_3_out, and_4_out);
  and and_4 (and_4_out, not_2_out, d_ff_1_q);
  D_Flip_Flop #(.trigger("falling")) d_ff_1 (
    .clk(not_1_out), .D(or_1_out), .Q(d_ff_1_q), .Qn(d_ff_1_qn), .reset(buffer_7_out));  // open: preset
  assign Q0 = and_2_out ? ~d_ff_1_qn : 1'bz;  // Controlled_Inverter controlled_inverter_1
  buf buffer_9 (buffer_9_out, D1);
  and and_5 (and_5_out, and_1_out, buffer_9_out);
  and and_6 (and_6_out, not_2_out, d_ff_2_q);
  or or_2 (or_2_out, and_5_out, and_6_out);
  and and_7 (and_7_out, and_1_out, buffer_10_out);
  D_Flip_Flop #(.trigger("falling")) d_ff_2 (
    .clk(not_1_out), .D(or_2_out), .Q(d_ff_2_q), .Qn(d_ff_2_qn), .reset(buffer_7_out));  // open: preset
  assign Q1 = and_2_out ? ~d_ff_2_qn : 1'bz;  // Controlled_Inverter controlled_inverter_2
  buf buffer_10 (buffer_10_out, D2);
  and and_8 (and_8_out, not_2_out, d_ff_3_q);
  or or_3 (or_3_out, and_7_out, and_8_out);
  D_Flip_Flop #(.trigger("falling")) d_ff_3 (
    .clk(not_1_out), .D(or_3_out), .Q(d_ff_3_q), .Qn(d_ff_3_qn), .reset(buffer_7_out));  // open: preset
  assign Q2 = and_2_out ? ~d_ff_3_qn : 1'bz;  // Controlled_Inverter controlled_inverter_3
  buf buffer_11 (buffer_11_out, D3);
  and and_9 (and_9_out, and_1_out, buffer_11_out);
  or or_4 (or_4_out, and_9_out, and_10_out);
  and and_10 (and_10_out, not_2_out, d_ff_4_q);
  D_Flip_Flop #(.trigger("falling")) d_ff_4 (
    .clk(not_1_out), .D(or_4_out), .Q(d_ff_4_q), .Qn(d_ff_4_qn), .reset(buffer_7_out));  // open: preset
  assign Q3 = and_2_out ? ~d_ff_4_qn : 1'bz;  // Controlled_Inverter controlled_inverter_4
endmodule

// 74377
module L_74377_c124c74f (
  input  D0,
  input  D1,
  input  D2,
  input  D3,
  input  D4,
  input  D5,
  input  D6,
  input  D7,
  input  iEN,
  input  CP,
  output Q0,
  output Q1,
  output Q2,
  output Q3,
  output Q4,
  output Q5,
  output Q6,
  output Q7
);

  wire and_1_out, and_2_out, and_3_out, and_4_out, and_5_out, and_6_out, and_7_out, and_8_out, and_9_out,
       and_10_out, and_11_out, and_12_out, and_13_out, and_14_out, and_15_out, and_16_out, buffer_1_out,
       buffer_2_out, buffer_3_out, buffer_4_out, buffer_5_out, buffer_6_out, buffer_7_out, buffer_8_out,
       buffer_9_out, d_ff_1_q, d_ff_2_q, d_ff_3_q, d_ff_4_q, d_ff_5_q, d_ff_6_q, d_ff_7_q, d_ff_8_q,
       not_1_out, not_2_out, or_1_out, or_2_out, or_3_out, or_4_out, or_5_out, or_6_out, or_7_out, or_8_out;

  buf buffer_1 (buffer_1_out, iEN);
  not not_1 (not_1_out, buffer_1_out);
  not not_2 (not_2_out, CP);
  buf buffer_2 (buffer_2_out, D0);
  and and_1 (and_1_out, buffer_1_out, buffer_2_out);
  and and_2 (and_2_out, not_1_out, d_ff_1_q);
  or or_1 (or_1_out, and_1_out, and_2_out);
  buf buffer_3 (buffer_3_out, D1);
  and and_3 (and_3_out, buffer_1_out, buffer_3_out);
  D_Flip_Flop #(.trigger("falling")) d_ff_1 (
    .clk(not_2_out), .D(or_1_out), .Q(d_ff_1_q), .Qn(Q0));  // open: preset, reset
  and and_4 (and_4_out, not_1_out, d_ff_2_q);
  or or_2 (or_2_out, and_3_out, and_4_out);
  D_Flip_Flop #(.trigger("falling")) d_ff_2 (
    .clk(not_2_out), .D(or_2_out), .Q(d_ff_2_q), .Qn(Q1));  // open: preset, reset
  buf buffer_4 (buffer_4_out, D2);
  and and_5 (and_5_out, buffer_1_out, buffer_4_out);
  and and_6 (and_6_out, not_1_out, d_ff_3_q);
  or or_3 (or_3_out, and_5_out, and_6_out);
  D_Flip_Flop #(.trigger("falling")) d_ff_3 (
    .clk(not_2_out), .D(or_3_out), .Q(d_ff_3_q), .Qn(Q2));  // open: preset, reset
  buf buffer_5 (buffer_5_out, D3);
  and and_7 (and_7_out, buffer_1_out, buffer_5_out);
  and and_8 (and_8_out, not_1_out, d_ff_4_q);
  or or_4 (or_4_out, and_7_out, and_8_out);
  D_Flip_Flop #(.trigger("falling")) d_ff_4 (
    .clk(not_2_out), .D(or_4_out), .Q(d_ff_4_q), .Qn(Q3));  // open: preset, reset
  buf buffer_6 (buffer_6_out, D4);
  and and_9 (and_9_out, buffer_1_out, buffer_6_out);
  or or_5 (or_5_out, and_9_out, and_10_out);
  and and_10 (and_10_out, not_1_out, d_ff_5_q);
  D_Flip_Flop #(.trigger("falling")) d_ff_5 (
    .clk(not_2_out), .D(or_5_out), .Q(d_ff_5_q), .Qn(Q4));  // open: preset, reset
  buf buffer_7 (buffer_7_out, D5);
  and and_11 (and_11_out, buffer_1_out, buffer_7_out);
  and and_12 (and_12_out, not_1_out, d_ff_6_q);
  or or_6 (or_6_out, and_11_out, and_12_out);
  and and_13 (and_13_out, buffer_1_out, buffer_8_out);
  D_Flip_Flop #(.trigger("falling")) d_ff_6 (
    .clk(not_2_out), .D(or_6_out), .Q(d_ff_6_q), .Qn(Q5));  // open: preset, reset
  buf buffer_8 (buffer_8_out, D6);
  and and_14 (and_14_out, not_1_out, d_ff_7_q);
  or or_7 (or_7_out, and_13_out, and_14_out);
  D_Flip_Flop #(.trigger("falling")) d_ff_7 (
    .clk(not_2_out), .D(or_7_out), .Q(d_ff_7_q), .Qn(Q6));  // open: preset, reset
  buf buffer_9 (buffer_9_out, D7);
  and and_15 (and_15_out, buffer_1_out, buffer_9_out);
  or or_8 (or_8_out, and_15_out, and_16_out);
  and and_16 (and_16_out, not_1_out, d_ff_8_q);
  D_Flip_Flop #(.trigger("falling")) d_ff_8 (
    .clk(not_2_out), .D(or_8_out), .Q(d_ff_8_q), .Qn(Q7));  // open: preset, reset
endmodule

// 74670
module L_74670_b8d3c2a9 (
  input  Gr,
  input  Ra,
  input  Rb,
  input  D0,
  input  D1,
  input  D2,
  input  D3,
  input  Gw,
  input  Wa,
  input  Wb,
  output Q0,
  output Q1,
  output Q2,
  output Q3
);

  wire decoder_1_out0, decoder_1_out1, decoder_1_out2, decoder_1_out3, not_1_out, not_2_out;
  wire [3:0] register_1_p3, register_2_p3, register_3_p3, register_4_q;

  not not_1 (not_1_out, Gw);
  Decoder #(.enable("false"), .select(2)) decoder_1 (
    .out0(decoder_1_out0), .out1(decoder_1_out1), .out2(decoder_1_out2), .out3(decoder_1_out3), .sel({Wb, Wa}));
  // Register #(.trigger("high"), .width(4)) register_1: pin names not known; wires that end beside it: {D3, D2, D1, D0}, decoder_1_out0, register_1_p3, decoder_1_out2, {D3, D2, D1, D0}, decoder_1_out1
  // Register #(.trigger("high"), .width(4)) register_2: pin names not known; wires that end beside it: {D3, D2, D1, D0}, decoder_1_out1, register_2_p3, decoder_1_out2, {D3, D2, D1, D0}
  // Register #(.trigger("high"), .width(4)) register_3: pin names not known; wires that end beside it: {D3, D2, D1, D0}, decoder_1_out2, register_3_p3
  not not_2 (not_2_out, Gr);
  Multiplexer #(.enable("true"), .select(2), .width(4)) multiplexer_1 (
    .in0(register_1_p3), .in1(register_2_p3), .in2(register_3_p3), .in3(register_4_q),
    .out({Q3, Q2, Q1, Q0}), .sel({Rb, Ra}), .en(not_2_out));
  Register #(.trigger("high"), .width(4)) register_4 (
    .D({D3, D2, D1, D0}), .en(not_1_out), .Q(register_4_q), .clk(decoder_1_out3));  // open: clr
endmodule

// 7485
module L_7485_53ed3bf5 (
  input  A3,
  input  B3,
  input  A2,
  input  B2,
  input  A_B_1d9f32e9,
  input  A_B_66665e43,
  input  A_B_fdd740bf,
  input  A1,
  input  B1,
  input  A0,
  input  B0,
  output Qa_b_0b90d7ec,
  output Qa_b_c79307e4,
  output Qa_b_f4b7afd4
);

  wire and_1_out, and_2_out, and_3_out, and_4_out, and_5_out, and_6_out, and_7_out, and_8_out, and_9_out,
       and_10_out, and_11_out, and_12_out, and_13_out, and_14_out, and_15_out, and_16_out, and_17_out,
       and_18_out, and_19_out, and_20_out, buffer_1_out, buffer_2_out, buffer_3_out, buffer_4_out,
       buffer_5_out, buffer_6_out, buffer_7_out, buffer_8_out, buffer_9_out, buffer_10_out, buffer_11_out,
       nand_1_out, nand_2_out, nand_3_out, nand_4_out, nor_1_out, nor_2_out, nor_3_out, nor_4_out;

  buf buffer_1 (buffer_1_out, A3);
  buf buffer_2 (buffer_2_out, B3);
  buf buffer_3 (buffer_3_out, A2);
  buf buffer_4 (buffer_4_out, B2);
  buf buffer_5 (buffer_5_out, A_B_1d9f32e9);
  buf buffer_6 (buffer_6_out, A_B_66665e43);
  buf buffer_7 (buffer_7_out, A_B_fdd740bf);
  buf buffer_8 (buffer_8_out, A1);
  buf buffer_9 (buffer_9_out, B1);
  buf buffer_10 (buffer_10_out, A0);
  buf buffer_11 (buffer_11_out, B0);
  nand nand_1 (nand_1_out, buffer_1_out, buffer_2_out);
  nand nand_2 (nand_2_out, buffer_3_out, buffer_4_out);
  nand nand_3 (nand_3_out, buffer_8_out, buffer_9_out);
  nand nand_4 (nand_4_out, buffer_10_out, buffer_11_out);
  and and_1 (and_1_out, buffer_1_out, nand_1_out);
  and and_2 (and_2_out, nand_1_out, buffer_2_out);
  and and_3 (and_3_out, buffer_3_out, nand_2_out);
  and and_4 (and_4_out, nand_2_out, buffer_4_out);
  and and_5 (and_5_out, buffer_8_out, nand_3_out);
  and and_6 (and_6_out, nand_3_out, buffer_9_out);
  and and_7 (and_7_out, buffer_10_out, nand_4_out);
  and and_8 (and_8_out, nand_4_out, buffer_11_out);
  nor nor_1 (nor_1_out, and_1_out, and_2_out);
  nor nor_2 (nor_2_out, and_3_out, and_4_out);
  nor nor_3 (nor_3_out, and_5_out, and_6_out);
  nor nor_4 (nor_4_out, and_7_out, and_8_out);
  and and_9 (and_9_out, buffer_2_out, nand_1_out);
  and and_10 (and_10_out, buffer_4_out, nand_2_out, nor_1_out);
  and and_11 (and_11_out, buffer_9_out, nand_3_out, nor_1_out, nor_2_out);
  and and_12 (and_12_out, nand_4_out, nor_2_out);
  and and_13 (and_13_out, nor_2_out, nor_4_out);
  and and_14 (and_14_out, nor_2_out, nor_4_out);
  and and_15 (and_15_out, nor_4_out, nor_2_out);
  and and_16 (and_16_out, nor_4_out, nor_3_out);
  and and_17 (and_17_out, nor_2_out, nand_4_out);
  and and_18 (and_18_out, nor_2_out, nor_1_out, nand_3_out, buffer_8_out);
  and and_19 (and_19_out, nor_1_out, nand_2_out, buffer_3_out);
  and and_20 (and_20_out, nand_1_out, buffer_1_out);
  and and_21 (Qa_b_0b90d7ec, ~and_9_out, ~and_10_out, ~and_11_out, ~and_12_out, ~and_13_out, ~and_14_out);  // AND_Gate
  and and_22 (Qa_b_c79307e4, nor_2_out, nor_3_out);
  and and_23 (Qa_b_f4b7afd4, ~and_15_out, ~and_16_out, ~and_17_out, ~and_18_out, ~and_19_out, ~and_20_out);  // AND_Gate
endmodule

// 74688
module L_74688_1a05922f (
  input  P0,
  input  P1,
  input  P2,
  input  P3,
  input  P4,
  input  P5,
  input  P6,
  input  P7,
  input  Q0,
  input  Q1,
  input  Q2,
  input  Q3,
  input  Q4,
  input  Q5,
  input  Q6,
  input  Q7,
  input  iE,
  output iP_Q_90e6ba27
);

  wire not_1_out;
  wire [7:0] xnor_1_out;

  assign xnor_1_out = ~(~{P7, P6, P5, P4, P3, P2, P1, P0} ^ ~{Q7, Q6, Q5, Q4, Q3, Q2, Q1, Q0});  // XNOR_Gate xnor_1, 8 bits wide
  not not_1 (not_1_out, iE);
  nand nand_1 (iP_Q_90e6ba27, xnor_1_out[0], xnor_1_out[1], xnor_1_out[2], xnor_1_out[3], xnor_1_out[4], xnor_1_out[5], xnor_1_out[6], xnor_1_out[7], not_1_out);
endmodule

// 4511
module L_4511_238369f7 (
  input  iBL,
  input  D3,
  input  D2,
  input  D1,
  input  D0,
  input  iLT,
  input  iLE,
  output A,
  output B,
  output C,
  output D,
  output E,
  output F,
  output G
);

  wire d_ff_1_q, d_ff_1_qn, d_ff_2_q, d_ff_2_qn, d_ff_3_q, d_ff_3_qn, d_ff_4_q, nand_1_out, nand_2_out,
       nand_3_out, nand_4_out, nand_5_out, nand_6_out, nand_7_out, nand_8_out, nand_9_out, nand_10_out,
       nand_11_out, nand_12_out, nand_13_out, nand_14_out, nand_15_out, nand_16_out, nand_17_out,
       nand_18_out, not_1_out, or_1_out, undriven;

  D_Flip_Flop d_ff_1 (.clk(iLE), .D(D3), .Q(d_ff_1_q), .Qn(d_ff_1_qn));  // open: preset, reset
  D_Flip_Flop d_ff_2 (.clk(iLE), .D(D2), .Q(d_ff_2_q), .Qn(d_ff_2_qn));  // open: preset, reset
  D_Flip_Flop d_ff_3 (.clk(iLE), .D(D1), .Q(d_ff_3_q), .Qn(d_ff_3_qn));  // open: preset, reset
  D_Flip_Flop d_ff_4 (.Q(d_ff_4_q), .preset(undriven));  // open: D, clk, Qn, reset
  nand nand_1 (nand_1_out, d_ff_2_q, d_ff_3_q, d_ff_4_q);
  nand nand_2 (nand_2_out, d_ff_2_q, undriven, d_ff_3_qn);
  nand nand_3 (nand_3_out, d_ff_2_q, d_ff_3_qn, d_ff_4_q);
  nand nand_4 (nand_4_out, d_ff_2_qn, d_ff_3_q, d_ff_4_q);
  nand nand_5 (nand_5_out, undriven, d_ff_3_qn, d_ff_2_qn);
  not not_1 (not_1_out, nand_6_out);
  nand nand_6 (nand_6_out, iBL, nand_7_out);
  nand nand_7 (nand_7_out, d_ff_1_q, or_1_out);
  or or_1 (or_1_out, d_ff_3_q, d_ff_2_q);
  nand nand_8 (nand_8_out, undriven, d_ff_1_qn, d_ff_2_qn, d_ff_3_qn);
  nand nand_9 (nand_9_out, d_ff_3_q, d_ff_2_qn);
  nand nand_10 (nand_10_out, d_ff_2_q, d_ff_3_q, undriven);
  nand nand_11 (nand_11_out, d_ff_1_qn, d_ff_2_qn, d_ff_3_qn, d_ff_4_q);
  nand nand_12 (nand_12_out, nand_3_out, nand_1_out, not_1_out, nand_8_out);
  nand nand_13 (nand_13_out, nand_1_out, nand_2_out, not_1_out);
  nand nand_14 (nand_14_out, nand_4_out, not_1_out);
  nand nand_15 (nand_15_out, nand_5_out, nand_3_out, nand_10_out, not_1_out);
  nand nand_16 (nand_16_out, nand_3_out, not_1_out, d_ff_4_q);
  nand nand_17 (nand_17_out, nand_9_out, not_1_out, nand_10_out, nand_8_out);
  nand nand_18 (nand_18_out, nand_8_out, not_1_out, nand_10_out, nand_11_out);
  nand nand_19 (A, nand_12_out, iLT);
  nand nand_20 (B, nand_13_out, iLT);
  nand nand_21 (C, nand_14_out, iLT);
  nand nand_22 (D, nand_15_out, iLT);
  nand nand_23 (E, nand_16_out, iLT);
  nand nand_24 (F, nand_17_out, iLT);
  nand nand_25 (G, nand_18_out, iLT);
endmodule
